// Logisim project cpu21-riscv-CCAB2.circ as structural Verilog
module \单周期RISC_V  (
  input  IR1,
  input  IR2,
  input  IR3,
  output RegWrite,
  output MemWrite,
  output [31:0] PC,
  output [31:0] IR,
  output [31:0] RDin,
  output [31:0] MDin,
  output [31:0] LedData
);

  wire AluSrcB, and_1_out, and_2_out, and_3_out, and_4_out, and_5_out, auipc, beq, blt, bne, Choice, CLK,
       clock_1_out, comparator_1_eq, comparator_2_eq, comparator_2_lt, d_ff_1_q, ecall, equal, Go, halt,
       IR1_t, IR2_t, IR3_t, IRA, IRB, IRC, jal, jalr, Jump, less, lhu, lui, MemToReg, nand_1_out, not_1_out,
       not_2_out, not_3_out, not_4_out, not_5_out, or_1_out, or_6_out, RST, S_type, W1, W2, W3;
  wire [3:0] AluOP;
  wire [4:0] multiplexer_4_out, multiplexer_5_out;
  wire [11:0] imm12_B, multiplexer_10_out;
  wire [12:0] CNT_num;
  wire [15:0] multiplexer_12_out, \总周期数 ;
  wire [19:0] imm20_J;
  wire [31:0] adder_1_out, adder_2_out, adder_4_out, bit_extender_1_out, bit_extender_2_out,
       bit_extender_3_out, bit_extender_4_out, MDout, multiplexer_1_out, multiplexer_2_out,
       multiplexer_3_out, multiplexer_6_out, multiplexer_7_out, multiplexer_9_out, multiplexer_11_out, PC_4,
       R1, ram_1_data, Result;

  Button \u_继续运行  (.out(Go));
  Button _1 (.out(IRA));
  Button _2 (.out(IRB));
  Button _3 (.out(IRC));
  LED #(.active("true")) led_1 (.in(W1));
  LED #(.active("true")) led_2 (.in(W2));
  LED #(.active("true")) led_3 (.in(W3));
  Button Reset (.out(RST));
  Hex_Digit_Display hex_digit_display_1 (.value(LedData[31:28]));  // open: dp
  and and_1 (and_1_out, blt, less);
  and and_2 (and_2_out, beq, equal);
  not not_1 (not_1_out, equal);
  and and_3 (and_3_out, not_1_out, bne);
  Hex_Digit_Display hex_digit_display_2 (.value(LedData[27:24]));  // open: dp
  Hex_Digit_Display hex_digit_display_3 (.value(LedData[23:20]));  // open: dp
  or or_1 (or_1_out, and_1_out, and_2_out, and_3_out);
  assign bit_extender_1_out = {{12{imm20_J[19]}}, imm20_J};  // Bit_Extender bit_extender_1
  assign bit_extender_2_out = {{20{imm12_B[11]}}, imm12_B};  // Bit_Extender bit_extender_2
  Comparator #(.width(32), .mode("twosComplement")) comparator_1 (
    .a(R1), .b(32'h22), .eq(comparator_1_eq));  // open: gt, lt
  not not_2 (not_2_out, comparator_1_eq);
  Hex_Digit_Display hex_digit_display_4 (.value(LedData[15:12]));  // open: dp
  Hex_Digit_Display hex_digit_display_5 (.value(LedData[19:16]));  // open: dp
  Multiplexer #(.select(1), .width(32), .disabled("Z"), .enable("false")) multiplexer_1 (
    .in0(PC_4), .in1({Result[31:2], Choice, Result[0]}), .out(multiplexer_1_out), .sel(jalr));
  Multiplexer #(.select(1), .width(32), .disabled("Z"), .enable("false")) multiplexer_2 (
    .in0(multiplexer_1_out), .in1(adder_1_out), .out(multiplexer_2_out), .sel(jal));
  Adder #(.width(32)) adder_1 (.a(bit_extender_1_out), .b(PC), .out(adder_1_out));  // open: cin, cout
  Adder #(.width(32)) adder_2 (.a(bit_extender_2_out), .b(PC), .out(adder_2_out));  // open: cin, cout
  and and_4 (and_4_out, ecall, comparator_1_eq);
  and and_5 (and_5_out, not_2_out, ecall);
  not not_3 (not_3_out, Go);
  Hex_Digit_Display hex_digit_display_6 (.value(LedData[7:4]));  // open: dp
  Hex_Digit_Display hex_digit_display_7 (.value(LedData[11:8]));  // open: dp
  // Probe on \总周期数 
  Multiplexer #(.select(1), .width(32), .disabled("Z"), .enable("false")) multiplexer_3 (
    .in0(multiplexer_2_out), .in1(adder_2_out), .out(multiplexer_3_out), .sel(or_1_out));
  not not_4 (not_4_out, halt);
  Register #(.width(32), .trigger("rising"), .Select("low")) register_1 (
    .D(MDin), .en(and_4_out), .Q(LedData), .clk(CLK), .clr(RST));
  and and_6 (halt, and_5_out, not_3_out);
  Hex_Digit_Display hex_digit_display_8 (.value(LedData[3:0]));  // open: dp
  Register #(.width(32), .trigger("rising"), .Select("low")) u_PC (
    .D(multiplexer_3_out), .en(not_4_out), .Q(PC), .clk(CLK), .clr(RST));
  not not_5 (not_5_out, halt);
  Counter #(.width(16), .max('hffff), .ongoal("wrap"), .trigger("rising"), .behavior("new")) counter_1 (
    .count(not_5_out), .Q(\总周期数 ), .clk(CLK), .clr(RST));  // open: load, D, carry, preset, down
  or or_2 (IR1_t, IR1, IRA);
  // RiscV_Probe riscv_probe_1: pin names not known; wires that end beside it: IR
  Adder #(.width(32)) adder_3 (.a(PC), .b(32'h4), .out(PC_4));  // open: cin, cout
  or or_3 (IR2_t, IR2, IRB);
  ROM #(.addrWidth(10), .dataWidth(32), .Select("high")) rom_1 (.addr(PC[11:2]), .data(IR));
  or or_4 (Jump, jal, jalr);
  or or_5 (IR3_t, IR3, IRC);
  \单周期硬布线控制器  \u_单周期硬布线控制器_1  (
    .Funct({IR[30], IR[25], IR[14:12]}), .OP(IR[6:2]), .ALU_OP(AluOP), .MemToReg(MemToReg),
    .MemWrite(MemWrite), .ALU_SRC(AluSrcB), .RegWrite(RegWrite), .ecall(ecall), .S_type(S_type), .Jalr(jalr),
    .Beq(beq), .JAL(jal), .Bne(bne), .in_3(IR[21]), .auipc(auipc), .lui(lui), .lhu(lhu), .blt(blt));  // open: uret, CSRRCI, CSRRSI
  Multiplexer #(.select(1), .width(5), .disabled("Z"), .enable("false")) multiplexer_4 (
    .in0(IR[19:15]), .in1(5'b10001), .out(multiplexer_4_out), .sel(ecall));
  Multiplexer #(.select(1), .width(5), .disabled("Z"), .enable("false")) multiplexer_5 (
    .in0(IR[24:20]), .in1(5'b01010), .out(multiplexer_5_out), .sel(ecall));
  Multiplexer #(.select(1), .width(32), .disabled("Z"), .enable("false")) multiplexer_6 (
    .in0({Result[31:2], Choice, Result[0]}), .in1(MDout), .out(multiplexer_6_out), .sel(MemToReg));
  Shifter #(.width(12), .shift("ll")) shifter_1 (
    .in({IR[31], IR[7], IR[30:25], IR[11:8]}), .\dist (4'b0001), .out(imm12_B));
  Shifter #(.width(20), .shift("ll")) shifter_2 (
    .in({IR[31], IR[19:12], IR[20], IR[30:21]}), .\dist (5'b00001), .out(imm20_J));
  Multiplexer #(.select(1), .width(32), .disabled("Z"), .enable("false")) multiplexer_7 (
    .in0(multiplexer_6_out), .in1(PC_4), .out(multiplexer_7_out), .sel(Jump));
  Adder #(.width(32)) adder_4 (.a({IR[31:12], {12{1'b0}}}), .b(PC), .out(adder_4_out));  // open: cin, cout
  Multiplexer #(.select(1), .width(32), .disabled("Z"), .enable("false")) multiplexer_8 (
    .in0(multiplexer_7_out), .in1(multiplexer_9_out), .out(RDin), .sel(or_6_out));
  Multiplexer #(.select(1), .width(32), .disabled("Z"), .enable("false")) multiplexer_9 (
    .in0({IR[31:12], {12{1'b0}}}), .in1(adder_4_out), .out(multiplexer_9_out), .sel(auipc));
  or or_6 (or_6_out, auipc, lui);
  Regifile regifile_1 (
    .Din(RDin), .Clk(CLK), .R1(R1), .R2(MDin), .WE(RegWrite), .W_num(IR[11:7]), .R1_num(multiplexer_4_out),
    .R2_num(multiplexer_5_out));
  Multiplexer #(.select(1), .width(12), .disabled("Z"), .enable("false")) multiplexer_10 (
    .in0(IR[31:20]), .in1({IR[31:25], IR[11:7]}), .out(multiplexer_10_out), .sel(S_type));
  D_Flip_Flop #(.trigger("high"), .Pre_Clr_Positions("LEGACY"), .NegatePresetClear("false"), .enable("true"), .NewFFLayout("false")) d_ff_1 (.Q(d_ff_1_q));  // open: clk, D, Qn, preset, en, reset
  // Probe on 13'h1f9
  assign bit_extender_3_out = {{20{multiplexer_10_out[11]}}, multiplexer_10_out};  // Bit_Extender bit_extender_3
  Comparator #(.width(13), .mode("twosComplement")) comparator_2 (
    .a(CNT_num), .b(13'h1f9), .eq(comparator_2_eq), .lt(comparator_2_lt));  // open: gt
  Clock #(.highDuration(1), .lowDuration(1)) clock_1 (.out(clock_1_out));
  Multiplexer #(.select(1), .width(32), .disabled("Z"), .enable("false")) multiplexer_11 (
    .in0(MDin), .in1(bit_extender_3_out), .out(multiplexer_11_out), .sel(AluSrcB));
  Counter #(.width(13), .max('h1fff), .ongoal("stay"), .trigger("rising"), .behavior("old")) counter_2 (
    .count(comparator_2_lt), .Q(CNT_num), .clk(clock_1_out));  // open: load, D, carry, clr, preset
  ALU alu_1 (
    .X(R1), .Y(multiplexer_11_out), .AluOP(AluOP), .Equal(equal), .Result({Result[31:2], Choice, Result[0]}),
    .out_6(less));  // open: Result_2, out_4
  nand nand_1 (nand_1_out, d_ff_1_q, comparator_2_eq);
  assign CLK = nand_1_out ? clock_1_out : 1'bz;  // Controlled_Buffer controlled_buffer_1
  Pull_Resistor #(.pull(1)) pull_resistor_1 (.node(CLK));
  RAM #(.addrWidth(10), .dataWidth(32), .bus("separate"), .Select("high")) ram_1 (
    .addr(Result[11:2]), .din(MDin), .data(ram_1_data), .str(MemWrite), .clk(CLK), .ld(MemToReg), .clr(RST));  // open: sel
  Multiplexer #(.select(1), .width(16), .disabled("Z"), .enable("false")) multiplexer_12 (
    .in0(ram_1_data[15:0]), .in1(ram_1_data[31:16]), .out(multiplexer_12_out), .sel(Choice));
  Multiplexer #(.select(1), .width(32), .disabled("Z"), .enable("false")) multiplexer_13 (
    .in0(ram_1_data), .in1(bit_extender_4_out), .out(MDout), .sel(lhu));
  assign bit_extender_4_out = {{16{1'b0}}, multiplexer_12_out};  // Bit_Extender bit_extender_4

  // Other names for the same wires on the sheet: imm12_S[11:0] = {IR[31:25], IR[11:7]}; imm12_I[11:0] = IR[31:20];
  //   imm32_U[31:12] = IR[31:12]; R2[31:0] = MDin; Result[1] = Choice

  // Notes on the sheet:
  //   中断源
  //   中断等待指示
  //   数码管输出应该用寄存器锁存，否则显示数据只能一闪而过
  //   数码管输出
  //   指令存储器
  //   指令字
  //   contents of rom_1 (hex, n*v repeats v):
  //   13 430497 900533 2200893 73 430497 900533 2200893 73 430497 900533 2200893 73 430497 900533 2200893
  //   73 430497 900533 2200893 73 430497 900533 2200893 73 430497 900533 2200893 73 430497 900533 2200893
  //   73 a00893 73 800e13 fedc04b7 fff00413 1045413 84e4b3 900533 2200893 73 ba984b7 900533 73 76544b7
  //   900533 73 32104b7 900533 73 fffe0e13 fa0e1ee3 a00893 73 313 1000e13 8400493 849493 8348493 400913
  //   891913 490913 849493 8248493 849493 8148493 891913 490913 891913 490913 932023 12484b3 430313
  //   fffe0e13 fe0e18e3 2000e13 313 35483 900533 2200893 73 230313 fffe0e13 fe0e14e3 a00893 73 ff100493
  //   900533 2200893 73 148493 fe04c8e3 a00893 73
  //   rs1
  //   rs2
  //   rd
  //   Beq
  //   Bne
  //   MemToReg
  //   MemWrite
  //   AluOP
  //   AluSrcB
  //   RegWrite
  //   转换为字偏移量,所以需要逻辑左移一位
  //   为方便自动评测，需要输出PC，IR，寄存器堆写如数据RDin
  //   RAM写使能MemWrite、RAM写入数据MDin等信号
  //   控制位
  //   暂停节拍，不能为0
  //   戳工具置1进入计数暂停模式，ctrl+k时钟自动运行到对应节拍暂停
  //   ctrl+k关闭时钟连续运行，将控制位置零，进入单步调试模式调试
  //   用这个时钟源需要去掉电路中的其他时钟源
  //   可计数暂停的时钟源
  //   数据存储器
endmodule

// 单周期硬布线控制器
module \单周期硬布线控制器  (
  input  [4:0] OP,
  input  [4:0] Funct,
  input  in_3,
  output [3:0] ALU_OP,
  output uret,
  output MemToReg,
  output ecall,
  output MemWrite,
  output ALU_SRC,
  output RegWrite,
  output S_type,
  output Beq,
  output Bne,
  output Jalr,
  output JAL,
  output auipc,
  output lui,
  output lhu,
  output blt,
  output CSRRCI,
  output CSRRSI
);

  wire \控制信号自动生成_1_ecall ;

  \运算控制器自动生成  \u_运算控制器自动生成_1  (
    .OP2(OP[0]), .OP3(OP[1]), .OP4(OP[2]), .OP5(OP[3]), .OP6(OP[4]), .F12(Funct[0]), .F13(Funct[1]),
    .F14(Funct[2]), .F25(Funct[3]), .F30(Funct[4]), .S0(ALU_OP[0]), .S1(ALU_OP[1]), .S2(ALU_OP[2]),
    .S3(ALU_OP[3]));
  \控制信号自动生成  \u_控制信号自动生成_1  (
    .OP2(OP[0]), .OP3(OP[1]), .OP4(OP[2]), .OP5(OP[3]), .OP6(OP[4]), .MemToReg(MemToReg), .F12(Funct[0]),
    .F13(Funct[1]), .F14(Funct[2]), .F25(Funct[3]), .F30(Funct[4]), .MemWrite(MemWrite), .ALU_SRC(ALU_SRC),
    .RegWrite(RegWrite), .ecall(\控制信号自动生成_1_ecall ), .S_Type(S_type), .BEQ(Beq), .BNE(Bne), .JALR(Jalr),
    .JAL(JAL), .auipc(auipc), .lui(lui), .lhu(lhu), .blt(blt), .CSRRCI(CSRRCI), .CSRRSI(CSRRSI));
  and and_1 (uret, in_3, \控制信号自动生成_1_ecall );
  and and_2 (ecall, ~in_3, \控制信号自动生成_1_ecall );  // AND_Gate

  // Other names for the same wires on the sheet: IR21 = in_3; OP_CODE[4:0] = OP

  // Notes on the sheet:
  //   控制信号生成，产生数据通路需要的其他控制信号
  //   运算器控制器，根据指令生成运算器功能选择信号
endmodule

// 运算器控制器
module \运算控制器自动生成  (
  input  OP2,
  input  OP3,
  input  OP4,
  input  OP5,
  input  OP6,
  input  F12,
  input  F13,
  input  F14,
  input  F25,
  input  F30,
  output S0,
  output S1,
  output S2,
  output S3
);

  wire and_1_out, and_2_out, and_3_out, and_4_out, and_5_out, and_6_out, and_7_out, and_8_out, and_9_out,
       and_10_out, and_11_out, and_12_out, and_13_out, and_14_out, and_15_out, and_16_out, and_17_out,
       and_18_out, and_19_out, and_20_out, and_21_out, and_22_out, and_23_out, and_24_out, and_25_out,
       and_26_out, and_27_out, and_28_out, and_29_out, and_30_out, and_31_out, and_32_out, and_33_out,
       and_34_out, and_35_out, and_36_out, and_37_out, and_38_out, and_39_out, and_40_out, and_41_out,
       and_42_out, and_43_out, not_1_out, not_2_out, not_3_out, not_4_out, not_5_out, not_6_out, not_7_out,
       not_8_out, not_9_out, not_10_out, not_11_out, not_12_out, not_13_out, not_14_out, not_15_out,
       not_16_out, not_17_out, not_18_out, not_19_out, not_20_out, not_21_out, not_22_out, not_23_out,
       not_24_out, not_25_out, not_26_out, not_27_out, not_28_out, not_29_out, not_30_out, not_31_out,
       not_32_out, not_33_out, not_34_out, not_35_out, not_36_out, not_37_out, not_38_out, not_39_out,
       not_40_out, not_41_out, not_42_out, not_43_out, not_44_out, not_45_out, not_46_out, not_47_out,
       not_48_out, not_49_out, not_50_out, not_51_out, not_52_out, not_53_out, not_54_out, not_55_out,
       not_56_out, not_57_out, not_58_out, not_59_out, not_60_out, not_61_out, not_62_out, not_63_out,
       not_64_out, not_65_out, not_66_out, not_67_out, not_68_out, not_69_out, not_70_out, not_71_out,
       not_72_out, not_73_out, not_74_out, not_75_out, not_76_out, not_77_out, not_78_out, not_79_out,
       not_80_out, not_81_out, not_82_out, not_83_out, not_84_out, not_85_out, not_86_out, not_87_out,
       not_88_out, not_89_out, not_90_out, not_91_out, not_92_out, not_93_out, not_94_out, not_95_out,
       not_96_out, not_97_out, not_98_out, not_99_out, not_100_out, not_101_out, not_102_out, not_103_out,
       not_104_out, not_105_out, not_106_out, not_107_out, not_108_out, not_109_out, not_110_out,
       not_111_out, not_112_out, not_113_out, not_114_out, not_115_out, not_116_out, not_117_out,
       not_118_out, not_119_out, not_120_out, not_121_out, not_122_out, not_123_out, not_124_out,
       not_125_out, not_126_out, not_127_out, not_128_out, not_129_out, not_130_out, not_131_out,
       not_132_out, not_133_out, not_134_out, not_135_out, not_136_out, not_137_out, not_138_out,
       not_139_out, not_140_out, not_141_out, not_142_out, not_143_out, not_144_out, not_145_out,
       not_146_out, not_147_out, not_148_out, not_149_out, not_150_out, not_151_out, not_152_out,
       not_153_out, not_154_out, not_155_out, not_156_out, not_157_out, not_158_out, not_159_out,
       not_160_out, not_161_out, not_162_out, not_163_out, not_164_out, not_165_out, not_166_out,
       not_167_out, not_168_out, not_169_out, not_170_out, not_171_out, not_172_out, not_173_out,
       not_174_out, not_175_out, not_176_out, not_177_out, not_178_out, not_179_out, not_180_out,
       not_181_out, not_182_out, not_183_out, not_184_out, not_185_out, not_186_out, not_187_out,
       not_188_out, not_189_out, not_190_out, not_191_out, not_192_out, not_193_out, not_194_out,
       not_195_out, not_196_out, not_197_out, not_198_out, not_199_out, not_200_out, not_201_out,
       not_202_out, not_203_out, not_204_out, not_205_out, not_206_out, not_207_out, not_208_out,
       not_209_out, not_210_out, not_211_out, not_212_out, not_213_out, not_214_out, not_215_out,
       not_216_out, not_217_out, not_218_out, not_219_out, not_220_out, not_221_out, not_222_out,
       not_223_out, not_224_out, not_225_out, not_226_out, not_227_out, not_228_out, not_229_out,
       not_230_out, not_231_out, not_232_out, not_233_out, not_234_out, not_235_out, not_236_out,
       not_237_out, not_238_out, not_239_out, not_240_out, not_241_out, not_242_out, not_243_out,
       not_244_out, not_245_out;

  not not_1 (not_1_out, F30);
  not not_2 (not_2_out, F25);
  not not_3 (not_3_out, F14);
  not not_4 (not_4_out, F13);
  not not_5 (not_5_out, F12);
  not not_6 (not_6_out, OP6);
  not not_7 (not_7_out, OP3);
  not not_8 (not_8_out, OP2);
  not not_9 (not_9_out, F30);
  not not_10 (not_10_out, F25);
  not not_11 (not_11_out, OP6);
  not not_12 (not_12_out, OP3);
  not not_13 (not_13_out, OP2);
  not not_14 (not_14_out, F30);
  not not_15 (not_15_out, F25);
  not not_16 (not_16_out, F14);
  not not_17 (not_17_out, F12);
  not not_18 (not_18_out, OP6);
  not not_19 (not_19_out, OP3);
  not not_20 (not_20_out, OP2);
  not not_21 (not_21_out, F14);
  not not_22 (not_22_out, F13);
  not not_23 (not_23_out, F12);
  not not_24 (not_24_out, OP6);
  not not_25 (not_25_out, OP5);
  not not_26 (not_26_out, OP3);
  not not_27 (not_27_out, OP2);
  not not_28 (not_28_out, OP6);
  not not_29 (not_29_out, OP5);
  not not_30 (not_30_out, OP3);
  not not_31 (not_31_out, OP2);
  not not_32 (not_32_out, F13);
  not not_33 (not_33_out, F12);
  not not_34 (not_34_out, OP6);
  not not_35 (not_35_out, OP5);
  not not_36 (not_36_out, OP3);
  not not_37 (not_37_out, OP2);
  not not_38 (not_38_out, F14);
  not not_39 (not_39_out, F12);
  not not_40 (not_40_out, OP6);
  not not_41 (not_41_out, OP5);
  not not_42 (not_42_out, OP3);
  not not_43 (not_43_out, OP2);
  not not_44 (not_44_out, F25);
  not not_45 (not_45_out, F13);
  not not_46 (not_46_out, OP6);
  not not_47 (not_47_out, OP5);
  not not_48 (not_48_out, OP3);
  not not_49 (not_49_out, OP2);
  not not_50 (not_50_out, F14);
  not not_51 (not_51_out, F12);
  not not_52 (not_52_out, OP6);
  not not_53 (not_53_out, OP5);
  not not_54 (not_54_out, OP4);
  not not_55 (not_55_out, OP3);
  not not_56 (not_56_out, OP2);
  not not_57 (not_57_out, F14);
  not not_58 (not_58_out, F12);
  not not_59 (not_59_out, OP6);
  not not_60 (not_60_out, OP4);
  not not_61 (not_61_out, OP3);
  not not_62 (not_62_out, OP2);
  not not_63 (not_63_out, F14);
  not not_64 (not_64_out, F13);
  not not_65 (not_65_out, F12);
  not not_66 (not_66_out, OP4);
  not not_67 (not_67_out, OP3);
  not not_68 (not_68_out, OP2);
  not not_69 (not_69_out, F14);
  not not_70 (not_70_out, F13);
  not not_71 (not_71_out, OP4);
  not not_72 (not_72_out, OP3);
  not not_73 (not_73_out, OP2);
  not not_74 (not_74_out, OP4);
  not not_75 (not_75_out, F14);
  not not_76 (not_76_out, F13);
  not not_77 (not_77_out, F12);
  not not_78 (not_78_out, OP4);
  not not_79 (not_79_out, OP3);
  not not_80 (not_80_out, F13);
  not not_81 (not_81_out, OP6);
  not not_82 (not_82_out, OP5);
  not not_83 (not_83_out, OP4);
  not not_84 (not_84_out, OP3);
  not not_85 (not_85_out, OP2);
  not not_86 (not_86_out, F13);
  not not_87 (not_87_out, F12);
  not not_88 (not_88_out, OP4);
  not not_89 (not_89_out, OP3);
  not not_90 (not_90_out, OP2);
  not not_91 (not_91_out, F25);
  not not_92 (not_92_out, F14);
  not not_93 (not_93_out, F13);
  not not_94 (not_94_out, F12);
  not not_95 (not_95_out, OP6);
  not not_96 (not_96_out, OP3);
  not not_97 (not_97_out, OP2);
  not not_98 (not_98_out, F30);
  not not_99 (not_99_out, F25);
  not not_100 (not_100_out, OP6);
  not not_101 (not_101_out, OP3);
  not not_102 (not_102_out, OP2);
  not not_103 (not_103_out, F30);
  not not_104 (not_104_out, F25);
  not not_105 (not_105_out, F14);
  not not_106 (not_106_out, F12);
  not not_107 (not_107_out, OP6);
  not not_108 (not_108_out, OP3);
  not not_109 (not_109_out, OP2);
  not not_110 (not_110_out, OP6);
  not not_111 (not_111_out, OP5);
  not not_112 (not_112_out, OP3);
  not not_113 (not_113_out, OP2);
  not not_114 (not_114_out, F14);
  not not_115 (not_115_out, F12);
  not not_116 (not_116_out, OP6);
  not not_117 (not_117_out, OP5);
  not not_118 (not_118_out, OP3);
  not not_119 (not_119_out, OP2);
  not not_120 (not_120_out, F30);
  not not_121 (not_121_out, F25);
  not not_122 (not_122_out, F13);
  not not_123 (not_123_out, OP6);
  not not_124 (not_124_out, OP5);
  not not_125 (not_125_out, OP3);
  not not_126 (not_126_out, OP2);
  not not_127 (not_127_out, F13);
  not not_128 (not_128_out, F12);
  not not_129 (not_129_out, OP4);
  not not_130 (not_130_out, OP3);
  not not_131 (not_131_out, OP2);
  not not_132 (not_132_out, F30);
  not not_133 (not_133_out, F25);
  not not_134 (not_134_out, F14);
  not not_135 (not_135_out, F13);
  not not_136 (not_136_out, F12);
  not not_137 (not_137_out, OP6);
  not not_138 (not_138_out, OP3);
  not not_139 (not_139_out, OP2);
  not not_140 (not_140_out, F25);
  not not_141 (not_141_out, F14);
  not not_142 (not_142_out, F13);
  not not_143 (not_143_out, F12);
  not not_144 (not_144_out, OP6);
  not not_145 (not_145_out, OP3);
  not not_146 (not_146_out, OP2);
  not not_147 (not_147_out, F30);
  not not_148 (not_148_out, F25);
  not not_149 (not_149_out, OP6);
  not not_150 (not_150_out, OP3);
  not not_151 (not_151_out, OP2);
  not not_152 (not_152_out, F30);
  not not_153 (not_153_out, F25);
  not not_154 (not_154_out, F14);
  not not_155 (not_155_out, OP6);
  not not_156 (not_156_out, OP3);
  not not_157 (not_157_out, OP2);
  not not_158 (not_158_out, F14);
  not not_159 (not_159_out, F13);
  not not_160 (not_160_out, F12);
  not not_161 (not_161_out, OP6);
  not not_162 (not_162_out, OP5);
  not not_163 (not_163_out, OP3);
  not not_164 (not_164_out, OP2);
  not not_165 (not_165_out, OP6);
  not not_166 (not_166_out, OP5);
  not not_167 (not_167_out, OP3);
  not not_168 (not_168_out, OP2);
  not not_169 (not_169_out, F14);
  not not_170 (not_170_out, F12);
  not not_171 (not_171_out, OP6);
  not not_172 (not_172_out, OP5);
  not not_173 (not_173_out, OP4);
  not not_174 (not_174_out, OP3);
  not not_175 (not_175_out, OP2);
  not not_176 (not_176_out, F14);
  not not_177 (not_177_out, F12);
  not not_178 (not_178_out, OP6);
  not not_179 (not_179_out, OP4);
  not not_180 (not_180_out, OP3);
  not not_181 (not_181_out, OP2);
  not not_182 (not_182_out, F14);
  not not_183 (not_183_out, F13);
  not not_184 (not_184_out, F12);
  not not_185 (not_185_out, OP4);
  not not_186 (not_186_out, OP3);
  not not_187 (not_187_out, OP2);
  not not_188 (not_188_out, F14);
  not not_189 (not_189_out, F13);
  not not_190 (not_190_out, OP4);
  not not_191 (not_191_out, OP3);
  not not_192 (not_192_out, OP2);
  not not_193 (not_193_out, OP4);
  not not_194 (not_194_out, F14);
  not not_195 (not_195_out, F13);
  not not_196 (not_196_out, F12);
  not not_197 (not_197_out, OP4);
  not not_198 (not_198_out, OP3);
  not not_199 (not_199_out, F13);
  not not_200 (not_200_out, OP6);
  not not_201 (not_201_out, OP5);
  not not_202 (not_202_out, OP4);
  not not_203 (not_203_out, OP3);
  not not_204 (not_204_out, OP2);
  not not_205 (not_205_out, F30);
  not not_206 (not_206_out, F25);
  not not_207 (not_207_out, F12);
  not not_208 (not_208_out, OP6);
  not not_209 (not_209_out, OP3);
  not not_210 (not_210_out, OP2);
  not not_211 (not_211_out, F30);
  not not_212 (not_212_out, F25);
  not not_213 (not_213_out, F14);
  not not_214 (not_214_out, F12);
  not not_215 (not_215_out, OP6);
  not not_216 (not_216_out, OP3);
  not not_217 (not_217_out, OP2);
  not not_218 (not_218_out, F30);
  not not_219 (not_219_out, F25);
  not not_220 (not_220_out, F14);
  not not_221 (not_221_out, OP6);
  not not_222 (not_222_out, OP3);
  not not_223 (not_223_out, OP2);
  not not_224 (not_224_out, F12);
  not not_225 (not_225_out, OP6);
  not not_226 (not_226_out, OP5);
  not not_227 (not_227_out, OP3);
  not not_228 (not_228_out, OP2);
  not not_229 (not_229_out, F13);
  not not_230 (not_230_out, F12);
  not not_231 (not_231_out, OP6);
  not not_232 (not_232_out, OP5);
  not not_233 (not_233_out, OP3);
  not not_234 (not_234_out, OP2);
  not not_235 (not_235_out, F14);
  not not_236 (not_236_out, F12);
  not not_237 (not_237_out, OP6);
  not not_238 (not_238_out, OP5);
  not not_239 (not_239_out, OP3);
  not not_240 (not_240_out, OP2);
  not not_241 (not_241_out, F13);
  not not_242 (not_242_out, F12);
  not not_243 (not_243_out, OP4);
  not not_244 (not_244_out, OP3);
  not not_245 (not_245_out, OP2);
  and and_1 (and_1_out, not_1_out, not_2_out, not_3_out, not_4_out, not_5_out, not_6_out, OP5, OP4, not_7_out, not_8_out);
  and and_2 (and_2_out, not_9_out, not_10_out, F14, F13, F12, not_11_out, OP5, OP4, not_12_out, not_13_out);
  and and_3 (and_3_out, not_14_out, not_15_out, not_16_out, F13, not_17_out, not_18_out, OP5, OP4, not_19_out, not_20_out);
  and and_4 (and_4_out, not_21_out, not_22_out, not_23_out, not_24_out, not_25_out, OP4, not_26_out, not_27_out);
  and and_5 (and_5_out, F14, F13, F12, not_28_out, not_29_out, OP4, not_30_out, not_31_out);
  and and_6 (and_6_out, F14, not_32_out, not_33_out, not_34_out, not_35_out, OP4, not_36_out, not_37_out);
  and and_7 (and_7_out, not_38_out, F13, not_39_out, not_40_out, not_41_out, OP4, not_42_out, not_43_out);
  and and_8 (and_8_out, F30, not_44_out, F14, not_45_out, F12, not_46_out, not_47_out, OP4, not_48_out, not_49_out);
  and and_9 (and_9_out, not_50_out, F13, not_51_out, not_52_out, not_53_out, not_54_out, not_55_out, not_56_out);
  and and_10 (and_10_out, not_57_out, F13, not_58_out, not_59_out, OP5, not_60_out, not_61_out, not_62_out);
  and and_11 (and_11_out, not_63_out, not_64_out, not_65_out, OP6, OP5, not_66_out, not_67_out, not_68_out);
  and and_12 (and_12_out, not_69_out, not_70_out, F12, OP6, OP5, not_71_out, not_72_out, not_73_out);
  and and_13 (and_13_out, OP6, OP5, not_74_out, OP3, OP2);
  and and_14 (and_14_out, not_75_out, not_76_out, not_77_out, OP6, OP5, not_78_out, not_79_out, OP2);
  and and_15 (and_15_out, F14, not_80_out, F12, not_81_out, not_82_out, not_83_out, not_84_out, not_85_out);
  and and_16 (and_16_out, F14, not_86_out, not_87_out, OP6, OP5, not_88_out, not_89_out, not_90_out);
  and and_17 (and_17_out, F30, not_91_out, not_92_out, not_93_out, not_94_out, not_95_out, OP5, OP4, not_96_out, not_97_out);
  and and_18 (and_18_out, not_98_out, not_99_out, F14, F13, F12, not_100_out, OP5, OP4, not_101_out, not_102_out);
  and and_19 (and_19_out, not_103_out, not_104_out, not_105_out, F13, not_106_out, not_107_out, OP5, OP4, not_108_out, not_109_out);
  and and_20 (and_20_out, F14, F13, F12, not_110_out, not_111_out, OP4, not_112_out, not_113_out);
  and and_21 (and_21_out, not_114_out, F13, not_115_out, not_116_out, not_117_out, OP4, not_118_out, not_119_out);
  and and_22 (and_22_out, not_120_out, not_121_out, F14, not_122_out, F12, not_123_out, not_124_out, OP4, not_125_out, not_126_out);
  and and_23 (and_23_out, F14, not_127_out, not_128_out, OP6, OP5, not_129_out, not_130_out, not_131_out);
  and and_24 (and_24_out, not_132_out, not_133_out, not_134_out, not_135_out, not_136_out, not_137_out, OP5, OP4, not_138_out, not_139_out);
  and and_25 (and_25_out, F30, not_140_out, not_141_out, not_142_out, not_143_out, not_144_out, OP5, OP4, not_145_out, not_146_out);
  and and_26 (and_26_out, not_147_out, not_148_out, F14, F13, F12, not_149_out, OP5, OP4, not_150_out, not_151_out);
  and and_27 (and_27_out, not_152_out, not_153_out, not_154_out, F13, F12, not_155_out, OP5, OP4, not_156_out, not_157_out);
  and and_28 (and_28_out, not_158_out, not_159_out, not_160_out, not_161_out, not_162_out, OP4, not_163_out, not_164_out);
  and and_29 (and_29_out, F14, F13, F12, not_165_out, not_166_out, OP4, not_167_out, not_168_out);
  and and_30 (and_30_out, not_169_out, F13, not_170_out, not_171_out, not_172_out, not_173_out, not_174_out, not_175_out);
  and and_31 (and_31_out, not_176_out, F13, not_177_out, not_178_out, OP5, not_179_out, not_180_out, not_181_out);
  and and_32 (and_32_out, not_182_out, not_183_out, not_184_out, OP6, OP5, not_185_out, not_186_out, not_187_out);
  and and_33 (and_33_out, not_188_out, not_189_out, F12, OP6, OP5, not_190_out, not_191_out, not_192_out);
  and and_34 (and_34_out, OP6, OP5, not_193_out, OP3, OP2);
  and and_35 (and_35_out, not_194_out, not_195_out, not_196_out, OP6, OP5, not_197_out, not_198_out, OP2);
  and and_36 (and_36_out, F14, not_199_out, F12, not_200_out, not_201_out, not_202_out, not_203_out, not_204_out);
  and and_37 (and_37_out, not_205_out, not_206_out, F14, F13, not_207_out, not_208_out, OP5, OP4, not_209_out, not_210_out);
  and and_38 (and_38_out, not_211_out, not_212_out, not_213_out, F13, not_214_out, not_215_out, OP5, OP4, not_216_out, not_217_out);
  and and_39 (and_39_out, not_218_out, not_219_out, not_220_out, F13, F12, not_221_out, OP5, OP4, not_222_out, not_223_out);
  and and_40 (and_40_out, F14, F13, not_224_out, not_225_out, not_226_out, OP4, not_227_out, not_228_out);
  and and_41 (and_41_out, F14, not_229_out, not_230_out, not_231_out, not_232_out, OP4, not_233_out, not_234_out);
  and and_42 (and_42_out, not_235_out, F13, not_236_out, not_237_out, not_238_out, OP4, not_239_out, not_240_out);
  and and_43 (and_43_out, F14, not_241_out, not_242_out, OP6, OP5, not_243_out, not_244_out, not_245_out);
  or or_1 (S0, and_1_out, and_2_out, and_3_out, and_4_out, and_5_out, and_6_out, and_7_out, and_8_out, and_9_out, and_10_out, and_11_out, and_12_out, and_13_out, and_14_out, and_15_out, and_16_out);
  or or_2 (S1, and_17_out, and_18_out, and_19_out, and_20_out, and_21_out, and_22_out, and_23_out);
  or or_3 (S2, and_24_out, and_25_out, and_26_out, and_27_out, and_28_out, and_29_out, and_30_out, and_31_out, and_32_out, and_33_out, and_34_out, and_35_out, and_36_out);
  or or_4 (S3, and_37_out, and_38_out, and_39_out, and_40_out, and_41_out, and_42_out, and_43_out);
endmodule

// 控制信号生成
module \控制信号自动生成  (
  input  OP2,
  input  OP3,
  input  OP4,
  input  OP5,
  input  OP6,
  input  F12,
  input  F13,
  input  F14,
  input  F25,
  input  F30,
  output MemToReg,
  output MemWrite,
  output ALU_SRC,
  output RegWrite,
  output ecall,
  output S_Type,
  output BEQ,
  output BNE,
  output JALR,
  output JAL,
  output auipc,
  output lui,
  output lhu,
  output blt,
  output CSRRCI,
  output CSRRSI
);

  wire and_1_out, and_2_out, and_4_out, and_5_out, and_6_out, and_7_out, and_8_out, and_9_out, and_10_out,
       and_11_out, and_12_out, and_13_out, and_14_out, and_15_out, and_16_out, and_17_out, and_18_out,
       and_19_out, and_20_out, and_21_out, and_22_out, and_23_out, and_24_out, and_25_out, and_26_out,
       and_27_out, and_28_out, and_29_out, and_30_out, not_1_out, not_2_out, not_3_out, not_4_out, not_5_out,
       not_6_out, not_7_out, not_8_out, not_9_out, not_10_out, not_11_out, not_12_out, not_13_out,
       not_14_out, not_15_out, not_16_out, not_17_out, not_18_out, not_19_out, not_20_out, not_21_out,
       not_22_out, not_23_out, not_24_out, not_25_out, not_26_out, not_27_out, not_28_out, not_29_out,
       not_30_out, not_31_out, not_32_out, not_33_out, not_34_out, not_35_out, not_36_out, not_37_out,
       not_38_out, not_39_out, not_40_out, not_41_out, not_42_out, not_43_out, not_44_out, not_45_out,
       not_46_out, not_47_out, not_48_out, not_49_out, not_50_out, not_51_out, not_52_out, not_53_out,
       not_54_out, not_55_out, not_56_out, not_57_out, not_58_out, not_59_out, not_60_out, not_61_out,
       not_62_out, not_63_out, not_64_out, not_65_out, not_66_out, not_67_out, not_68_out, not_69_out,
       not_70_out, not_71_out, not_72_out, not_73_out, not_74_out, not_75_out, not_76_out, not_77_out,
       not_78_out, not_79_out, not_80_out, not_81_out, not_82_out, not_83_out, not_84_out, not_85_out,
       not_86_out, not_87_out, not_88_out, not_89_out, not_90_out, not_91_out, not_92_out, not_93_out,
       not_94_out, not_95_out, not_96_out, not_97_out, not_98_out, not_99_out, not_100_out, not_101_out,
       not_102_out, not_103_out, not_104_out, not_105_out, not_106_out, not_107_out, not_108_out,
       not_109_out, not_110_out, not_111_out, not_112_out, not_113_out, not_114_out, not_115_out,
       not_116_out, not_117_out, not_118_out, not_119_out, not_120_out, not_121_out, not_122_out,
       not_123_out, not_124_out, not_125_out, not_126_out, not_127_out, not_128_out, not_129_out,
       not_130_out, not_131_out, not_132_out, not_133_out, not_134_out, not_135_out, not_136_out,
       not_137_out, not_138_out, not_139_out, not_140_out, not_141_out, not_142_out, not_143_out,
       not_144_out, not_145_out, not_146_out, not_147_out, not_148_out, not_149_out, not_150_out,
       not_151_out, not_152_out, not_153_out, not_154_out, not_155_out, not_156_out, not_157_out,
       not_158_out, not_159_out, not_160_out, not_161_out, not_162_out, not_163_out, not_164_out,
       not_165_out, not_166_out, not_167_out, not_168_out, not_169_out, not_170_out, not_171_out,
       not_172_out, not_173_out, not_174_out, not_175_out, not_176_out, not_177_out, not_178_out,
       not_179_out, not_180_out, not_181_out, not_182_out, not_183_out, not_184_out, not_185_out,
       not_186_out, not_187_out, not_188_out, not_189_out, not_190_out, not_191_out, not_192_out,
       not_193_out, not_194_out, not_195_out, not_196_out, not_197_out, not_198_out, not_199_out,
       not_200_out, not_201_out, not_202_out, not_203_out, not_204_out, not_205_out, not_206_out,
       not_207_out, not_208_out, not_209_out, not_210_out, not_211_out, not_212_out, not_213_out,
       not_214_out, not_215_out, not_216_out, not_217_out, not_218_out, not_219_out, not_220_out;

  not not_1 (not_1_out, OP2);
  not not_2 (not_2_out, OP3);
  not not_3 (not_3_out, OP4);
  not not_4 (not_4_out, OP5);
  not not_5 (not_5_out, OP6);
  not not_6 (not_6_out, F12);
  not not_7 (not_7_out, F14);
  not not_8 (not_8_out, OP2);
  not not_9 (not_9_out, OP3);
  not not_10 (not_10_out, OP4);
  not not_11 (not_11_out, OP5);
  not not_12 (not_12_out, OP6);
  not not_13 (not_13_out, F13);
  not not_14 (not_14_out, OP2);
  not not_15 (not_15_out, OP3);
  not not_16 (not_16_out, OP4);
  not not_17 (not_17_out, OP6);
  not not_18 (not_18_out, F12);
  not not_19 (not_19_out, F14);
  not not_20 (not_20_out, OP2);
  not not_21 (not_21_out, OP3);
  not not_22 (not_22_out, OP4);
  not not_23 (not_23_out, OP6);
  not not_24 (not_24_out, F12);
  not not_25 (not_25_out, F14);
  not not_26 (not_26_out, OP2);
  not not_27 (not_27_out, OP3);
  not not_28 (not_28_out, OP4);
  not not_29 (not_29_out, OP5);
  not not_30 (not_30_out, OP6);
  not not_31 (not_31_out, F13);
  not not_32 (not_32_out, OP2);
  not not_33 (not_33_out, OP3);
  not not_34 (not_34_out, OP5);
  not not_35 (not_35_out, OP6);
  not not_36 (not_36_out, F12);
  not not_37 (not_37_out, OP2);
  not not_38 (not_38_out, OP3);
  not not_39 (not_39_out, OP5);
  not not_40 (not_40_out, OP6);
  not not_41 (not_41_out, F13);
  not not_42 (not_42_out, F25);
  not not_43 (not_43_out, F30);
  not not_44 (not_44_out, OP2);
  not not_45 (not_45_out, OP3);
  not not_46 (not_46_out, OP5);
  not not_47 (not_47_out, OP6);
  not not_48 (not_48_out, F25);
  not not_49 (not_49_out, OP2);
  not not_50 (not_50_out, OP3);
  not not_51 (not_51_out, OP5);
  not not_52 (not_52_out, OP6);
  not not_53 (not_53_out, OP3);
  not not_54 (not_54_out, OP4);
  not not_55 (not_55_out, F12);
  not not_56 (not_56_out, F13);
  not not_57 (not_57_out, F14);
  not not_58 (not_58_out, F30);
  not not_59 (not_59_out, F25);
  not not_60 (not_60_out, F14);
  not not_61 (not_61_out, F13);
  not not_62 (not_62_out, F12);
  not not_63 (not_63_out, OP6);
  not not_64 (not_64_out, OP3);
  not not_65 (not_65_out, OP2);
  not not_66 (not_66_out, F25);
  not not_67 (not_67_out, F14);
  not not_68 (not_68_out, F13);
  not not_69 (not_69_out, F12);
  not not_70 (not_70_out, OP6);
  not not_71 (not_71_out, OP3);
  not not_72 (not_72_out, OP2);
  not not_73 (not_73_out, F30);
  not not_74 (not_74_out, F25);
  not not_75 (not_75_out, OP6);
  not not_76 (not_76_out, OP3);
  not not_77 (not_77_out, OP2);
  not not_78 (not_78_out, F30);
  not not_79 (not_79_out, F25);
  not not_80 (not_80_out, F12);
  not not_81 (not_81_out, OP6);
  not not_82 (not_82_out, OP3);
  not not_83 (not_83_out, OP2);
  not not_84 (not_84_out, F30);
  not not_85 (not_85_out, F25);
  not not_86 (not_86_out, F14);
  not not_87 (not_87_out, F12);
  not not_88 (not_88_out, OP6);
  not not_89 (not_89_out, OP3);
  not not_90 (not_90_out, OP2);
  not not_91 (not_91_out, F30);
  not not_92 (not_92_out, F25);
  not not_93 (not_93_out, F14);
  not not_94 (not_94_out, OP6);
  not not_95 (not_95_out, OP3);
  not not_96 (not_96_out, OP2);
  not not_97 (not_97_out, F14);
  not not_98 (not_98_out, F13);
  not not_99 (not_99_out, F12);
  not not_100 (not_100_out, OP6);
  not not_101 (not_101_out, OP5);
  not not_102 (not_102_out, OP3);
  not not_103 (not_103_out, OP2);
  not not_104 (not_104_out, OP6);
  not not_105 (not_105_out, OP5);
  not not_106 (not_106_out, OP3);
  not not_107 (not_107_out, OP2);
  not not_108 (not_108_out, F12);
  not not_109 (not_109_out, OP6);
  not not_110 (not_110_out, OP5);
  not not_111 (not_111_out, OP3);
  not not_112 (not_112_out, OP2);
  not not_113 (not_113_out, F13);
  not not_114 (not_114_out, F12);
  not not_115 (not_115_out, OP6);
  not not_116 (not_116_out, OP5);
  not not_117 (not_117_out, OP3);
  not not_118 (not_118_out, OP2);
  not not_119 (not_119_out, F14);
  not not_120 (not_120_out, F12);
  not not_121 (not_121_out, OP6);
  not not_122 (not_122_out, OP5);
  not not_123 (not_123_out, OP3);
  not not_124 (not_124_out, OP2);
  not not_125 (not_125_out, F30);
  not not_126 (not_126_out, F25);
  not not_127 (not_127_out, F14);
  not not_128 (not_128_out, F13);
  not not_129 (not_129_out, OP6);
  not not_130 (not_130_out, OP5);
  not not_131 (not_131_out, OP3);
  not not_132 (not_132_out, OP2);
  not not_133 (not_133_out, F30);
  not not_134 (not_134_out, F25);
  not not_135 (not_135_out, F13);
  not not_136 (not_136_out, OP6);
  not not_137 (not_137_out, OP5);
  not not_138 (not_138_out, OP3);
  not not_139 (not_139_out, OP2);
  not not_140 (not_140_out, F25);
  not not_141 (not_141_out, F13);
  not not_142 (not_142_out, OP6);
  not not_143 (not_143_out, OP5);
  not not_144 (not_144_out, OP3);
  not not_145 (not_145_out, OP2);
  not not_146 (not_146_out, F14);
  not not_147 (not_147_out, F12);
  not not_148 (not_148_out, OP6);
  not not_149 (not_149_out, OP5);
  not not_150 (not_150_out, OP4);
  not not_151 (not_151_out, OP3);
  not not_152 (not_152_out, OP2);
  not not_153 (not_153_out, OP4);
  not not_154 (not_154_out, F14);
  not not_155 (not_155_out, F13);
  not not_156 (not_156_out, F12);
  not not_157 (not_157_out, OP4);
  not not_158 (not_158_out, OP3);
  not not_159 (not_159_out, OP6);
  not not_160 (not_160_out, OP5);
  not not_161 (not_161_out, OP3);
  not not_162 (not_162_out, OP6);
  not not_163 (not_163_out, OP3);
  not not_164 (not_164_out, F13);
  not not_165 (not_165_out, OP6);
  not not_166 (not_166_out, OP5);
  not not_167 (not_167_out, OP4);
  not not_168 (not_168_out, OP3);
  not not_169 (not_169_out, OP2);
  not not_170 (not_170_out, OP2);
  not not_171 (not_171_out, OP3);
  not not_172 (not_172_out, F12);
  not not_173 (not_173_out, F13);
  not not_174 (not_174_out, F14);
  not not_175 (not_175_out, F25);
  not not_176 (not_176_out, F30);
  not not_177 (not_177_out, OP2);
  not not_178 (not_178_out, OP3);
  not not_179 (not_179_out, OP4);
  not not_180 (not_180_out, OP6);
  not not_181 (not_181_out, F12);
  not not_182 (not_182_out, F14);
  not not_183 (not_183_out, OP2);
  not not_184 (not_184_out, OP3);
  not not_185 (not_185_out, OP4);
  not not_186 (not_186_out, F12);
  not not_187 (not_187_out, F13);
  not not_188 (not_188_out, F14);
  not not_189 (not_189_out, OP2);
  not not_190 (not_190_out, OP3);
  not not_191 (not_191_out, OP4);
  not not_192 (not_192_out, F13);
  not not_193 (not_193_out, F14);
  not not_194 (not_194_out, OP3);
  not not_195 (not_195_out, OP4);
  not not_196 (not_196_out, F12);
  not not_197 (not_197_out, F13);
  not not_198 (not_198_out, F14);
  not not_199 (not_199_out, OP4);
  not not_200 (not_200_out, OP3);
  not not_201 (not_201_out, OP5);
  not not_202 (not_202_out, OP6);
  not not_203 (not_203_out, OP3);
  not not_204 (not_204_out, OP6);
  not not_205 (not_205_out, OP2);
  not not_206 (not_206_out, OP3);
  not not_207 (not_207_out, OP4);
  not not_208 (not_208_out, OP5);
  not not_209 (not_209_out, OP6);
  not not_210 (not_210_out, F13);
  not not_211 (not_211_out, OP2);
  not not_212 (not_212_out, OP3);
  not not_213 (not_213_out, OP4);
  not not_214 (not_214_out, F12);
  not not_215 (not_215_out, F13);
  not not_216 (not_216_out, OP2);
  not not_217 (not_217_out, OP3);
  not not_218 (not_218_out, OP2);
  not not_219 (not_219_out, OP3);
  not not_220 (not_220_out, F12);
  and and_1 (and_1_out, not_1_out, not_2_out, not_3_out, not_4_out, not_5_out, not_6_out, F13, not_7_out);
  and and_2 (and_2_out, not_8_out, not_9_out, not_10_out, not_11_out, not_12_out, F12, not_13_out, F14);
  and and_3 (MemWrite, not_14_out, not_15_out, not_16_out, OP5, not_17_out, not_18_out, F13, not_19_out);
  and and_4 (and_4_out, not_20_out, not_21_out, not_22_out, not_23_out, not_24_out, F13, not_25_out);
  and and_5 (and_5_out, not_26_out, not_27_out, not_28_out, not_29_out, not_30_out, F12, not_31_out, F14);
  and and_6 (and_6_out, not_32_out, not_33_out, OP4, not_34_out, not_35_out, not_36_out);
  and and_7 (and_7_out, not_37_out, not_38_out, OP4, not_39_out, not_40_out, not_41_out, not_42_out, not_43_out);
  and and_8 (and_8_out, not_44_out, not_45_out, OP4, not_46_out, not_47_out, F14, not_48_out);
  and and_9 (and_9_out, not_49_out, not_50_out, OP4, not_51_out, not_52_out, F13, F14);
  and and_10 (and_10_out, OP2, not_53_out, not_54_out, OP5, OP6, not_55_out, not_56_out, not_57_out);
  and and_11 (and_11_out, not_58_out, not_59_out, not_60_out, not_61_out, not_62_out, not_63_out, OP5, OP4, not_64_out, not_65_out);
  and and_12 (and_12_out, F30, not_66_out, not_67_out, not_68_out, not_69_out, not_70_out, OP5, OP4, not_71_out, not_72_out);
  and and_13 (and_13_out, not_73_out, not_74_out, F14, F13, F12, not_75_out, OP5, OP4, not_76_out, not_77_out);
  and and_14 (and_14_out, not_78_out, not_79_out, F14, F13, not_80_out, not_81_out, OP5, OP4, not_82_out, not_83_out);
  and and_15 (and_15_out, not_84_out, not_85_out, not_86_out, F13, not_87_out, not_88_out, OP5, OP4, not_89_out, not_90_out);
  and and_16 (and_16_out, not_91_out, not_92_out, not_93_out, F13, F12, not_94_out, OP5, OP4, not_95_out, not_96_out);
  and and_17 (and_17_out, not_97_out, not_98_out, not_99_out, not_100_out, not_101_out, OP4, not_102_out, not_103_out);
  and and_18 (and_18_out, F14, F13, F12, not_104_out, not_105_out, OP4, not_106_out, not_107_out);
  and and_19 (and_19_out, F14, F13, not_108_out, not_109_out, not_110_out, OP4, not_111_out, not_112_out);
  and and_20 (and_20_out, F14, not_113_out, not_114_out, not_115_out, not_116_out, OP4, not_117_out, not_118_out);
  and and_21 (and_21_out, not_119_out, F13, not_120_out, not_121_out, not_122_out, OP4, not_123_out, not_124_out);
  and and_22 (and_22_out, not_125_out, not_126_out, not_127_out, not_128_out, F12, not_129_out, not_130_out, OP4, not_131_out, not_132_out);
  and and_23 (and_23_out, not_133_out, not_134_out, F14, not_135_out, F12, not_136_out, not_137_out, OP4, not_138_out, not_139_out);
  and and_24 (and_24_out, F30, not_140_out, F14, not_141_out, F12, not_142_out, not_143_out, OP4, not_144_out, not_145_out);
  and and_25 (and_25_out, not_146_out, F13, not_147_out, not_148_out, not_149_out, not_150_out, not_151_out, not_152_out);
  and and_26 (and_26_out, OP6, OP5, not_153_out, OP3, OP2);
  and and_27 (and_27_out, not_154_out, not_155_out, not_156_out, OP6, OP5, not_157_out, not_158_out, OP2);
  and and_28 (and_28_out, not_159_out, not_160_out, OP4, not_161_out, OP2);
  and and_29 (and_29_out, not_162_out, OP5, OP4, not_163_out, OP2);
  and and_30 (and_30_out, F14, not_164_out, F12, not_165_out, not_166_out, not_167_out, not_168_out, not_169_out);
  and and_31 (ecall, not_170_out, not_171_out, OP4, OP5, OP6, not_172_out, not_173_out, not_174_out, not_175_out, not_176_out);
  and and_32 (S_Type, not_177_out, not_178_out, not_179_out, OP5, not_180_out, not_181_out, F13, not_182_out);
  and and_33 (BEQ, not_183_out, not_184_out, not_185_out, OP5, OP6, not_186_out, not_187_out, not_188_out);
  and and_34 (BNE, not_189_out, not_190_out, not_191_out, OP5, OP6, F12, not_192_out, not_193_out);
  and and_35 (JALR, OP2, not_194_out, not_195_out, OP5, OP6, not_196_out, not_197_out, not_198_out);
  and and_36 (JAL, OP2, OP3, not_199_out, OP5, OP6);
  and and_37 (auipc, OP2, not_200_out, OP4, not_201_out, not_202_out);
  and and_38 (lui, OP2, not_203_out, OP4, OP5, not_204_out);
  and and_39 (lhu, not_205_out, not_206_out, not_207_out, not_208_out, not_209_out, F12, not_210_out, F14);
  and and_40 (blt, not_211_out, not_212_out, not_213_out, OP5, OP6, not_214_out, not_215_out, F14);
  and and_41 (CSRRCI, not_216_out, not_217_out, OP4, OP5, OP6, F12, F13, F14);
  and and_42 (CSRRSI, not_218_out, not_219_out, OP4, OP5, OP6, not_220_out, F13, F14);
  or or_1 (MemToReg, and_1_out, and_2_out);
  or or_2 (ALU_SRC, and_4_out, and_5_out, and_6_out, and_7_out, and_8_out, and_9_out, and_10_out);
  or or_3 (RegWrite, and_11_out, and_12_out, and_13_out, and_14_out, and_15_out, and_16_out, and_17_out, and_18_out, and_19_out, and_20_out, and_21_out, and_22_out, and_23_out, and_24_out, and_25_out, and_26_out, and_27_out, and_28_out, and_29_out, and_30_out);
endmodule

// ALU
module ALU (
  input  [31:0] X,
  input  [31:0] Y,
  input  [3:0] AluOP,
  output out_4,
  output Equal,
  output out_6,
  output [31:0] Result,
  output [31:0] Result_2
);

  wire [0:0] comparator_1_lt, comparator_2_lt;
  wire [31:0] adder_1_out, AND_out, divider_1_out, divider_1_rem, multiplier_1_cout, multiplier_1_out,
       NOR_out, OR_out, shifter_1_out, shifter_2_out, shifter_3_out, subtractor_1_out, XOR_out;

  assign AND_out = X & Y;  // AND_Gate AND, 32 bits wide
  assign OR_out = X | Y;  // OR_Gate OR, 32 bits wide
  Shifter #(.width(32), .shift("ll")) shifter_1 (.in(X), .\dist (Y[4:0]), .out(shifter_1_out));
  Shifter #(.width(32), .shift("ar")) shifter_2 (.in(X), .\dist (Y[4:0]), .out(shifter_2_out));
  Shifter #(.width(32), .shift("lr")) shifter_3 (.in(X), .\dist (Y[4:0]), .out(shifter_3_out));
  Multiplier #(.width(32)) multiplier_1 (.a(X), .b(Y), .out(multiplier_1_out), .cout(multiplier_1_cout));  // open: cin
  Divider #(.width(32)) divider_1 (.a(X), .b(Y), .out(divider_1_out), .rem(divider_1_rem));  // open: upper
  Adder #(.width(32)) adder_1 (.a(X), .b(Y), .out(adder_1_out));  // open: cin, cout
  Subtractor #(.width(32)) subtractor_1 (.a(X), .b(Y), .out(subtractor_1_out));  // open: bin, bout
  assign XOR_out = X ^ Y;  // XOR_Gate XOR, 32 bits wide
  assign NOR_out = ~(X | Y);  // NOR_Gate NOR, 32 bits wide
  Comparator #(.width(32), .mode("twosComplement")) comparator_1 (
    .a(X), .b(Y), .eq(Equal), .lt(comparator_1_lt[0]));  // open: gt
  Comparator #(.width(32), .mode("unsigned")) comparator_2 (.a(X), .b(Y), .lt(comparator_2_lt[0]));  // open: gt, eq
  Multiplexer #(.select(4), .width(32), .disabled("Z"), .enable("false")) multiplexer_1 (
    .in0(shifter_1_out), .in1(shifter_2_out), .in2(shifter_3_out), .in3(multiplier_1_out),
    .in4(divider_1_out), .in5(adder_1_out), .in6(subtractor_1_out), .in7(AND_out), .in8(OR_out),
    .in9(XOR_out), .in10(NOR_out), .in11({{31{1'b0}}, comparator_1_lt[0]}),
    .in12({{31{1'b0}}, comparator_2_lt[0]}), .in13({32{1'b0}}), .in14({32{1'b0}}), .in15({32{1'b0}}),
    .out(Result), .sel(AluOP));
  Multiplexer #(.select(4), .width(32), .disabled("Z"), .enable("false")) multiplexer_2 (
    .in0({32{1'b0}}), .in1({32{1'b0}}), .in2({32{1'b0}}), .in3(multiplier_1_cout), .in4(divider_1_rem),
    .in5({32{1'b0}}), .in6({32{1'b0}}), .in7({32{1'b0}}), .in8({32{1'b0}}), .in9({32{1'b0}}),
    .in10({32{1'b0}}), .in11({32{1'b0}}), .in12({32{1'b0}}), .in13({32{1'b0}}), .in14({32{1'b0}}),
    .in15({32{1'b0}}), .out(Result_2), .sel(AluOP));
  Multiplexer #(.select(4), .width(1), .disabled("Z"), .enable("false")) multiplexer_3 (
    .in0(1'b0), .in1(1'b0), .in2(1'b0), .in3(1'b0), .in4(1'b0), .in5(1'b0), .in6(1'b0), .in7(1'b0),
    .in8(1'b0), .in9(1'b0), .in10(1'b0), .in11(comparator_1_lt[0]), .in12(comparator_2_lt[0]), .in13(1'b0),
    .in14(1'b0), .in15(1'b0), .out(out_6), .sel(AluOP));
  not not_1 (out_4, out_6);

  // Other names for the same wires on the sheet: Result2[31:0] = Result_2; S[3:0] = AluOP; tunnel = out_6;
  //   tunnel_t = out_4

  // Notes on the sheet:
  //   不要改变此引脚区域内容，也不要改变ALU封装形式
  //   输入引脚
  //   输出引脚
endmodule

module Regifile (
  input  [31:0] Din,
  input  Clk,
  input  WE,
  input  [4:0] R1_num,
  input  [4:0] W_num,
  input  [4:0] R2_num,
  output [31:0] R1,
  output [31:0] R2
);

  // RegisterFile registerfile_1: pin names not known; wires that end beside it: Din, Clk, WE, W_num, R1_num, R2_num, R1, R2
endmodule

module \理想流水线  (
  output RegWrite,
  output MemWrite,
  output [31:0] IF_PC,
  output [31:0] ID_PC,
  output [31:0] EX_PC,
  output [31:0] M_PC,
  output [31:0] WB_PC,
  output [31:0] RDin,
  output [31:0] MDin,
  output [31:0] LedData
);

  wire and_1_out, and_2_out, and_3_out, and_4_out, and_5_out, and_6_out, auipc, beq, blt, branch, Choice,
       CLK, clock_1_out, comparator_1_eq, comparator_1_lt, comparator_2_eq, d_ff_1_q, ecall, en, equal,
       EX_MEM_auipcout, EX_MEM_haltout, EX_MEM_jumpout, EX_MEM_lhuout, EX_MEM_luiout, EX_MEM_memtoregout,
       EX_MEM_regwriteout, Go, halt, ID_EX_alusrcbout, ID_EX_auipcout, ID_EX_haltout, ID_EX_lhuout,
       ID_EX_luiout, ID_EX_memtoregout, ID_EX_memwriteout, ID_EX_regwriteout, ID_EX_s_tpyeout, IR1, IR2, IR3,
       jal, jalr, Jump, less, lui, MemToReg, nand_1_out, not_1_out, not_2_out, not_3_out, not_4_out,
       not_5_out, or_1_out, or_2_out, or_4_out, RST, W1, W2, W3, \单周期硬布线控制器_1_alu_src , \单周期硬布线控制器_1_auipc ,
       \单周期硬布线控制器_1_beq , \单周期硬布线控制器_1_blt , \单周期硬布线控制器_1_jal , \单周期硬布线控制器_1_jalr , \单周期硬布线控制器_1_lhu ,
       \单周期硬布线控制器_1_lui , \单周期硬布线控制器_1_memtoreg , \单周期硬布线控制器_1_memwrite , \单周期硬布线控制器_1_regwrite ,
       \单周期硬布线控制器_1_s_type ;
  wire [3:0] ID_EX_aluopout, \单周期硬布线控制器_1_alu_op ;
  wire [4:0] EX_MEM_w_out, ID_EX_w_out, multiplexer_4_out, multiplexer_5_out, W_num;
  wire [11:0] shifter_1_out;
  wire [12:0] CNT_num;
  wire [15:0] adder_4_out, \LoadUse次数 , multiplexer_8_out, \分支成功数 , \总周期数 , \插入气泡数 , \无条件分支数 , \条件分支成功数 ;
  wire [19:0] shifter_2_out;
  wire [31:0] adder_1_out, adder_2_out, adder_3_out, adder_5_out, adder_6_out, alu_1_result,
       bit_extender_1_out, bit_extender_2_out, bit_extender_3_out, bit_extender_4_out, bit_extender_5_out,
       EX_IR, EX_MEM_imm_u_out, ID_EX_imm_i_out, ID_EX_imm_s_out, ID_EX_imm_u_out, ID_EX_r1out, ID_EX_r2out,
       ID_IR, IF_IR, imm32_B, imm32_J, imm32_U, MDout, MEM_IR, multiplexer_1_out, multiplexer_2_out,
       multiplexer_3_out, multiplexer_6_out, multiplexer_7_out, multiplexer_9_out, multiplexer_10_out,
       multiplexer_11_out, multiplexer_13_out, R1, R2, ram_1_data, Result, WB_IR;
  wire [31:1] EX_MEM_resultout;

  Button \u_总复位  (.out(RST));
  Button _1 (.out(IR1));
  Button _2 (.out(IR2));
  Button _3 (.out(IR3));
  // Probe on \总周期数 
  // Probe on \总周期数 
  Button \u_继续运行  (.out(Go));
  LED #(.active("true")) led_1 (.in(W1));
  LED #(.active("true")) led_2 (.in(W2));
  LED #(.active("true")) led_3 (.in(W3));
  Hex_Digit_Display hex_digit_display_1 (.value(LedData[31:28]));  // open: dp
  // Probe on IF_PC[19:0]
  // RiscV_Probe riscv_probe_1: pin names not known; wires that end beside it: IF_IR
  Hex_Digit_Display hex_digit_display_2 (.value(LedData[23:20]));  // open: dp
  Hex_Digit_Display hex_digit_display_3 (.value(LedData[27:24]));  // open: dp
  // Probe on ID_PC[19:0]
  // RiscV_Probe riscv_probe_2: pin names not known; wires that end beside it: ID_IR
  Hex_Digit_Display hex_digit_display_4 (.value(LedData[19:16]));  // open: dp
  Hex_Digit_Display hex_digit_display_5 (.value(LedData[15:12]));  // open: dp
  not not_1 (not_1_out, halt);
  Hex_Digit_Display hex_digit_display_6 (.value(LedData[7:4]));  // open: dp
  Hex_Digit_Display hex_digit_display_7 (.value(LedData[11:8]));  // open: dp
  // Probe on EX_PC[19:0]
  // RiscV_Probe riscv_probe_3: pin names not known; wires that end beside it: EX_IR
  Button Reset (.out(RST));
  Counter #(.width(16), .max('hffff), .ongoal("wrap"), .trigger("rising"), .behavior("new")) counter_1 (
    .count(not_1_out), .Q(\总周期数 ), .clk(CLK), .clr(RST));  // open: load, D, carry, preset, down
  Hex_Digit_Display hex_digit_display_8 (.value(LedData[3:0]));  // open: dp
  Multiplexer #(.select(1), .width(32), .disabled("Z"), .enable("false")) multiplexer_1 (
    .in0(adder_3_out), .in1(Result), .out(multiplexer_1_out), .sel(jalr));
  Multiplexer #(.select(1), .width(32), .disabled("Z"), .enable("false")) multiplexer_2 (
    .in0(multiplexer_1_out), .in1(adder_1_out), .out(multiplexer_2_out), .sel(jal));
  Adder #(.width(32)) adder_1 (.a(imm32_J), .b(WB_PC), .out(adder_1_out));  // open: cin, cout
  Adder #(.width(32)) adder_2 (.a(imm32_B), .b(WB_PC), .out(adder_2_out));  // open: cin, cout
  // Probe on \总周期数 
  // Probe on M_PC[19:0]
  // RiscV_Probe riscv_probe_4: pin names not known; wires that end beside it: MEM_IR
  Multiplexer #(.select(1), .width(32), .disabled("Z"), .enable("false")) multiplexer_3 (
    .in0(multiplexer_2_out), .in1(adder_2_out), .out(multiplexer_3_out), .sel(branch));
  not not_2 (not_2_out, halt);
  // Probe on \总周期数 
  // Probe on \无条件分支数 
  // Probe on \条件分支成功数 
  // Probe on \插入气泡数 
  // Probe on \LoadUse次数 
  Register #(.width(32), .trigger("rising"), .Select("low")) PC (
    .D(multiplexer_3_out), .en(not_2_out), .Q(IF_PC), .clk(CLK), .clr(RST));
  // Probe on IF_PC[11:0]
  // Probe on WB_PC[19:0]
  // RiscV_Probe riscv_probe_5: pin names not known; wires that end beside it: WB_IR
  // Probe on EX_PC[11:0]
  // Probe on ID_PC[11:0]
  Adder #(.width(32)) adder_3 (.a(IF_PC), .b(32'h4), .out(adder_3_out));  // open: cin, cout
  // Probe on M_PC[11:0]
  D_Flip_Flop #(.trigger("high"), .Pre_Clr_Positions("LEGACY"), .NegatePresetClear("false"), .enable("true"), .NewFFLayout("false")) d_ff_1 (.Q(d_ff_1_q));  // open: clk, D, Qn, preset, en, reset
  // Probe on 13'hc
  ROM #(.addrWidth(10), .dataWidth(32), .Select("high")) rom_1 (.addr(IF_PC[11:2]), .data(IF_IR));
  // Probe on WB_PC[11:0]
  Comparator #(.width(13), .mode("twosComplement")) comparator_1 (
    .a(CNT_num), .b(13'hc), .eq(comparator_1_eq), .lt(comparator_1_lt));  // open: gt
  Clock #(.highDuration(1), .lowDuration(1)) clock_1 (.out(clock_1_out));
  IF_ID IF_ID (
    .PCin(IF_PC), .IRin(IF_IR), .PCout(ID_PC), .IRout(ID_IR), .RST(RST), .clk(CLK), .EN(en));  // open: PridictJumpin, PridictJumpout
  nand nand_1 (nand_1_out, d_ff_1_q, comparator_1_eq);
  Counter #(.width(13), .max('h1fff), .ongoal("stay"), .trigger("rising"), .behavior("old")) counter_2 (
    .count(comparator_1_lt), .Q(CNT_num), .clk(clock_1_out));  // open: load, D, carry, clr, preset
  assign CLK = nand_1_out ? clock_1_out : 1'bz;  // Controlled_Buffer controlled_buffer_1
  // RiscV_Probe riscv_probe_6: pin names not known; wires that end beside it: IF_PC, IF_IR, ID_IR
  Pull_Resistor #(.pull(1)) pull_resistor_1 (.node(CLK));
  \单周期硬布线控制器  \u_单周期硬布线控制器_1  (
    .Funct({ID_IR[30], ID_IR[25], ID_IR[14:12]}), .OP(ID_IR[6:2]), .ALU_OP(\单周期硬布线控制器_1_alu_op ),
    .MemToReg(\单周期硬布线控制器_1_memtoreg ), .MemWrite(\单周期硬布线控制器_1_memwrite ), .ALU_SRC(\单周期硬布线控制器_1_alu_src ),
    .RegWrite(\单周期硬布线控制器_1_regwrite ), .ecall(ecall), .S_type(\单周期硬布线控制器_1_s_type ),
    .Jalr(\单周期硬布线控制器_1_jalr ), .Beq(\单周期硬布线控制器_1_beq ), .JAL(\单周期硬布线控制器_1_jal ),
    .Bne(\单周期硬布线控制器_1_memtoreg ), .in_3(ID_IR[21]), .auipc(\单周期硬布线控制器_1_auipc ), .lui(\单周期硬布线控制器_1_lui ),
    .lhu(\单周期硬布线控制器_1_lhu ), .blt(\单周期硬布线控制器_1_blt ));  // open: uret, CSRRCI, CSRRSI
  Multiplexer #(.select(1), .width(5), .disabled("Z"), .enable("false")) multiplexer_4 (
    .in0(ID_IR[19:15]), .in1(5'b10001), .out(multiplexer_4_out), .sel(ecall));
  Multiplexer #(.select(1), .width(5), .disabled("Z"), .enable("false")) multiplexer_5 (
    .in0(ID_IR[24:20]), .in1(5'b01010), .out(multiplexer_5_out), .sel(ecall));
  assign bit_extender_1_out = {{20{ID_IR[31]}}, ID_IR[31:20]};  // Bit_Extender bit_extender_1
  assign bit_extender_2_out = {{20{ID_IR[31]}}, {ID_IR[31:25], ID_IR[11:7]}};  // Bit_Extender bit_extender_2
  Shifter #(.width(12), .shift("ll")) shifter_1 (
    .in({ID_IR[31], ID_IR[7], ID_IR[30:25], ID_IR[11:8]}), .\dist (4'b0001), .out(shifter_1_out));
  Shifter #(.width(20), .shift("ll")) shifter_2 (
    .in({ID_IR[31], ID_IR[19:12], ID_IR[20], ID_IR[30:21]}), .\dist (5'b00001), .out(shifter_2_out));
  assign bit_extender_3_out = {{20{shifter_1_out[11]}}, shifter_1_out};  // Bit_Extender bit_extender_3
  assign bit_extender_4_out = {{12{shifter_2_out[19]}}, shifter_2_out};  // Bit_Extender bit_extender_4
  Comparator #(.width(32), .mode("twosComplement")) comparator_2 (
    .a(R1), .b(32'ha), .eq(comparator_2_eq));  // open: gt, lt
  not not_3 (not_3_out, comparator_2_eq);
  and and_1 (and_1_out, ecall, not_3_out);
  and and_2 (and_2_out, comparator_2_eq, ecall);
  Regifile regifile_1 (
    .Din(RDin), .Clk(CLK), .R1(R1), .R2(R2), .WE(RegWrite), .W_num(W_num), .R1_num(multiplexer_4_out),
    .R2_num(multiplexer_5_out));
  Register #(.width(32), .trigger("rising"), .Select("low")) register_1 (
    .D(R2), .en(and_1_out), .Q(LedData), .clk(CLK), .clr(RST));
  and and_3 (and_3_out, and_2_out, not_4_out);
  not not_4 (not_4_out, Go);
  Counter #(.width(16), .max('hffff), .ongoal("wrap"), .trigger("rising"), .behavior("new")) counter_3 (
    .count(branch), .Q(\条件分支成功数 ), .clk(CLK), .clr(RST));  // open: load, D, carry, preset, down
  or or_1 (or_1_out, jal, jalr);
  Counter #(.width(16), .max('hffff), .ongoal("wrap"), .trigger("rising"), .behavior("new")) counter_4 (
    .count(or_1_out), .Q(\无条件分支数 ), .clk(CLK), .clr(RST));  // open: load, D, carry, preset, down
  ID_EX ID_EX (
    .PCin(ID_PC), .Lhuin(\单周期硬布线控制器_1_lhu ), .Jalrin(\单周期硬布线控制器_1_jalr ), .IRin(ID_IR),
    .Jalin(\单周期硬布线控制器_1_jal ), .Beqin(\单周期硬布线控制器_1_beq ), .Imm_I_in(bit_extender_1_out),
    .Bltin(\单周期硬布线控制器_1_blt ), .Imm_S_in(bit_extender_2_out), .Bnein(\单周期硬布线控制器_1_memtoreg ),
    .Imm_B_in(bit_extender_3_out), .MemToRegin(\单周期硬布线控制器_1_memtoreg ), .MemWritein(\单周期硬布线控制器_1_memwrite ),
    .Imm_J_in(bit_extender_4_out), .AluOpin(\单周期硬布线控制器_1_alu_op ), .Imm_U_in({ID_IR[31:12], {12{1'b0}}}),
    .AluSrcBin(\单周期硬布线控制器_1_alu_src ), .R1in(R1), .RegWritein(\单周期硬布线控制器_1_regwrite ), .R2in(R2),
    .S_Typein(\单周期硬布线控制器_1_s_type ), .haltin(and_3_out), .W_in(ID_IR[11:7]), .PCout(EX_PC),
    .Lhuout(ID_EX_lhuout), .Jalrout(jalr), .IRout(EX_IR), .Jalout(jal), .Beqout(beq),
    .Imm_I_out(ID_EX_imm_i_out), .Bltout(blt), .Imm_S_out(ID_EX_imm_s_out), .Bneout(blt),
    .Imm_B_out(imm32_B), .MemToRegout(ID_EX_memtoregout), .MemWriteout(ID_EX_memwriteout),
    .Imm_J_out(imm32_J), .AluOpout(ID_EX_aluopout), .Imm_U_out(ID_EX_imm_u_out),
    .AluSrcBout(ID_EX_alusrcbout), .R1out(ID_EX_r1out), .RegWriteout(ID_EX_regwriteout), .R2out(ID_EX_r2out),
    .S_Tpyeout(ID_EX_s_tpyeout), .haltout(ID_EX_haltout), .W_out(ID_EX_w_out), .RST(RST), .EN_H(en),
    .CLK(CLK), .Luiin(\单周期硬布线控制器_1_lui ), .Luiout(ID_EX_luiout), .auipcin(\单周期硬布线控制器_1_auipc ),
    .auipcout(ID_EX_auipcout));  // open: R1CHOICEin, R1CHOICEout, R2CHOICEin, R2CHOICEout, PridictJumpin, PridictJumpout
  or or_2 (or_2_out, jal, jalr);
  Multiplexer #(.select(1), .width(32), .disabled("Z"), .enable("false")) multiplexer_6 (
    .in0(ID_EX_imm_i_out), .in1(ID_EX_imm_s_out), .out(multiplexer_6_out), .sel(ID_EX_s_tpyeout));
  Multiplexer #(.select(1), .width(32), .disabled("Z"), .enable("false")) multiplexer_7 (
    .in0(ID_EX_r2out), .in1(multiplexer_6_out), .out(multiplexer_7_out), .sel(ID_EX_alusrcbout));
  Adder #(.width(16)) adder_4 (.a(\无条件分支数 ), .b(\条件分支成功数 ), .out(adder_4_out));  // open: cin, cout
  ALU alu_1 (
    .X(ID_EX_r1out), .Y(multiplexer_7_out), .AluOP(ID_EX_aluopout), .Equal(equal), .Result(alu_1_result),
    .out_6(less));  // open: Result_2, out_4
  Shifter #(.width(16), .shift("ll")) shifter_3 (.in(adder_4_out), .\dist (4'b0001), .out(\插入气泡数 ));
  not not_5 (not_5_out, equal);
  and and_4 (and_4_out, blt, less);
  or or_3 (branch, and_4_out, and_5_out, and_6_out);
  and and_5 (and_5_out, beq, equal);
  and and_6 (and_6_out, not_5_out, blt);
  Counter #(.width(16), .max('hffff), .ongoal("wrap"), .trigger("rising"), .behavior("new")) counter_5 (
    .count(branch), .Q(\分支成功数 ), .clk(CLK), .clr(RST));  // open: load, D, carry, preset, down
  EX_MEM EX_MEM (
    .MemToRegin(ID_EX_memtoregout), .PCin(EX_PC), .MemWritein(ID_EX_memwriteout), .IRin(EX_IR),
    .Jumpin(or_2_out), .RegWritein(ID_EX_regwriteout), .Resultin(alu_1_result), .Haltin(ID_EX_haltout),
    .MDatain(ID_EX_r2out), .W_in(ID_EX_w_out), .MemToRegout(EX_MEM_memtoregout), .PCout(M_PC),
    .MemWriteout(MemWrite), .IRout(MEM_IR), .Jumpout(EX_MEM_jumpout), .RegWriteout(EX_MEM_regwriteout),
    .Resultout({EX_MEM_resultout, Choice}), .Haltout(EX_MEM_haltout), .Mdataout(MDin), .W_out(EX_MEM_w_out),
    .RST(RST), .EN_H(en), .CLK(CLK), .auipcin(ID_EX_auipcout), .auipcout(EX_MEM_auipcout),
    .Luiin(ID_EX_luiout), .Luiout(EX_MEM_luiout), .Lhuin(ID_EX_lhuout), .Lhuout(EX_MEM_lhuout),
    .Imm_U_in(ID_EX_imm_u_out), .Imm_U_out(EX_MEM_imm_u_out));
  RAM #(.addrWidth(10), .dataWidth(32), .bus("separate"), .Select("high")) ram_1 (
    .addr(EX_MEM_resultout[10:1]), .din(MDin), .data(ram_1_data), .str(MemWrite), .clk(CLK),
    .ld(EX_MEM_memtoregout), .clr(RST));  // open: sel
  assign bit_extender_5_out = {{16{1'b0}}, multiplexer_8_out};  // Bit_Extender bit_extender_5
  Multiplexer #(.select(1), .width(16), .disabled("Z"), .enable("false")) multiplexer_8 (
    .in0(ram_1_data[15:0]), .in1(ram_1_data[31:16]), .out(multiplexer_8_out), .sel(Choice));
  Multiplexer #(.select(1), .width(32), .disabled("Z"), .enable("false")) multiplexer_9 (
    .in0(ram_1_data), .in1(bit_extender_5_out), .out(multiplexer_9_out), .sel(EX_MEM_lhuout));
  MEM_WB MEM_WB (
    .PCin(M_PC), .MemToRegin(EX_MEM_memtoregout), .IRin(MEM_IR), .Jumpin(EX_MEM_jumpout),
    .RegWritein(EX_MEM_regwriteout), .Resultin({EX_MEM_resultout, Choice}), .Haltin(EX_MEM_haltout),
    .RMDatain(multiplexer_9_out), .W_in(EX_MEM_w_out), .PCout(WB_PC), .MemToRegout(MemToReg), .IRout(WB_IR),
    .Jumpout(Jump), .RegWriteout(RegWrite), .Resultout(Result), .Haltout(halt), .RMdataout(MDout),
    .W_out(W_num), .RST(RST), .EN_H(en), .CLK(CLK), .auipcin(EX_MEM_auipcout), .auipcout(auipc),
    .Luiin(EX_MEM_luiout), .Luiout(lui), .Imm_U_in(EX_MEM_imm_u_out), .Imm_U_out(imm32_U));  // open: lhuin, lhuout, choicein, choiceout
  not not_6 (en, halt);
  Multiplexer #(.select(1), .width(32), .disabled("Z"), .enable("false")) multiplexer_10 (
    .in0(Result), .in1(MDout), .out(multiplexer_10_out), .sel(MemToReg));
  Adder #(.width(32)) adder_5 (.a(WB_PC), .b(32'h4), .out(adder_5_out));  // open: cin, cout
  Multiplexer #(.select(1), .width(32), .disabled("Z"), .enable("false")) multiplexer_11 (
    .in0(multiplexer_10_out), .in1(adder_5_out), .out(multiplexer_11_out), .sel(Jump));
  Adder #(.width(32)) adder_6 (.a(imm32_U), .b(WB_PC), .out(adder_6_out));  // open: cin, cout
  Multiplexer #(.select(1), .width(32), .disabled("Z"), .enable("false")) multiplexer_12 (
    .in0(multiplexer_11_out), .in1(multiplexer_13_out), .out(RDin), .sel(or_4_out));
  Multiplexer #(.select(1), .width(32), .disabled("Z"), .enable("false")) multiplexer_13 (
    .in0(imm32_U), .in1(adder_6_out), .out(multiplexer_13_out), .sel(auipc));
  or or_4 (or_4_out, auipc, lui);

  // Other names for the same wires on the sheet: bne = blt; MEM_PC[31:0] = M_PC

  // Notes on the sheet:
  //   中断源
  //   时空图监测，可删除
  //   中断等待指示
  //   数码管输出
  //   控制位
  //   指令存储器
  //   流水调试日志用
  //   暂停节拍，不能为0
  //   contents of rom_1 (hex, n*v repeats v):
  //   13 430497 900533 2200893 73 430497 900533 2200893 73 430497 900533 2200893 73 430497 900533 2200893
  //   73 430497 900533 2200893 73 430497 900533 2200893 73 430497 900533 2200893 73 430497 900533 2200893
  //   73 a00893 73 800e13 fedc04b7 fff00413 1045413 84e4b3 900533 2200893 73 ba984b7 900533 73 76544b7
  //   900533 73 32104b7 900533 73 fffe0e13 fa0e1ee3 a00893 73 313 1000e13 8400493 849493 8348493 400913
  //   891913 490913 849493 8248493 849493 8148493 891913 490913 891913 490913 932023 12484b3 430313
  //   fffe0e13 fe0e18e3 2000e13 313 35483 900533 2200893 73 230313 fffe0e13 fe0e14e3 a00893 73 ff100493
  //   900533 2200893 73 148493 fe04c8e3 a00893 73
  //   戳工具置1进入计数暂停模式，ctrl+k时钟自动运行到对应节拍暂停
  //   ctrl+k关闭时钟连续运行，将控制位置零，进入单步调试模式调试
  //   指令字ID.IR
  //   可计数暂停的时钟源
  //   用这个时钟源需要去掉电路中的其他时钟源
  //   rs1
  //   rs2
  //   rd
  //   Beq
  //   Bne
  //   MemToReg
  //   MemWrite
  //   AluOP
  //   AluSrcB
  //   RegWrite
  //   转换为字偏移量,所以需要逻辑左移一位
  //   为方便自动评测，需要输出流水线各段保存的PC值，注意是PC不是PC+4，另外ID段寄存器写入信息，Mem段内存写入信息也要输出
  //   数据存储器
endmodule

module \重定向流水线  (
  output RegWrite,
  output MemWrite,
  output [31:0] IF_PC,
  output [31:0] ID_PC,
  output [31:0] EX_PC,
  output [31:0] M_PC,
  output [31:0] WB_PC,
  output [31:0] RDin,
  output [31:0] MDin,
  output [31:0] LedData
);

  wire and_1_out, and_2_out, and_3_out, and_4_out, and_5_out, and_6_out, and_7_out, and_8_out, auipc, beq,
       blt, bne, branch, Choicein, CLK, clock_1_out, comparator_1_eq, comparator_1_lt, comparator_2_eq,
       d_ff_1_q, en, equal, EX_ecall, EX_MEM_auipcout, EX_MEM_haltout, EX_MEM_jumpout, EX_MEM_lhuout,
       EX_MEM_luiout, EX_MEM_memtoregout, EX_RegWrite, Go, halt, ID_ecall, ID_EX_alusrcbout, ID_EX_auipcout,
       ID_EX_lhuout, ID_EX_luiout, ID_EX_memtoregout, ID_EX_memwriteout, ID_EX_s_tpyeout, IR1, IR2, IR3, jal,
       jalr, Jump, less, lhuout, LoadUse, lui, MEM_RegWrite, MEM_WB_choiceout, MEM_WB_haltout, MemToReg,
       nand_1_out, not_1_out, not_2_out, not_3_out, not_4_out, not_5_out, not_6_out, not_7_out, not_8_out,
       or_1_out, or_2_out, or_3_out, or_4_out, or_6_out, RST, W1, W2, W3, \单周期硬布线控制器_1_alu_src ,
       \单周期硬布线控制器_1_auipc , \单周期硬布线控制器_1_beq , \单周期硬布线控制器_1_blt , \单周期硬布线控制器_1_bne , \单周期硬布线控制器_1_jal ,
       \单周期硬布线控制器_1_jalr , \单周期硬布线控制器_1_lhu , \单周期硬布线控制器_1_lui , \单周期硬布线控制器_1_memtoreg ,
       \单周期硬布线控制器_1_memwrite , \单周期硬布线控制器_1_regwrite , \单周期硬布线控制器_1_s_type , \数据相关 ;
  wire [1:0] EX_R1C, EX_R2C, ID_R1C, ID_R2C;
  wire [3:0] ID_EX_aluopout, \单周期硬布线控制器_1_alu_op ;
  wire [4:0] EX_W_num, ID_funct, ID_R1_num, ID_R2_num, MEM_W_num, W_num;
  wire [11:0] shifter_1_out;
  wire [12:0] CNT_num;
  wire [15:0] adder_4_out, \LoadUse次数 , multiplexer_10_out, shifter_3_out, \总周期数 , \插入气泡数 , \无条件分支数 ,
       \条件分支成功数 ;
  wire [19:0] shifter_2_out;
  wire [31:0] adder_1_out, adder_2_out, adder_3_out, adder_6_out, adder_7_out, bit_extender_1_out,
       bit_extender_2_out, bit_extender_3_out, bit_extender_4_out, bit_extender_5_out, EX_IR,
       EX_MEM_imm_u_out, EX_R1, EX_R2, ID_EX_imm_i_out, ID_EX_imm_s_out, ID_EX_imm_u_out, ID_IR, IF_IR,
       imm32_B, imm32_J, jaddress, MDout, MEM_IR, MEM_Result, MEM_WB_rmdataout, multiplexer_1_out,
       multiplexer_2_out, multiplexer_3_out, multiplexer_7_out, multiplexer_8_out, multiplexer_12_out,
       multiplexer_13_out, multiplexer_14_out, R1, R1out, R2, R2out, ram_1_data, Result, WB_imm32_U, WB_IR;

  Button \u_总复位  (.out(RST));
  Button _1 (.out(IR1));
  Button _2 (.out(IR2));
  Button _3 (.out(IR3));
  // Probe on \总周期数 
  // Probe on \总周期数 
  Button \u_继续运行  (.out(Go));
  LED #(.active("true")) led_1 (.in(W1));
  LED #(.active("true")) led_2 (.in(W2));
  LED #(.active("true")) led_3 (.in(W3));
  Hex_Digit_Display hex_digit_display_1 (.value(LedData[31:28]));  // open: dp
  // Probe on IF_PC[19:0]
  // RiscV_Probe riscv_probe_1: pin names not known; wires that end beside it: IF_IR
  Hex_Digit_Display hex_digit_display_2 (.value(LedData[27:24]));  // open: dp
  Hex_Digit_Display hex_digit_display_3 (.value(LedData[23:20]));  // open: dp
  // Probe on ID_PC[19:0]
  // RiscV_Probe riscv_probe_2: pin names not known; wires that end beside it: {ID_IR[31], ID_funct[4], ID_IR[29:26], ID_funct[3], ID_IR[24:15], ID_funct[2:0], ID_IR[11:0]}
  Hex_Digit_Display hex_digit_display_4 (.value(LedData[19:16]));  // open: dp
  Hex_Digit_Display hex_digit_display_5 (.value(LedData[15:12]));  // open: dp
  Hex_Digit_Display hex_digit_display_6 (.value(LedData[7:4]));  // open: dp
  Hex_Digit_Display hex_digit_display_7 (.value(LedData[11:8]));  // open: dp
  // Probe on EX_PC[19:0]
  // RiscV_Probe riscv_probe_3: pin names not known; wires that end beside it: EX_IR
  Hex_Digit_Display hex_digit_display_8 (.value(LedData[3:0]));  // open: dp
  Multiplexer #(.select(1), .width(32), .disabled("Z"), .enable("false")) multiplexer_1 (
    .in0(adder_3_out), .in1(jaddress), .out(multiplexer_1_out), .sel(jalr));
  Adder #(.width(32)) adder_1 (.a(imm32_J), .b(EX_PC), .out(adder_1_out));  // open: cin, cout
  Adder #(.width(32)) adder_2 (.a(imm32_B), .b(EX_PC), .out(adder_2_out));  // open: cin, cout
  \数据相关_重定向流水线  \u_数据相关_重定向流水线_1  (
    .ID_R1_num(ID_R1_num), .EX_W_num(EX_W_num), .EX_RegWrite(EX_RegWrite), .ID_R2_num(ID_R2_num),
    .MEM_W_num(MEM_W_num), .MEM_RegWrite(MEM_RegWrite), .ID_OP(ID_IR[6:2]), .EX_OP(EX_IR[6:2]),
    .ID_Funct(ID_funct), .R1C(ID_R1C), .R2C(ID_R2C), .\数据相关 (\数据相关 ), .Load_Use(LoadUse));
  // Probe on \总周期数 
  // Probe on M_PC[19:0]
  // RiscV_Probe riscv_probe_4: pin names not known; wires that end beside it: MEM_IR
  Multiplexer #(.select(1), .width(32), .disabled("Z"), .enable("false")) multiplexer_2 (
    .in0(multiplexer_1_out), .in1(adder_1_out), .out(multiplexer_2_out), .sel(jal));
  Multiplexer #(.select(1), .width(32), .disabled("Z"), .enable("false")) multiplexer_3 (
    .in0(multiplexer_2_out), .in1(adder_2_out), .out(multiplexer_3_out), .sel(branch));
  not not_1 (not_1_out, LoadUse);
  // Probe on \总周期数 
  // Probe on \无条件分支数 
  // Probe on \条件分支成功数 
  // Probe on \插入气泡数 
  // Probe on \LoadUse次数 
  Register #(.width(32), .trigger("rising"), .Select("low")) PC (
    .D(multiplexer_3_out), .en(and_1_out), .Q(IF_PC), .clk(CLK), .clr(RST));
  and and_1 (and_1_out, not_1_out, not_2_out);
  not not_2 (not_2_out, halt);
  // Probe on IF_PC[11:0]
  // Probe on WB_PC[19:0]
  // RiscV_Probe riscv_probe_5: pin names not known; wires that end beside it: WB_IR
  // Probe on ID_PC[11:0]
  // Probe on EX_PC[11:0]
  // Probe on M_PC[11:0]
  D_Flip_Flop #(.trigger("high"), .Pre_Clr_Positions("LEGACY"), .NegatePresetClear("false"), .enable("true"), .NewFFLayout("false")) d_ff_1 (.Q(d_ff_1_q));  // open: clk, D, Qn, preset, en, reset
  // Probe on 13'h97
  ROM #(.addrWidth(10), .dataWidth(32), .Select("high")) rom_1 (.addr(IF_PC[11:2]), .data(IF_IR));
  Adder #(.width(32)) adder_3 (.a(IF_PC), .b(32'h4), .out(adder_3_out));  // open: cin, cout
  or or_1 (or_1_out, RST, branch, jal, jalr);
  // Probe on WB_PC[11:0]
  Comparator #(.width(13), .mode("twosComplement")) comparator_1 (
    .a(CNT_num), .b(13'h97), .eq(comparator_1_eq), .lt(comparator_1_lt));  // open: gt
  Clock #(.highDuration(1), .lowDuration(1)) clock_1 (.out(clock_1_out));
  IF_ID IF_ID (
    .PCin(IF_PC), .IRin(IF_IR), .PCout(ID_PC),
    .IRout({ID_IR[31], ID_funct[4], ID_IR[29:26], ID_funct[3], ID_IR[24:15], ID_funct[2:0], ID_IR[11:0]}),
    .RST(or_1_out), .clk(CLK), .EN(and_2_out));  // open: PridictJumpin, PridictJumpout
  and and_2 (and_2_out, en, not_3_out);
  not not_3 (not_3_out, LoadUse);
  nand nand_1 (nand_1_out, d_ff_1_q, comparator_1_eq);
  Counter #(.width(13), .max('h1fff), .ongoal("stay"), .trigger("rising"), .behavior("old")) counter_1 (
    .count(comparator_1_lt), .Q(CNT_num), .clk(clock_1_out));  // open: load, D, carry, clr, preset
  // RiscV_Probe riscv_probe_6: pin names not known; wires that end beside it: {ID_IR[31], ID_funct[4], ID_IR[29:26], ID_funct[3], ID_IR[24:15], ID_funct[2:0], ID_IR[11:0]}
  assign CLK = nand_1_out ? clock_1_out : 1'bz;  // Controlled_Buffer controlled_buffer_1
  Pull_Resistor #(.pull(1)) pull_resistor_1 (.node(CLK));
  assign bit_extender_1_out = {{20{ID_IR[31]}}, {ID_IR[31], ID_funct[4], ID_IR[29:26], ID_funct[3], ID_IR[24:20]}};  // Bit_Extender bit_extender_1
  assign bit_extender_2_out = {{20{ID_IR[31]}}, {ID_IR[31], ID_funct[4], ID_IR[29:26], ID_funct[3], ID_IR[11:7]}};  // Bit_Extender bit_extender_2
  \单周期硬布线控制器  \u_单周期硬布线控制器_1  (
    .Funct(ID_funct), .OP(ID_IR[6:2]), .ALU_OP(\单周期硬布线控制器_1_alu_op ), .MemToReg(\单周期硬布线控制器_1_memtoreg ),
    .MemWrite(\单周期硬布线控制器_1_memwrite ), .ALU_SRC(\单周期硬布线控制器_1_alu_src ), .RegWrite(\单周期硬布线控制器_1_regwrite ),
    .ecall(ID_ecall), .S_type(\单周期硬布线控制器_1_s_type ), .Jalr(\单周期硬布线控制器_1_jalr ), .Beq(\单周期硬布线控制器_1_beq ),
    .JAL(\单周期硬布线控制器_1_jal ), .Bne(\单周期硬布线控制器_1_bne ), .in_3(ID_IR[21]), .auipc(\单周期硬布线控制器_1_auipc ),
    .lui(\单周期硬布线控制器_1_lui ), .lhu(\单周期硬布线控制器_1_lhu ), .blt(\单周期硬布线控制器_1_blt ));  // open: uret, CSRRCI, CSRRSI
  Multiplexer #(.select(1), .width(5), .disabled("Z"), .enable("false")) multiplexer_4 (
    .in0(ID_IR[19:15]), .in1(5'b10001), .out(ID_R1_num), .sel(ID_ecall));
  Multiplexer #(.select(1), .width(5), .disabled("Z"), .enable("false")) multiplexer_5 (
    .in0(ID_IR[24:20]), .in1(5'b01010), .out(ID_R2_num), .sel(ID_ecall));
  Shifter #(.width(12), .shift("ll")) shifter_1 (
    .in({ID_IR[31], ID_IR[7], ID_funct[4], ID_IR[29:26], ID_funct[3], ID_IR[11:8]}), .\dist (4'b0001),
    .out(shifter_1_out));
  assign bit_extender_3_out = {{20{shifter_1_out[11]}}, shifter_1_out};  // Bit_Extender bit_extender_3
  Shifter #(.width(20), .shift("ll")) shifter_2 (
    .in({ID_IR[31], ID_IR[19:15], ID_funct[2:0], ID_IR[20], ID_funct[4], ID_IR[29:26], ID_funct[3], ID_IR[24:21]}),
    .\dist (5'b00001), .out(shifter_2_out));
  assign bit_extender_4_out = {{12{shifter_2_out[19]}}, shifter_2_out};  // Bit_Extender bit_extender_4
  not not_4 (not_4_out, CLK);
  Regifile regifile_1 (
    .Din(RDin), .Clk(not_4_out), .R1(R1), .R2(R2), .WE(RegWrite), .W_num(W_num), .R1_num(ID_R1_num),
    .R2_num(ID_R2_num));
  or or_2 (or_2_out, LoadUse, or_1_out);
  ID_EX ID_EX (
    .PCin(ID_PC), .Lhuin(\单周期硬布线控制器_1_lhu ), .Jalrin(\单周期硬布线控制器_1_jalr ),
    .IRin({ID_IR[31], ID_funct[4], ID_IR[29:26], ID_funct[3], ID_IR[24:15], ID_funct[2:0], ID_IR[11:0]}),
    .Jalin(\单周期硬布线控制器_1_jal ), .Beqin(\单周期硬布线控制器_1_beq ), .Imm_I_in(bit_extender_1_out),
    .Bltin(\单周期硬布线控制器_1_blt ), .Imm_S_in(bit_extender_2_out), .Bnein(\单周期硬布线控制器_1_bne ),
    .Imm_B_in(bit_extender_3_out), .MemToRegin(\单周期硬布线控制器_1_memtoreg ), .MemWritein(\单周期硬布线控制器_1_memwrite ),
    .Imm_J_in(bit_extender_4_out), .AluOpin(\单周期硬布线控制器_1_alu_op ),
    .Imm_U_in({ID_IR[31], ID_funct[4], ID_IR[29:26], ID_funct[3], ID_IR[24:15], ID_funct[2:0], {12{1'b0}}}),
    .AluSrcBin(\单周期硬布线控制器_1_alu_src ), .R1in(R1), .RegWritein(\单周期硬布线控制器_1_regwrite ), .R2in(R2),
    .S_Typein(\单周期硬布线控制器_1_s_type ), .haltin(ID_ecall), .W_in(ID_IR[11:7]), .PCout(EX_PC),
    .Lhuout(ID_EX_lhuout), .Jalrout(jalr), .IRout(EX_IR), .Jalout(jal), .Beqout(beq),
    .Imm_I_out(ID_EX_imm_i_out), .Bltout(blt), .Imm_S_out(ID_EX_imm_s_out), .Bneout(bne),
    .Imm_B_out(imm32_B), .MemToRegout(ID_EX_memtoregout), .MemWriteout(ID_EX_memwriteout),
    .Imm_J_out(imm32_J), .AluOpout(ID_EX_aluopout), .Imm_U_out(ID_EX_imm_u_out),
    .AluSrcBout(ID_EX_alusrcbout), .R1out(R1out), .RegWriteout(EX_RegWrite), .R2out(R2out),
    .S_Tpyeout(ID_EX_s_tpyeout), .haltout(EX_ecall), .W_out(EX_W_num), .RST(or_2_out), .EN_H(en), .CLK(CLK),
    .Luiin(\单周期硬布线控制器_1_lui ), .Luiout(ID_EX_luiout), .auipcin(\单周期硬布线控制器_1_auipc ),
    .auipcout(ID_EX_auipcout), .R1CHOICEin(ID_R1C), .R1CHOICEout(EX_R1C), .R2CHOICEin(ID_R2C),
    .R2CHOICEout(EX_R2C));  // open: PridictJumpin, PridictJumpout
  or or_3 (or_3_out, jal, jalr);
  Multiplexer #(.select(2), .width(32), .disabled("Z"), .enable("false")) multiplexer_6 (
    .in0(R2out), .in1(RDin), .in2({MEM_Result[31:2], Choicein, MEM_Result[0]}), .out(EX_R2), .sel(EX_R2C));  // open: in3
  Multiplexer #(.select(1), .width(32), .disabled("Z"), .enable("false")) multiplexer_7 (
    .in0(ID_EX_imm_i_out), .in1(ID_EX_imm_s_out), .out(multiplexer_7_out), .sel(ID_EX_s_tpyeout));
  Counter #(.width(16), .max('hffff), .ongoal("wrap"), .trigger("rising"), .behavior("new")) counter_2 (
    .count(branch), .Q(\条件分支成功数 ), .clk(CLK), .clr(RST));  // open: load, D, carry, preset, down
  Multiplexer #(.select(1), .width(32), .disabled("Z"), .enable("false")) multiplexer_8 (
    .in0(EX_R2), .in1(multiplexer_7_out), .out(multiplexer_8_out), .sel(ID_EX_alusrcbout));
  Comparator #(.width(32), .mode("twosComplement")) comparator_2 (
    .a(EX_R1), .b(32'h22), .eq(comparator_2_eq));  // open: gt, lt
  not not_5 (not_5_out, comparator_2_eq);
  Multiplexer #(.select(2), .width(32), .disabled("Z"), .enable("false")) multiplexer_9 (
    .in0(R1out), .in1(RDin), .in2({MEM_Result[31:2], Choicein, MEM_Result[0]}), .out(EX_R1), .sel(EX_R1C));  // open: in3
  ALU alu_1 (
    .X(EX_R1), .Y(multiplexer_8_out), .AluOP(ID_EX_aluopout), .Equal(equal), .Result(jaddress), .out_6(less));  // open: Result_2, out_4
  and and_3 (and_3_out, EX_ecall, comparator_2_eq);
  and and_4 (and_4_out, not_5_out, EX_ecall);
  and and_5 (and_5_out, blt, less);
  and and_6 (and_6_out, beq, equal);
  not not_6 (not_6_out, equal);
  and and_7 (and_7_out, not_6_out, bne);
  Register #(.width(32), .trigger("rising"), .Select("low")) register_1 (
    .D(EX_R2), .en(and_3_out), .Q(LedData), .clk(CLK), .clr(RST));
  or or_4 (or_4_out, jal, jalr);
  Counter #(.width(16), .max('hffff), .ongoal("wrap"), .trigger("rising"), .behavior("new")) counter_3 (
    .count(or_4_out), .Q(\无条件分支数 ), .clk(CLK), .clr(RST));  // open: load, D, carry, preset, down
  or or_5 (branch, and_5_out, and_6_out, and_7_out);
  not not_7 (not_7_out, halt);
  EX_MEM EX_MEM (
    .MemToRegin(ID_EX_memtoregout), .PCin(EX_PC), .MemWritein(ID_EX_memwriteout), .IRin(EX_IR),
    .Jumpin(or_3_out), .RegWritein(EX_RegWrite), .Resultin(jaddress), .Haltin(and_4_out), .MDatain(EX_R2),
    .W_in(EX_W_num), .MemToRegout(EX_MEM_memtoregout), .PCout(M_PC), .MemWriteout(MemWrite), .IRout(MEM_IR),
    .Jumpout(EX_MEM_jumpout), .RegWriteout(MEM_RegWrite),
    .Resultout({MEM_Result[31:2], Choicein, MEM_Result[0]}), .Haltout(EX_MEM_haltout), .Mdataout(MDin),
    .W_out(MEM_W_num), .RST(RST), .EN_H(en), .CLK(CLK), .auipcin(ID_EX_auipcout), .auipcout(EX_MEM_auipcout),
    .Luiin(ID_EX_luiout), .Luiout(EX_MEM_luiout), .Lhuin(ID_EX_lhuout), .Lhuout(EX_MEM_lhuout),
    .Imm_U_in(ID_EX_imm_u_out), .Imm_U_out(EX_MEM_imm_u_out));
  Counter #(.width(16), .max('hffff), .ongoal("wrap"), .trigger("rising"), .behavior("new")) counter_4 (
    .count(not_7_out), .Q(\总周期数 ), .clk(CLK), .clr(RST));  // open: load, D, carry, preset, down
  not not_8 (not_8_out, halt);
  and and_8 (and_8_out, not_8_out, LoadUse);
  Adder #(.width(16)) adder_4 (.a(\条件分支成功数 ), .b(\无条件分支数 ), .out(adder_4_out));  // open: cin, cout
  RAM #(.addrWidth(10), .dataWidth(32), .bus("separate"), .Select("high")) ram_1 (
    .addr(MEM_Result[11:2]), .din(MDin), .data(ram_1_data), .str(MemWrite), .clk(CLK),
    .ld(EX_MEM_memtoregout), .clr(RST));  // open: sel
  Shifter #(.width(16), .shift("ll")) shifter_3 (.in(adder_4_out), .\dist (4'b0001), .out(shifter_3_out));
  Counter #(.width(16), .max('hffff), .ongoal("wrap"), .trigger("rising"), .behavior("new")) counter_5 (
    .count(and_8_out), .Q(\LoadUse次数 ), .clk(CLK), .clr(RST));  // open: load, D, carry, preset, down
  MEM_WB MEM_WB (
    .PCin(M_PC), .MemToRegin(EX_MEM_memtoregout), .IRin(MEM_IR), .Jumpin(EX_MEM_jumpout),
    .RegWritein(MEM_RegWrite), .Resultin({MEM_Result[31:2], Choicein, MEM_Result[0]}),
    .Haltin(EX_MEM_haltout), .RMDatain(ram_1_data), .W_in(MEM_W_num), .PCout(WB_PC), .MemToRegout(MemToReg),
    .IRout(WB_IR), .Jumpout(Jump), .RegWriteout(RegWrite), .Resultout(Result), .Haltout(MEM_WB_haltout),
    .RMdataout(MEM_WB_rmdataout), .W_out(W_num), .RST(RST), .EN_H(en), .CLK(CLK), .auipcin(EX_MEM_auipcout),
    .auipcout(auipc), .Luiin(EX_MEM_luiout), .Luiout(lui), .Imm_U_in(EX_MEM_imm_u_out),
    .Imm_U_out(WB_imm32_U), .lhuin(EX_MEM_lhuout), .lhuout(lhuout), .choicein(Choicein),
    .choiceout(MEM_WB_choiceout));
  Adder #(.width(16)) adder_5 (.a(shifter_3_out), .b(\LoadUse次数 ), .out(\插入气泡数 ));  // open: cin, cout
  assign bit_extender_5_out = {{16{1'b0}}, multiplexer_10_out};  // Bit_Extender bit_extender_5
  Multiplexer #(.select(1), .width(16), .disabled("Z"), .enable("false")) multiplexer_10 (
    .in0(MEM_WB_rmdataout[15:0]), .in1(MEM_WB_rmdataout[31:16]), .out(multiplexer_10_out),
    .sel(MEM_WB_choiceout));
  Multiplexer #(.select(1), .width(32), .disabled("Z"), .enable("false")) multiplexer_11 (
    .in0(MEM_WB_rmdataout), .in1(bit_extender_5_out), .out(MDout), .sel(lhuout));
  and and_9 (halt, MEM_WB_haltout, ~Go);  // AND_Gate
  not not_9 (en, halt);
  Multiplexer #(.select(1), .width(32), .disabled("Z"), .enable("false")) multiplexer_12 (
    .in0(Result), .in1(MDout), .out(multiplexer_12_out), .sel(MemToReg));
  Adder #(.width(32)) adder_6 (.a(WB_PC), .b(32'h4), .out(adder_6_out));  // open: cin, cout
  Multiplexer #(.select(1), .width(32), .disabled("Z"), .enable("false")) multiplexer_13 (
    .in0(multiplexer_12_out), .in1(adder_6_out), .out(multiplexer_13_out), .sel(Jump));
  Multiplexer #(.select(1), .width(32), .disabled("Z"), .enable("false")) multiplexer_14 (
    .in0(WB_imm32_U), .in1(adder_7_out), .out(multiplexer_14_out), .sel(auipc));
  Adder #(.width(32)) adder_7 (.a(WB_imm32_U), .b(WB_PC), .out(adder_7_out));  // open: cin, cout
  Multiplexer #(.select(1), .width(32), .disabled("Z"), .enable("false")) multiplexer_15 (
    .in0(multiplexer_13_out), .in1(multiplexer_14_out), .out(RDin), .sel(or_6_out));
  or or_6 (or_6_out, auipc, lui);

  // Other names for the same wires on the sheet: ID_IR (some bits) = ID_funct; ID_OP[4:0] = ID_IR[6:2];
  //   MEM_PC[31:0] = M_PC; MEM_Result[1] = Choicein; WriteBackData[31:0] = RDin

  // Notes on the sheet:
  //   中断源
  //   时空图监测，可删除
  //   中断等待指示
  //   数码管输出
  //   控制位
  //   指令存储器
  //   流水调试日志用
  //   暂停节拍，不能为0
  //   contents of rom_1 (hex, n*v repeats v):
  //   100493 100006f 100493 200913 300993 100006f 100493 200913 300993 100006f 100493 200913 300993
  //   100006f 100493 200913 300993 424000ef 100413 100493 1f49493 900533 2200893 73 24d493 48463 fedff06f
  //   900533 2200893 73 100493 249493 900533 2200893 73 48463 fedff06f 100493 1f49493 900533 2200893 73
  //   4034d493 900533 2200893 73 4044d493 900533 2200893 73 4044d493 900533 2200893 73 4044d493 900533
  //   2200893 73 4044d493 900533 2200893 73 4044d493 900533 2200893 73 4044d493 900533 2200893 73 4044d493
  //   900533 2200893 73 100413 1f41993 41f9d993 433 c00913 300b13 140413 f47413 800293 100313 499993
  //   89e9b3 1300533 2200893 73 406282b3 fe0294e3 140413 f00f93 1f47433 1c41413 800293 100313 49d993
  //   89e9b3 1300533 2200893 73 406282b3 fe0294e3 1c45413 406b0b33 b0463 f95ff06f 2b3 fff2c293 829293
  //   ff2e293 500533 2200893 73 fff00413 493 84a023 140413 448493 84a023 140413 448493 84a023 140413
  //   448493 84a023 140413 448493 84a023 140413 448493 84a023 140413 448493 84a023 140413 448493 84a023
  //   140413 448493 84a023 140413 448493 84a023 140413 448493 84a023 140413 448493 84a023 140413 448493
  //   84a023 140413 448493 84a023 140413 448493 84a023 140413 448493 84a023 140413 448493 140413 433
  //   3c00493 42983 4aa03 149a2b3 28663 134a023 1442023 ffc48493 fe9412e3 800533 2200893 73 440413 3c00493
  //   fc9416e3 3200893 73 13 430497 900533 2200893 73 430497 900533 2200893 73 430497 900533 2200893 73
  //   430497 900533 2200893 73 430497 900533 2200893 73 430497 900533 2200893 73 430497 900533 2200893 73
  //   430497 900533 2200893 73 a00893 73 800e13 fedc04b7 fff00413 1045413 84e4b3 900533 2200893 73 ba984b7
  //   900533 73 76544b7 900533 73 32104b7 900533 73 fffe0e13 fa0e1ee3 a00893 73 313 1000e13 8400493 849493
  //   8348493 400913 891913 490913 849493 8248493 849493 8148493 891913 490913 891913 490913 932023
  //   12484b3 430313 fffe0e13 fe0e18e3 2000e13 313 35483 900533 2200893 73 230313 fffe0e13 fe0e14e3 a00893
  //   73 ff100493 900533 2200893 73 148493 fe04c8e3 a00893 73 a00893 73 413 140413 800533 2200893 73
  //   240413 800533 2200893 73 340413 800533 2200893 73 440413 800533 2200893 73 540413 800533 2200893 73
  //   640413 800533 2200893 73 740413 800533 2200893 73 840413 800533 2200893 2200893 73 8067
  //   戳工具置1进入计数暂停模式，ctrl+k时钟自动运行到对应节拍暂停
  //   ctrl+k关闭时钟连续运行，将控制位置零，进入单步调试模式调试
  //   指令字ID.IR
  //   可计数暂停的时钟源
  //   rs1
  //   rs2
  //   rd
  //   Beq
  //   Bne
  //   MemToReg
  //   MemWrite
  //   AluOP
  //   AluSrcB
  //   RegWrite
  //   转换为字偏移量,所以需要逻辑左移一位
  //   为方便自动评测，需要输出流水线各段保存的PC值，注意是PC不是PC+4，另外ID段寄存器写入信息，Mem段内存写入信息也要输出
  //   数据存储器
endmodule
module \气泡流水线  (
  output RegWrite,
  output MemWrite,
  output [31:0] IF_PC,
  output [31:0] ID_PC,
  output [31:0] EX_PC,
  output [31:0] M_PC,
  output [31:0] WB_PC,
  output [31:0] RDin,
  output [31:0] MDin,
  output [31:0] LedData
);

  wire and_1_out, and_2_out, and_3_out, and_4_out, and_5_out, and_6_out, and_7_out, and_8_out, auipc, beq,
       blt, bne, branch, Choicein, CLK, clock_1_out, comparator_1_eq, comparator_1_lt, comparator_2_eq,
       d_ff_1_q, ecall, en, equal, EX_MEM_auipcout, EX_MEM_haltout, EX_MEM_jumpout, EX_MEM_lhuout,
       EX_MEM_luiout, EX_MEM_memtoregout, EX_RegWrite, Go, halt, ID_EX_alusrcbout, ID_EX_auipcout,
       ID_EX_haltout, ID_EX_lhuout, ID_EX_luiout, ID_EX_memtoregout, ID_EX_memwriteout, ID_EX_s_tpyeout, IR1,
       IR2, IR3, jal, jalr, Jump, less, lhuout, lui, MEM_RegWrite, MEM_WB_choiceout, MEM_WB_haltout,
       MemToReg, nand_1_out, not_1_out, not_2_out, not_3_out, not_4_out, not_5_out, not_6_out, not_7_out,
       not_8_out, or_1_out, or_2_out, or_3_out, or_5_out, or_6_out, RST, W1, W2, W3, \单周期硬布线控制器_1_alu_src ,
       \单周期硬布线控制器_1_auipc , \单周期硬布线控制器_1_beq , \单周期硬布线控制器_1_blt , \单周期硬布线控制器_1_bne , \单周期硬布线控制器_1_jal ,
       \单周期硬布线控制器_1_jalr , \单周期硬布线控制器_1_lhu , \单周期硬布线控制器_1_lui , \单周期硬布线控制器_1_memtoreg ,
       \单周期硬布线控制器_1_memwrite , \单周期硬布线控制器_1_regwrite , \单周期硬布线控制器_1_s_type , \数据相关 ;
  wire [3:0] ID_EX_aluopout, \单周期硬布线控制器_1_alu_op ;
  wire [4:0] EX_W_num, ID_funct, ID_R1_num, ID_R2_num, MEM_W_num, W_num;
  wire [11:0] shifter_1_out;
  wire [12:0] CNT_num;
  wire [15:0] \LoadUse次数 , multiplexer_8_out, \总周期数 , \插入气泡数 , \无条件分支数 , \条件分支成功数 ;
  wire [19:0] shifter_2_out;
  wire [31:0] adder_1_out, adder_2_out, adder_3_out, adder_4_out, adder_5_out, bit_extender_1_out,
       bit_extender_2_out, bit_extender_3_out, bit_extender_4_out, bit_extender_5_out, EX_IR,
       EX_MEM_imm_u_out, EX_MEM_resultout, ID_EX_imm_i_out, ID_EX_imm_s_out, ID_EX_imm_u_out, ID_EX_r1out,
       ID_EX_r2out, ID_IR, IF_IR, imm32_B, imm32_J, jaddress, MDout, MEM_IR, MEM_WB_rmdataout,
       multiplexer_1_out, multiplexer_2_out, multiplexer_3_out, multiplexer_6_out, multiplexer_7_out,
       multiplexer_10_out, multiplexer_11_out, multiplexer_12_out, R1, R2, ram_1_data, Result, WB_imm32_U,
       WB_IR;

  Button \u_总复位  (.out(RST));
  Button _1 (.out(IR1));
  Button _2 (.out(IR2));
  Button _3 (.out(IR3));
  // Probe on \总周期数 
  // Probe on \总周期数 
  Button \u_继续运行  (.out(Go));
  LED #(.active("true")) led_1 (.in(W1));
  LED #(.active("true")) led_2 (.in(W2));
  LED #(.active("true")) led_3 (.in(W3));
  Hex_Digit_Display hex_digit_display_1 (.value(LedData[31:28]));  // open: dp
  // Probe on IF_PC[19:0]
  // RiscV_Probe riscv_probe_1: pin names not known; wires that end beside it: IF_IR
  Hex_Digit_Display hex_digit_display_2 (.value(LedData[23:20]));  // open: dp
  Hex_Digit_Display hex_digit_display_3 (.value(LedData[27:24]));  // open: dp
  // Probe on ID_PC[19:0]
  // RiscV_Probe riscv_probe_2: pin names not known; wires that end beside it: {ID_IR[31], ID_funct[4], ID_IR[29:26], ID_funct[3], ID_IR[24:15], ID_funct[2:0], ID_IR[11:0]}
  Hex_Digit_Display hex_digit_display_4 (.value(LedData[19:16]));  // open: dp
  Hex_Digit_Display hex_digit_display_5 (.value(LedData[15:12]));  // open: dp
  Multiplexer #(.select(1), .width(32), .disabled("Z"), .enable("false")) multiplexer_1 (
    .in0(adder_3_out), .in1(jaddress), .out(multiplexer_1_out), .sel(jalr));
  Adder #(.width(32)) adder_1 (.a(imm32_J), .b(EX_PC), .out(adder_1_out));  // open: cin, cout
  Adder #(.width(32)) adder_2 (.a(imm32_B), .b(EX_PC), .out(adder_2_out));  // open: cin, cout
  Hex_Digit_Display hex_digit_display_6 (.value(LedData[7:4]));  // open: dp
  Hex_Digit_Display hex_digit_display_7 (.value(LedData[11:8]));  // open: dp
  // Probe on EX_PC[19:0]
  // RiscV_Probe riscv_probe_3: pin names not known; wires that end beside it: EX_IR
  Multiplexer #(.select(1), .width(32), .disabled("Z"), .enable("false")) multiplexer_2 (
    .in0(multiplexer_1_out), .in1(adder_1_out), .out(multiplexer_2_out), .sel(jal));
  Multiplexer #(.select(1), .width(32), .disabled("Z"), .enable("false")) multiplexer_3 (
    .in0(multiplexer_2_out), .in1(adder_2_out), .out(multiplexer_3_out), .sel(branch));
  not not_1 (not_1_out, \数据相关 );
  Hex_Digit_Display hex_digit_display_8 (.value(LedData[3:0]));  // open: dp
  Register #(.width(32), .trigger("rising"), .Select("low")) PC (
    .D(multiplexer_3_out), .en(and_1_out), .Q(IF_PC), .clk(CLK), .clr(RST));
  and and_1 (and_1_out, not_1_out, not_2_out);
  not not_2 (not_2_out, halt);
  \数据相关_气泡流水线  \u_数据相关_气泡流水线_1  (
    .ID_R1_num(ID_R1_num), .EX_W_num(EX_W_num), .EX_RegWrite(EX_RegWrite), .ID_R2_num(ID_R2_num),
    .MEM_W_num(MEM_W_num), .MEM_RegWrite(MEM_RegWrite), .\数据相关 (\数据相关 ), .ID_OP(ID_IR[6:2]),
    .ID_Funct(ID_funct));
  // Probe on \总周期数 
  // Probe on M_PC[19:0]
  // RiscV_Probe riscv_probe_4: pin names not known; wires that end beside it: MEM_IR
  // Probe on \总周期数 
  // Probe on \无条件分支数 
  // Probe on \条件分支成功数 
  // Probe on \插入气泡数 
  // Probe on \LoadUse次数 
  // Probe on IF_PC[11:0]
  // Probe on WB_PC[19:0]
  // RiscV_Probe riscv_probe_5: pin names not known; wires that end beside it: WB_IR
  ROM #(.addrWidth(10), .dataWidth(32), .Select("high")) rom_1 (.addr(IF_PC[11:2]), .data(IF_IR));
  Adder #(.width(32)) adder_3 (.a(IF_PC), .b(32'h4), .out(adder_3_out));  // open: cin, cout
  or or_1 (or_1_out, RST, branch, jal, jalr);
  // Probe on EX_PC[11:0]
  // Probe on ID_PC[11:0]
  IF_ID IF_ID (
    .PCin(IF_PC), .IRin(IF_IR), .PCout(ID_PC),
    .IRout({ID_IR[31], ID_funct[4], ID_IR[29:26], ID_funct[3], ID_IR[24:15], ID_funct[2:0], ID_IR[11:0]}),
    .RST(or_1_out), .clk(CLK), .EN(and_2_out));  // open: PridictJumpin, PridictJumpout
  and and_2 (and_2_out, not_3_out, en);
  not not_3 (not_3_out, \数据相关 );
  // Probe on M_PC[11:0]
  D_Flip_Flop #(.trigger("high"), .Pre_Clr_Positions("LEGACY"), .NegatePresetClear("false"), .enable("true"), .NewFFLayout("false")) d_ff_1 (.Q(d_ff_1_q));  // open: clk, D, Qn, preset, en, reset
  // Probe on 13'h68
  // Probe on WB_PC[11:0]
  Comparator #(.width(13), .mode("twosComplement")) comparator_1 (
    .a(CNT_num), .b(13'h68), .eq(comparator_1_eq), .lt(comparator_1_lt));  // open: gt
  Clock #(.highDuration(1), .lowDuration(1)) clock_1 (.out(clock_1_out));
  // RiscV_Probe riscv_probe_6: pin names not known; wires that end beside it: IF_PC, {ID_IR[31], ID_funct[4], ID_IR[29:26], ID_funct[3], ID_IR[24:15], ID_funct[2:0], ID_IR[11:0]}
  nand nand_1 (nand_1_out, d_ff_1_q, comparator_1_eq);
  Counter #(.width(13), .max('h1fff), .ongoal("stay"), .trigger("rising"), .behavior("old")) counter_1 (
    .count(comparator_1_lt), .Q(CNT_num), .clk(clock_1_out));  // open: load, D, carry, clr, preset
  assign CLK = nand_1_out ? clock_1_out : 1'bz;  // Controlled_Buffer controlled_buffer_1
  assign bit_extender_1_out = {{20{ID_IR[31]}}, {ID_IR[31], ID_funct[4], ID_IR[29:26], ID_funct[3], ID_IR[24:20]}};  // Bit_Extender bit_extender_1
  assign bit_extender_2_out = {{20{ID_IR[31]}}, {ID_IR[31], ID_funct[4], ID_IR[29:26], ID_funct[3], ID_IR[11:7]}};  // Bit_Extender bit_extender_2
  Pull_Resistor #(.pull(1)) pull_resistor_1 (.node(CLK));
  \单周期硬布线控制器  \u_单周期硬布线控制器_1  (
    .Funct(ID_funct), .OP(ID_IR[6:2]), .ALU_OP(\单周期硬布线控制器_1_alu_op ), .MemToReg(\单周期硬布线控制器_1_memtoreg ),
    .MemWrite(\单周期硬布线控制器_1_memwrite ), .ALU_SRC(\单周期硬布线控制器_1_alu_src ), .RegWrite(\单周期硬布线控制器_1_regwrite ),
    .ecall(ecall), .S_type(\单周期硬布线控制器_1_s_type ), .Jalr(\单周期硬布线控制器_1_jalr ), .Beq(\单周期硬布线控制器_1_beq ),
    .JAL(\单周期硬布线控制器_1_jal ), .Bne(\单周期硬布线控制器_1_bne ), .in_3(ID_IR[21]), .auipc(\单周期硬布线控制器_1_auipc ),
    .lui(\单周期硬布线控制器_1_lui ), .lhu(\单周期硬布线控制器_1_lhu ), .blt(\单周期硬布线控制器_1_blt ));  // open: uret, CSRRCI, CSRRSI
  Multiplexer #(.select(1), .width(5), .disabled("Z"), .enable("false")) multiplexer_4 (
    .in0(ID_IR[19:15]), .in1(5'b10001), .out(ID_R1_num), .sel(ecall));
  Multiplexer #(.select(1), .width(5), .disabled("Z"), .enable("false")) multiplexer_5 (
    .in0(ID_IR[24:20]), .in1(5'b01010), .out(ID_R2_num), .sel(ecall));
  assign bit_extender_3_out = {{20{shifter_1_out[11]}}, shifter_1_out};  // Bit_Extender bit_extender_3
  Shifter #(.width(12), .shift("ll")) shifter_1 (
    .in({ID_IR[31], ID_IR[7], ID_funct[4], ID_IR[29:26], ID_funct[3], ID_IR[11:8]}), .\dist (4'b0001),
    .out(shifter_1_out));
  assign bit_extender_4_out = {{12{shifter_2_out[19]}}, shifter_2_out};  // Bit_Extender bit_extender_4
  Shifter #(.width(20), .shift("ll")) shifter_2 (
    .in({ID_IR[31], ID_IR[19:15], ID_funct[2:0], ID_IR[20], ID_funct[4], ID_IR[29:26], ID_funct[3], ID_IR[24:21]}),
    .\dist (5'b00001), .out(shifter_2_out));
  Comparator #(.width(32), .mode("twosComplement")) comparator_2 (
    .a(R1), .b(32'h22), .eq(comparator_2_eq));  // open: gt, lt
  not not_4 (not_4_out, comparator_2_eq);
  and and_3 (and_3_out, ecall, comparator_2_eq);
  and and_4 (and_4_out, not_4_out, ecall);
  not not_5 (not_5_out, CLK);
  Regifile regifile_1 (
    .Din(RDin), .Clk(not_5_out), .R1(R1), .R2(R2), .WE(RegWrite), .W_num(W_num), .R1_num(ID_R1_num),
    .R2_num(ID_R2_num));
  Register #(.width(32), .trigger("rising"), .Select("low")) register_1 (
    .D(R2), .en(and_3_out), .Q(LedData), .clk(CLK), .clr(RST));
  or or_2 (or_2_out, \数据相关 , or_1_out);
  ID_EX ID_EX (
    .PCin(ID_PC), .Lhuin(\单周期硬布线控制器_1_lhu ), .Jalrin(\单周期硬布线控制器_1_jalr ),
    .IRin({ID_IR[31], ID_funct[4], ID_IR[29:26], ID_funct[3], ID_IR[24:15], ID_funct[2:0], ID_IR[11:0]}),
    .Jalin(\单周期硬布线控制器_1_jal ), .Beqin(\单周期硬布线控制器_1_beq ), .Imm_I_in(bit_extender_1_out),
    .Bltin(\单周期硬布线控制器_1_blt ), .Imm_S_in(bit_extender_2_out), .Bnein(\单周期硬布线控制器_1_bne ),
    .Imm_B_in(bit_extender_3_out), .MemToRegin(\单周期硬布线控制器_1_memtoreg ), .MemWritein(\单周期硬布线控制器_1_memwrite ),
    .Imm_J_in(bit_extender_4_out), .AluOpin(\单周期硬布线控制器_1_alu_op ),
    .Imm_U_in({ID_IR[31], ID_funct[4], ID_IR[29:26], ID_funct[3], ID_IR[24:15], ID_funct[2:0], {12{1'b0}}}),
    .AluSrcBin(\单周期硬布线控制器_1_alu_src ), .R1in(R1), .RegWritein(\单周期硬布线控制器_1_regwrite ), .R2in(R2),
    .S_Typein(\单周期硬布线控制器_1_s_type ), .haltin(and_4_out), .W_in(ID_IR[11:7]), .PCout(EX_PC),
    .Lhuout(ID_EX_lhuout), .Jalrout(jalr), .IRout(EX_IR), .Jalout(jal), .Beqout(beq),
    .Imm_I_out(ID_EX_imm_i_out), .Bltout(blt), .Imm_S_out(ID_EX_imm_s_out), .Bneout(bne),
    .Imm_B_out(imm32_B), .MemToRegout(ID_EX_memtoregout), .MemWriteout(ID_EX_memwriteout),
    .Imm_J_out(imm32_J), .AluOpout(ID_EX_aluopout), .Imm_U_out(ID_EX_imm_u_out),
    .AluSrcBout(ID_EX_alusrcbout), .R1out(ID_EX_r1out), .RegWriteout(EX_RegWrite), .R2out(ID_EX_r2out),
    .S_Tpyeout(ID_EX_s_tpyeout), .haltout(ID_EX_haltout), .W_out(EX_W_num), .RST(or_2_out), .EN_H(en),
    .CLK(CLK), .Luiin(\单周期硬布线控制器_1_lui ), .Luiout(ID_EX_luiout), .auipcin(\单周期硬布线控制器_1_auipc ),
    .auipcout(ID_EX_auipcout));  // open: R1CHOICEin, R1CHOICEout, R2CHOICEin, R2CHOICEout, PridictJumpin, PridictJumpout
  or or_3 (or_3_out, jal, jalr);
  Multiplexer #(.select(1), .width(32), .disabled("Z"), .enable("false")) multiplexer_6 (
    .in0(ID_EX_imm_i_out), .in1(ID_EX_imm_s_out), .out(multiplexer_6_out), .sel(ID_EX_s_tpyeout));
  Multiplexer #(.select(1), .width(32), .disabled("Z"), .enable("false")) multiplexer_7 (
    .in0(ID_EX_r2out), .in1(multiplexer_6_out), .out(multiplexer_7_out), .sel(ID_EX_alusrcbout));
  ALU alu_1 (
    .X(ID_EX_r1out), .Y(multiplexer_7_out), .AluOP(ID_EX_aluopout), .Equal(equal), .Result(jaddress),
    .out_6(less));  // open: Result_2, out_4
  Counter #(.width(16), .max('hffff), .ongoal("wrap"), .trigger("rising"), .behavior("new")) counter_2 (
    .count(branch), .Q(\条件分支成功数 ), .clk(CLK), .clr(RST));  // open: load, D, carry, preset, down
  and and_5 (and_5_out, blt, less);
  and and_6 (and_6_out, beq, equal);
  not not_6 (not_6_out, equal);
  and and_7 (and_7_out, not_6_out, bne);
  or or_4 (branch, and_5_out, and_6_out, and_7_out);
  or or_5 (or_5_out, jal, jalr);
  Counter #(.width(16), .max('hffff), .ongoal("wrap"), .trigger("rising"), .behavior("new")) counter_3 (
    .count(or_5_out), .Q(\无条件分支数 ), .clk(CLK), .clr(RST));  // open: load, D, carry, preset, down
  EX_MEM EX_MEM (
    .MemToRegin(ID_EX_memtoregout), .PCin(EX_PC), .MemWritein(ID_EX_memwriteout), .IRin(EX_IR),
    .Jumpin(or_3_out), .RegWritein(EX_RegWrite), .Resultin(jaddress), .Haltin(ID_EX_haltout),
    .MDatain(ID_EX_r2out), .W_in(EX_W_num), .MemToRegout(EX_MEM_memtoregout), .PCout(M_PC),
    .MemWriteout(MemWrite), .IRout(MEM_IR), .Jumpout(EX_MEM_jumpout), .RegWriteout(MEM_RegWrite),
    .Resultout({EX_MEM_resultout[31:2], Choicein, EX_MEM_resultout[0]}), .Haltout(EX_MEM_haltout),
    .Mdataout(MDin), .W_out(MEM_W_num), .RST(RST), .EN_H(en), .CLK(CLK), .auipcin(ID_EX_auipcout),
    .auipcout(EX_MEM_auipcout), .Luiin(ID_EX_luiout), .Luiout(EX_MEM_luiout), .Lhuin(ID_EX_lhuout),
    .Lhuout(EX_MEM_lhuout), .Imm_U_in(ID_EX_imm_u_out), .Imm_U_out(EX_MEM_imm_u_out));
  not not_7 (not_7_out, halt);
  Counter #(.width(16), .max('hffff), .ongoal("wrap"), .trigger("rising"), .behavior("new")) counter_4 (
    .count(not_7_out), .Q(\总周期数 ), .clk(CLK), .clr(RST));  // open: load, D, carry, preset, down
  RAM #(.addrWidth(10), .dataWidth(32), .bus("separate"), .Select("high")) ram_1 (
    .addr(EX_MEM_resultout[11:2]), .din(MDin), .data(ram_1_data), .str(MemWrite), .clk(CLK),
    .ld(EX_MEM_memtoregout), .clr(RST));  // open: sel
  not not_8 (not_8_out, halt);
  MEM_WB MEM_WB (
    .PCin(M_PC), .MemToRegin(EX_MEM_memtoregout), .IRin(MEM_IR), .Jumpin(EX_MEM_jumpout),
    .RegWritein(MEM_RegWrite), .Resultin({EX_MEM_resultout[31:2], Choicein, EX_MEM_resultout[0]}),
    .Haltin(EX_MEM_haltout), .RMDatain(ram_1_data), .W_in(MEM_W_num), .PCout(WB_PC), .MemToRegout(MemToReg),
    .IRout(WB_IR), .Jumpout(Jump), .RegWriteout(RegWrite), .Resultout(Result), .Haltout(MEM_WB_haltout),
    .RMdataout(MEM_WB_rmdataout), .W_out(W_num), .RST(RST), .EN_H(en), .CLK(CLK), .auipcin(EX_MEM_auipcout),
    .auipcout(auipc), .Luiin(EX_MEM_luiout), .Luiout(lui), .Imm_U_in(EX_MEM_imm_u_out),
    .Imm_U_out(WB_imm32_U), .lhuin(EX_MEM_lhuout), .lhuout(lhuout), .choicein(Choicein),
    .choiceout(MEM_WB_choiceout));
  and and_8 (and_8_out, not_8_out, \数据相关 );
  Counter #(.width(16), .max('hffff), .ongoal("wrap"), .trigger("rising"), .behavior("new")) counter_5 (
    .count(and_8_out), .Q(\插入气泡数 ), .clk(CLK), .clr(RST));  // open: load, D, carry, preset, down
  Multiplexer #(.select(1), .width(16), .disabled("Z"), .enable("false")) multiplexer_8 (
    .in0(MEM_WB_rmdataout[15:0]), .in1(MEM_WB_rmdataout[31:16]), .out(multiplexer_8_out),
    .sel(MEM_WB_choiceout));
  Multiplexer #(.select(1), .width(32), .disabled("Z"), .enable("false")) multiplexer_9 (
    .in0(MEM_WB_rmdataout), .in1(bit_extender_5_out), .out(MDout), .sel(lhuout));
  assign bit_extender_5_out = {{16{1'b0}}, multiplexer_8_out};  // Bit_Extender bit_extender_5
  and and_9 (halt, MEM_WB_haltout, ~Go);  // AND_Gate
  not not_9 (en, halt);
  Multiplexer #(.select(1), .width(32), .disabled("Z"), .enable("false")) multiplexer_10 (
    .in0(Result), .in1(MDout), .out(multiplexer_10_out), .sel(MemToReg));
  Adder #(.width(32)) adder_4 (.a(WB_PC), .b(32'h4), .out(adder_4_out));  // open: cin, cout
  Multiplexer #(.select(1), .width(32), .disabled("Z"), .enable("false")) multiplexer_11 (
    .in0(multiplexer_10_out), .in1(adder_4_out), .out(multiplexer_11_out), .sel(Jump));
  Adder #(.width(32)) adder_5 (.a(WB_imm32_U), .b(WB_PC), .out(adder_5_out));  // open: cin, cout
  Multiplexer #(.select(1), .width(32), .disabled("Z"), .enable("false")) multiplexer_12 (
    .in0(WB_imm32_U), .in1(adder_5_out), .out(multiplexer_12_out), .sel(auipc));
  or or_6 (or_6_out, auipc, lui);
  Multiplexer #(.select(1), .width(32), .disabled("Z"), .enable("false")) multiplexer_13 (
    .in0(multiplexer_11_out), .in1(multiplexer_12_out), .out(RDin), .sel(or_6_out));

  // Other names for the same wires on the sheet: ID_IR (some bits) = ID_funct; ID_OP[4:0] = ID_IR[6:2];
  //   MEM_PC[31:0] = M_PC

  // Notes on the sheet:
  //   中断源
  //   时空图监测，可删除
  //   中断等待指示
  //   数码管输出
  //   指令存储器
  //   contents of rom_1 (hex, n*v repeats v):
  //   13 430497 900533 2200893 73 430497 900533 2200893 73 430497 900533 2200893 73 430497 900533 2200893
  //   73 430497 900533 2200893 73 430497 900533 2200893 73 430497 900533 2200893 73 430497 900533 2200893
  //   73 a00893 73 800e13 fedc04b7 fff00413 1045413 84e4b3 900533 2200893 73 ba984b7 900533 73 76544b7
  //   900533 73 32104b7 900533 73 fffe0e13 fa0e1ee3 a00893 73 313 1000e13 8400493 849493 8348493 400913
  //   891913 490913 849493 8248493 849493 8148493 891913 490913 891913 490913 932023 12484b3 430313
  //   fffe0e13 fe0e18e3 2000e13 313 35483 900533 2200893 73 230313 fffe0e13 fe0e14e3 a00893 73 ff100493
  //   900533 2200893 73 148493 fe04c8e3 a00893 73
  //   控制位
  //   流水调试日志用
  //   暂停节拍，不能为0
  //   戳工具置1进入计数暂停模式，ctrl+k时钟自动运行到对应节拍暂停
  //   ctrl+k关闭时钟连续运行，将控制位置零，进入单步调试模式调试
  //   指令字ID.IR
  //   rs1
  //   rs2
  //   rd
  //   可计数暂停的时钟源
  //   Beq
  //   Bne
  //   MemToReg
  //   MemWrite
  //   AluOP
  //   AluSrcB
  //   RegWrite
  //   转换为字偏移量,所以需要逻辑左移一位
  //   为方便自动评测，需要输出流水线各段保存的PC值，注意是PC不是PC+4，另外ID段寄存器写入信息，Mem段内存写入信息也要输出
  //   数据存储器
endmodule

module \中断按键参考电路  (
  input  \同步清零信号 ,
  output \与中断屏蔽位与 
);

  wire \_1号中断_out , and_1_out, clock_1_out, d_ff_1_q, or_1_out, or_2_out;

  Clock #(.highDuration(1), .lowDuration(1)) clock_1 (.out(clock_1_out));
  Button \_1号中断  (.out(\_1号中断_out ));
  or or_1 (or_1_out, \与中断屏蔽位与 , d_ff_1_q);
  LED #(.active("true")) \_1号中断等待指示灯  (.in(or_1_out));
  D_Flip_Flop #(.trigger("rising"), .Pre_Clr_Positions("LEGACY"), .NegatePresetClear("false"), .enable("true"), .NewFFLayout("false")) d_ff_1 (
    .clk(\_1号中断_out ), .D(1'b1), .Q(d_ff_1_q), .reset(\与中断屏蔽位与 ));  // open: Qn, preset, en
  or or_2 (or_2_out, d_ff_1_q, \与中断屏蔽位与 );
  and and_1 (and_1_out, or_2_out, ~\同步清零信号 );  // AND_Gate
  D_Flip_Flop #(.trigger("rising"), .Pre_Clr_Positions("LEGACY"), .NegatePresetClear("false"), .enable("true"), .NewFFLayout("false")) IR1 (
    .clk(clock_1_out), .D(and_1_out), .Q(\与中断屏蔽位与 ));  // open: Qn, preset, en, reset

  // Notes on the sheet:
  //   中断信号采样参考电路
  //   Reset 
endmodule

module \单周期_单级中断  (
  input  IR1,
  input  IR2,
  input  IR3,
  output RegWrite,
  output MemWrite,
  output [31:0] PC,
  output [31:0] IR,
  output [31:0] RDin,
  output [31:0] MDin,
  output [31:0] LedData
);

  wire AluSrcB, and_1_out, and_2_out, and_3_out, and_4_out, and_5_out, and_7_out, and_8_out, and_9_out,
       auipc, beq, blt, bne, ChoiceForLhu, CLK, clock_1_out, comparator_1_eq, comparator_2_eq,
       comparator_3_eq, comparator_4_eq, comparator_5_eq, comparator_6_eq, comparator_6_lt, d_ff_1_q,
       d_ff_2_q, d_ff_3_q, d_ff_4_q, demultiplexer_1_out1, demultiplexer_1_out2, demultiplexer_1_out3, ecall,
       equal, Go, halt, IE_q, Interr, InterrEN, Interrupt1, Interrupt2, Interrupt3, IR1_t, IR2_t, IR3_t, IRA,
       IRB, IRC, jal, jalr, Jump, less, lhu, lui, MemToReg, nand_1_out, not_1_out, not_2_out, not_3_out,
       not_4_out, not_5_out, not_6_out, or_1_out, or_2_out, or_7_out, or_11_out, or_12_out, or_13_out,
       or_14_out, pull_resistor_1_node, pull_resistor_2_node, pull_resistor_3_node, RST, S_type, uret, uret1,
       uret2, uret3, W1, W2, W3;
  wire [1:0] priority_encoder_1_out, retReg_q;
  wire [3:0] AluOP;
  wire [4:0] multiplexer_6_out, multiplexer_8_out;
  wire [11:0] imm12_B, multiplexer_12_out;
  wire [12:0] CNT_num;
  wire [15:0] multiplexer_15_out, \总周期数 ;
  wire [19:0] imm20_J;
  wire [31:0] adder_1_out, adder_2_out, adder_4_out, bit_extender_1_out, bit_extender_2_out,
       bit_extender_3_out, bit_extender_4_out, EPC, InterrAddr, MDout, multiplexer_1_out, multiplexer_2_out,
       multiplexer_4_out, multiplexer_5_out, multiplexer_7_out, multiplexer_9_out, multiplexer_10_out,
       multiplexer_14_out, nextPC, PC_4, R1, ram_1_data, Result;

  Button \u_继续运行  (.out(Go));
  Button _1 (.out(IRA));
  Button _2 (.out(IRB));
  Button _3 (.out(IRC));
  not not_1 (not_1_out, equal);
  LED #(.active("true")) led_1 (.in(W1));
  LED #(.active("true")) led_2 (.in(W2));
  LED #(.active("true")) led_3 (.in(W3));
  and and_1 (and_1_out, blt, less);
  and and_2 (and_2_out, beq, equal);
  and and_3 (and_3_out, not_1_out, bne);
  assign bit_extender_1_out = {{12{imm20_J[19]}}, imm20_J};  // Bit_Extender bit_extender_1
  assign bit_extender_2_out = {{20{imm12_B[11]}}, imm12_B};  // Bit_Extender bit_extender_2
  Hex_Digit_Display hex_digit_display_1 (.value(LedData[31:28]));  // open: dp
  Comparator #(.width(16), .mode("twosComplement")) comparator_1 (
    .a(16'h23b), .b(\总周期数 ), .eq(comparator_1_eq));  // open: gt, lt
  or or_1 (or_1_out, comparator_1_eq, comparator_2_eq);
  Comparator #(.width(16), .mode("twosComplement")) comparator_2 (
    .a(\总周期数 ), .b(16'h1), .eq(comparator_2_eq));  // open: gt, lt
  Comparator #(.width(16), .mode("twosComplement")) comparator_3 (
    .a(\总周期数 ), .b(16'h4), .eq(comparator_3_eq));  // open: gt, lt
  Comparator #(.width(16), .mode("twosComplement")) comparator_4 (
    .a(\总周期数 ), .b(16'h7), .eq(comparator_4_eq));  // open: gt, lt
  or or_2 (or_2_out, and_1_out, and_2_out, and_3_out);
  Multiplexer #(.select(1), .width(32), .disabled("Z"), .enable("false")) multiplexer_1 (
    .in0(PC_4), .in1({Result[31:2], ChoiceForLhu, Result[0]}), .out(multiplexer_1_out), .sel(jalr));
  Adder #(.width(32)) adder_1 (.a(bit_extender_1_out), .b(PC), .out(adder_1_out));  // open: cin, cout
  Adder #(.width(32)) adder_2 (.a(bit_extender_2_out), .b(PC), .out(adder_2_out));  // open: cin, cout
  Hex_Digit_Display hex_digit_display_2 (.value(LedData[27:24]));  // open: dp
  Hex_Digit_Display hex_digit_display_3 (.value(LedData[23:20]));  // open: dp
  Button Reset (.out(RST));
  Pull_Resistor #(.pull(0)) pull_resistor_1 (.node(pull_resistor_1_node));
  assign pull_resistor_1_node = or_1_out ? ~CLK : 1'bz;  // Controlled_Inverter controlled_inverter_1
  Pull_Resistor #(.pull(0)) pull_resistor_2 (.node(pull_resistor_2_node));
  assign pull_resistor_2_node = comparator_3_eq ? ~CLK : 1'bz;  // Controlled_Inverter controlled_inverter_2
  Pull_Resistor #(.pull(0)) pull_resistor_3 (.node(pull_resistor_3_node));
  assign pull_resistor_3_node = comparator_4_eq ? ~CLK : 1'bz;  // Controlled_Inverter controlled_inverter_3
  Multiplexer #(.select(1), .width(32), .disabled("Z"), .enable("false")) multiplexer_2 (
    .in0(multiplexer_1_out), .in1(adder_1_out), .out(multiplexer_2_out), .sel(jal));
  Comparator #(.width(32), .mode("twosComplement")) comparator_5 (
    .a(R1), .b(32'h22), .eq(comparator_5_eq));  // open: gt, lt
  not not_2 (not_2_out, comparator_5_eq);
  Hex_Digit_Display hex_digit_display_4 (.value(LedData[19:16]));  // open: dp
  Hex_Digit_Display hex_digit_display_5 (.value(LedData[15:12]));  // open: dp
  Multiplexer #(.select(1), .width(32), .disabled("Z"), .enable("false")) multiplexer_3 (
    .in0(multiplexer_2_out), .in1(adder_2_out), .out(nextPC), .sel(or_2_out));
  Multiplexer #(.select(1), .width(32), .disabled("Z"), .enable("false")) multiplexer_4 (
    .in0(nextPC), .in1(InterrAddr), .out(multiplexer_4_out), .sel(InterrEN));
  and and_4 (and_4_out, ecall, comparator_5_eq);
  and and_5 (and_5_out, not_2_out, ecall);
  Hex_Digit_Display hex_digit_display_6 (.value(LedData[11:8]));  // open: dp
  Hex_Digit_Display hex_digit_display_7 (.value(LedData[7:4]));  // open: dp
  // Probe on \总周期数 
  Multiplexer #(.select(1), .width(32), .disabled("Z"), .enable("false")) multiplexer_5 (
    .in0(multiplexer_4_out), .in1(EPC), .out(multiplexer_5_out), .sel(uret));
  Register #(.width(32), .trigger("rising"), .Select("low")) register_1 (
    .D(MDin), .en(and_4_out), .Q(LedData), .clk(CLK), .clr(RST));
  and and_6 (halt, and_5_out, not_3_out);
  not not_3 (not_3_out, Go);
  Hex_Digit_Display hex_digit_display_8 (.value(LedData[3:0]));  // open: dp
  Register #(.width(32), .trigger("rising"), .Select("low")) u_PC (
    .D(multiplexer_5_out), .en(not_4_out), .Q(PC), .clk(CLK), .clr(RST));
  not not_4 (not_4_out, halt);
  not not_5 (not_5_out, halt);
  or or_3 (IR1_t, IR1, IRA);
  // RiscV_Probe riscv_probe_1: pin names not known; wires that end beside it: IR
  Counter #(.width(16), .max('hffff), .ongoal("wrap"), .trigger("rising"), .behavior("new")) counter_1 (
    .count(not_5_out), .Q(\总周期数 ), .clk(CLK), .clr(RST));  // open: load, D, carry, preset, down
  or or_4 (IR2_t, IR2, IRB);
  ROM #(.addrWidth(10), .dataWidth(32), .Select("high")) rom_1 (.addr(PC[11:2]), .data(IR));
  Adder #(.width(32)) adder_3 (.a(PC), .b(32'h4), .out(PC_4));  // open: cin, cout
  or or_5 (Jump, jal, jalr);
  or or_6 (IR3_t, IR3, IRC);
  \单周期硬布线控制器  \u_单周期硬布线控制器_1  (
    .Funct({IR[30], IR[25], IR[14:12]}), .OP(IR[6:2]), .ALU_OP(AluOP), .MemToReg(MemToReg),
    .MemWrite(MemWrite), .ALU_SRC(AluSrcB), .RegWrite(RegWrite), .ecall(ecall), .S_type(S_type), .Jalr(jalr),
    .Beq(beq), .JAL(jal), .Bne(bne), .in_3(IR[21]), .uret(uret), .auipc(auipc), .lui(lui), .lhu(lhu),
    .blt(blt));  // open: CSRRCI, CSRRSI
  Multiplexer #(.select(1), .width(5), .disabled("Z"), .enable("false")) multiplexer_6 (
    .in0(IR[24:20]), .in1(5'b01010), .out(multiplexer_6_out), .sel(ecall));
  Multiplexer #(.select(1), .width(32), .disabled("Z"), .enable("false")) multiplexer_7 (
    .in0({Result[31:2], ChoiceForLhu, Result[0]}), .in1(MDout), .out(multiplexer_7_out), .sel(MemToReg));
  Multiplexer #(.select(1), .width(5), .disabled("Z"), .enable("false")) multiplexer_8 (
    .in0(IR[19:15]), .in1(5'b10001), .out(multiplexer_8_out), .sel(ecall));
  Shifter #(.width(12), .shift("ll")) shifter_1 (
    .in({IR[31], IR[7], IR[30:25], IR[11:8]}), .\dist (4'b0001), .out(imm12_B));
  Shifter #(.width(20), .shift("ll")) shifter_2 (
    .in({IR[31], IR[19:12], IR[20], IR[30:21]}), .\dist (5'b00001), .out(imm20_J));
  Multiplexer #(.select(1), .width(32), .disabled("Z"), .enable("false")) multiplexer_9 (
    .in0(multiplexer_7_out), .in1(PC_4), .out(multiplexer_9_out), .sel(Jump));
  Adder #(.width(32)) adder_4 (.a({IR[31:12], {12{1'b0}}}), .b(PC), .out(adder_4_out));  // open: cin, cout
  \中断按键参考电路  \u_中断按键参考电路_1  ();  // open: 与中断屏蔽位与, 同步清零信号
  Multiplexer #(.select(1), .width(32), .disabled("Z"), .enable("false")) multiplexer_10 (
    .in0({IR[31:12], {12{1'b0}}}), .in1(adder_4_out), .out(multiplexer_10_out), .sel(auipc));
  or or_7 (or_7_out, auipc, lui);
  or or_8 (W1, Interrupt1, d_ff_1_q);
  Multiplexer #(.select(1), .width(32), .disabled("Z"), .enable("false")) multiplexer_11 (
    .in0(multiplexer_9_out), .in1(multiplexer_10_out), .out(RDin), .sel(or_7_out));
  D_Flip_Flop #(.trigger("rising"), .Pre_Clr_Positions("LEGACY"), .NegatePresetClear("false"), .enable("true"), .NewFFLayout("false")) d_ff_1 (
    .clk(IR1_t), .D(1'b1), .Q(d_ff_1_q), .reset(Interrupt1));  // open: Qn, preset, en
  D_Flip_Flop #(.trigger("rising"), .Pre_Clr_Positions("LEGACY"), .NegatePresetClear("false"), .enable("true"), .NewFFLayout("false")) d_ff_2 (
    .clk(IR2_t), .D(1'b1), .Q(d_ff_2_q), .reset(Interrupt2));  // open: Qn, preset, en
  or or_9 (W2, Interrupt2, d_ff_2_q);
  D_Flip_Flop #(.trigger("rising"), .Pre_Clr_Positions("LEGACY"), .NegatePresetClear("false"), .enable("true"), .NewFFLayout("false")) d_ff_3 (
    .clk(IR3_t), .D(1'b1), .Q(d_ff_3_q), .reset(Interrupt3));  // open: Qn, preset, en
  or or_10 (W3, Interrupt3, d_ff_3_q);
  Priority_Encoder #(.select(2), .disabled("Z")) priority_encoder_1 (
    .in0(1'b0), .in1(Interrupt1), .in2(Interrupt2), .in3(Interrupt3), .out(priority_encoder_1_out),
    .gs(Interr));  // open: en_out, en_in
  Regifile regifile_1 (
    .Din(RDin), .Clk(CLK), .R1(R1), .R2(MDin), .WE(RegWrite), .W_num(IR[11:7]), .R1_num(multiplexer_8_out),
    .R2_num(multiplexer_6_out));
  or or_11 (or_11_out, d_ff_1_q, Interrupt1);
  or or_12 (or_12_out, d_ff_2_q, Interrupt2);
  or or_13 (or_13_out, d_ff_3_q, Interrupt3);
  D_Flip_Flop #(.trigger("high"), .Pre_Clr_Positions("LEGACY"), .NegatePresetClear("false"), .enable("true"), .NewFFLayout("false")) d_ff_4 (.Q(d_ff_4_q));  // open: clk, D, Qn, preset, en, reset
  // Probe on 13'hc
  Multiplexer #(.select(1), .width(12), .disabled("Z"), .enable("false")) multiplexer_12 (
    .in0(IR[31:20]), .in1({IR[31:25], IR[11:7]}), .out(multiplexer_12_out), .sel(S_type));
  assign bit_extender_3_out = {{20{multiplexer_12_out[11]}}, multiplexer_12_out};  // Bit_Extender bit_extender_3
  and and_7 (and_7_out, or_11_out, ~uret1);  // AND_Gate
  and and_8 (and_8_out, or_12_out, ~uret2);  // AND_Gate
  and and_9 (and_9_out, or_13_out, ~uret3);  // AND_Gate
  Multiplexer #(.select(2), .width(32), .disabled("Z"), .enable("false")) multiplexer_13 (
    .in1(32'h30ac), .in2(32'h3150), .in3(32'h31f4), .out(InterrAddr), .sel(priority_encoder_1_out));  // open: in0
  Comparator #(.width(13), .mode("twosComplement")) comparator_6 (
    .a(CNT_num), .b(13'hc), .eq(comparator_6_eq), .lt(comparator_6_lt));  // open: gt
  Clock #(.highDuration(1), .lowDuration(1)) clock_1 (.out(clock_1_out));
  Multiplexer #(.select(1), .width(32), .disabled("Z"), .enable("false")) multiplexer_14 (
    .in0(MDin), .in1(bit_extender_3_out), .out(multiplexer_14_out), .sel(AluSrcB));
  D_Flip_Flop #(.trigger("rising"), .Pre_Clr_Positions("LEGACY"), .NegatePresetClear("false"), .enable("true"), .NewFFLayout("false")) u_IR1 (
    .clk(CLK), .D(and_7_out), .Q(Interrupt1));  // open: Qn, preset, en, reset
  D_Flip_Flop #(.trigger("rising"), .Pre_Clr_Positions("LEGACY"), .NegatePresetClear("false"), .enable("true"), .NewFFLayout("false")) u_IR2 (
    .clk(CLK), .D(and_8_out), .Q(Interrupt2));  // open: Qn, preset, en, reset
  D_Flip_Flop #(.trigger("rising"), .Pre_Clr_Positions("LEGACY"), .NegatePresetClear("false"), .enable("true"), .NewFFLayout("false")) u_IR3 (
    .clk(CLK), .D(and_9_out), .Q(Interrupt3));  // open: Qn, preset, en, reset
  Register #(.width(2), .trigger("rising"), .Select("low")) retReg (
    .D(priority_encoder_1_out), .en(InterrEN), .Q(retReg_q), .clk(CLK));  // open: clr
  Counter #(.width(13), .max('h1fff), .ongoal("stay"), .trigger("rising"), .behavior("old")) counter_2 (
    .count(comparator_6_lt), .Q(CNT_num), .clk(clock_1_out));  // open: load, D, carry, clr, preset
  Register #(.width(1), .trigger("rising"), .Select("low")) IE (
    .D(InterrEN), .en(or_14_out), .Q(IE_q), .clk(CLK));  // open: clr
  or or_14 (or_14_out, InterrEN, uret);
  Register #(.width(32), .trigger("rising"), .Select("low")) u_EPC (
    .D(nextPC), .en(InterrEN), .Q(EPC), .clk(CLK));  // open: clr
  ALU alu_1 (
    .X(R1), .Y(multiplexer_14_out), .AluOP(AluOP), .Equal(equal),
    .Result({Result[31:2], ChoiceForLhu, Result[0]}), .out_6(less));  // open: Result_2, out_4
  Demultiplexer #(.select(2), .width(1), .tristate("false"), .disabled("Z"), .enable("false")) demultiplexer_1 (
    .out1(demultiplexer_1_out1), .out2(demultiplexer_1_out2), .out3(demultiplexer_1_out3), .in(1'b1),
    .sel(retReg_q));  // open: out0
  nand nand_1 (nand_1_out, d_ff_4_q, comparator_6_eq);
  not not_6 (not_6_out, IE_q);
  and and_10 (InterrEN, not_6_out, Interr);
  and and_11 (uret1, uret, demultiplexer_1_out1);
  and and_12 (uret2, demultiplexer_1_out2, uret);
  and and_13 (uret3, demultiplexer_1_out3, uret);
  assign CLK = nand_1_out ? clock_1_out : 1'bz;  // Controlled_Buffer controlled_buffer_1
  Pull_Resistor #(.pull(1)) pull_resistor_4 (.node(CLK));
  RAM #(.addrWidth(10), .dataWidth(32), .bus("separate"), .Select("high")) ram_1 (
    .addr(Result[11:2]), .din(MDin), .data(ram_1_data), .str(MemWrite), .clk(CLK), .ld(MemToReg), .clr(RST));  // open: sel
  Multiplexer #(.select(1), .width(16), .disabled("Z"), .enable("false")) multiplexer_15 (
    .in0(ram_1_data[15:0]), .in1(ram_1_data[31:16]), .out(multiplexer_15_out), .sel(ChoiceForLhu));
  assign bit_extender_4_out = {{16{1'b0}}, multiplexer_15_out};  // Bit_Extender bit_extender_4
  Multiplexer #(.select(1), .width(32), .disabled("Z"), .enable("false")) multiplexer_16 (
    .in0(ram_1_data), .in1(bit_extender_4_out), .out(MDout), .sel(lhu));

  // Other names for the same wires on the sheet: imm12_S[11:0] = {IR[31:25], IR[11:7]}; imm32_U[31:12] = IR[31:12];
  //   imm12_I[11:0] = IR[31:20]; R2[31:0] = MDin; Result[1] = ChoiceForLhu

  // Notes on the sheet:
  //   中断源
  //   中断等待指示
  //   总复位信号应将除ROM以外所有存储组件全部清零
  //   单级中断测试信号模拟器
  //   数码管输出
  //   数码管输出应该用寄存器锁存，否则显示数据只能一闪而过
  //   指令存储器
  //   指令字
  //   contents of rom_1 (hex, n*v repeats v):
  //   7d000113 100413 1f41993 41f9d993 433 c00913 800b13 140413 f47413 800293 100313 499993 89e9b3 1300533
  //   2200893 73 406282b3 fe0294e3 140413 f00f93 1f47433 1c41413 800293 100313 49d993 89e9b3 1300533
  //   2200893 73 406282b3 fe0294e3 1c45413 406b0b33 b0463 f95ff06f 2b3 fff2c293 1029293 fff2e293 500533
  //   2200893 73 f5dff06f 1112023 410113 a12023 410113 812023 410113 1312023 410113 1412023 410113 1512023
  //   410113 1612023 410113 100b13 300a13 100a93 1600433 441413 14469b3 1300533 2200893 73 fe0416e3
  //   415a0a33 fe0a10e3 ffc10113 12b03 ffc10113 12a83 ffc10113 12a03 ffc10113 12983 ffc10113 12403
  //   ffc10113 12503 ffc10113 12883 200073 1112023 410113 a12023 410113 812023 410113 1312023 410113
  //   1412023 410113 1512023 410113 1612023 410113 200b13 300a13 100a93 1600433 441413 14469b3 1300533
  //   2200893 73 fe0416e3 415a0a33 fe0a10e3 ffc10113 12b03 ffc10113 12a83 ffc10113 12a03 ffc10113 12983
  //   ffc10113 12403 ffc10113 12503 ffc10113 12883 200073 1112023 410113 a12023 410113 812023 410113
  //   1312023 410113 1412023 410113 1512023 410113 1612023 410113 300b13 300a13 100a93 1600433 441413
  //   14469b3 1300533 2200893 73 fe0416e3 415a0a33 fe0a10e3 ffc10113 12b03 ffc10113 12a83 ffc10113 12a03
  //   ffc10113 12983 ffc10113 12403 ffc10113 12503 ffc10113 12883 200073
  //   rs1
  //   rs2
  //   rd
  //   Beq
  //   Bne
  //   MemToReg
  //   MemWrite
  //   AluOP
  //   AluSrcB
  //   RegWrite
  //   转换为字偏移量,所以需要逻辑左移一位
  //   为方便自动评测，需要输出PC，IR，寄存器堆写如数据RDin
  //   RAM写使能MemWrite、RAM写入数据MDin等信号
  //   控制位
  //   暂停节拍，不能为0
  //   Reset 
  //   戳工具置1进入计数暂停模式，ctrl+k时钟自动运行到对应节拍暂停
  //   ctrl+k关闭时钟连续运行，将控制位置零，进入单步调试模式调试
  //   Reset 
  //   Reset 
  //   可计数暂停的时钟源
  //   数据存储器
endmodule

module \单周期_多级中断  (
  input  IR1,
  input  IR2,
  input  IR3,
  output RegWrite,
  output MemWrite,
  output [31:0] PC,
  output [31:0] IR,
  output [31:0] RDin,
  output [31:0] MDin,
  output [31:0] LedData
);

  wire AluSrcB, and_1_out, and_2_out, and_3_out, and_4_out, and_5_out, and_8_out, and_12_out, and_13_out,
       and_14_out, auipc, beq, blt, bne, ChoiceForLhu, CLK, clock_1_out, comparator_1_eq, comparator_2_eq,
       comparator_3_eq, comparator_4_eq, comparator_5_eq, comparator_6_eq, comparator_7_eq, comparator_8_eq,
       comparator_8_lt, CSRRCI, CSRRSI, d_ff_1_q, d_ff_2_q, d_ff_3_q, d_ff_4_q, demultiplexer_1_out1,
       demultiplexer_1_out2, demultiplexer_1_out3, demultiplexer_2_out1, demultiplexer_2_out2,
       demultiplexer_2_out3, demultiplexer_3_out0, demultiplexer_3_out1, demultiplexer_3_out2, ecall, equal,
       Go, halt, Interr, InterrEN, Interrupt1, Interrupt2, Interrupt3, IR1_t, IR2_t, IR3_t, IRA, IRB, IRC,
       jal, jalr, Jump, less, lhu, lui, MemToReg, nand_1_out, not_1_out, not_2_out, not_3_out, not_4_out,
       not_5_out, or_1_out, or_2_out, or_3_out, or_6_out, or_12_out, or_13_out, or_14_out, or_15_out,
       or_16_out, priority_encoder_1_gs, RST, S_type, shield, uret, uret1, uret2, uret3, W1, W2, W3;
  wire [1:0] counter_3_q, InterrNum, InterrPreNum, IR1_2_q, IR2_2_q, IR3_2_q;
  wire [3:0] AluOP;
  wire [4:0] multiplexer_7_out, multiplexer_9_out;
  wire [11:0] imm12_B, multiplexer_13_out;
  wire [12:0] CNT_num;
  wire [15:0] multiplexer_17_out, \总周期数 ;
  wire [19:0] imm20_J;
  wire [31:0] adder_1_out, adder_2_out, adder_4_out, bit_extender_1_out, bit_extender_2_out,
       bit_extender_3_out, bit_extender_4_out, EPC, EPC1_q, EPC2_q, EPC3_q, InterrAddr, MDout,
       multiplexer_1_out, multiplexer_2_out, multiplexer_4_out, multiplexer_5_out, multiplexer_8_out,
       multiplexer_10_out, multiplexer_11_out, multiplexer_15_out, nextPC, PC_4, R1, ram_1_data, Result;

  Button \u_继续运行  (.out(Go));
  Button _1 ();  // open: out
  Button _2 ();  // open: out
  Button _3 ();  // open: out
  LED #(.active("true")) led_1 (.in(W1));
  LED #(.active("true")) led_2 (.in(W2));
  LED #(.active("true")) led_3 (.in(W3));
  not not_1 (not_1_out, equal);
  Hex_Digit_Display hex_digit_display_1 (.value(LedData[31:28]));  // open: dp
  Comparator #(.width(16), .mode("twosComplement")) comparator_1 (
    .a(\总周期数 ), .b(16'h7), .eq(comparator_1_eq));  // open: gt, lt
  Comparator #(.width(16), .mode("twosComplement")) comparator_2 (
    .a(\总周期数 ), .b(16'h241), .eq(comparator_2_eq));  // open: gt, lt
  and and_1 (and_1_out, blt, less);
  and and_2 (and_2_out, beq, equal);
  and and_3 (and_3_out, not_1_out, bne);
  assign bit_extender_1_out = {{12{imm20_J[19]}}, imm20_J};  // Bit_Extender bit_extender_1
  assign bit_extender_2_out = {{20{imm12_B[11]}}, imm12_B};  // Bit_Extender bit_extender_2
  Hex_Digit_Display hex_digit_display_2 (.value(LedData[23:20]));  // open: dp
  Hex_Digit_Display hex_digit_display_3 (.value(LedData[27:24]));  // open: dp
  Comparator #(.width(16), .mode("twosComplement")) comparator_3 (
    .a(16'h258), .b(\总周期数 ), .eq(comparator_3_eq));  // open: gt, lt
  or or_1 (or_1_out, comparator_3_eq, comparator_4_eq);
  Comparator #(.width(16), .mode("twosComplement")) comparator_4 (
    .a(\总周期数 ), .b(16'h1), .eq(comparator_4_eq));  // open: gt, lt
  Comparator #(.width(16), .mode("twosComplement")) comparator_5 (
    .a(\总周期数 ), .b(16'h4), .eq(comparator_5_eq));  // open: gt, lt
  or or_2 (or_2_out, comparator_1_eq, comparator_2_eq);
  or or_3 (or_3_out, and_1_out, and_2_out, and_3_out);
  Multiplexer #(.select(1), .width(32), .disabled("Z"), .enable("false")) multiplexer_1 (
    .in0(PC_4), .in1({Result[31:2], ChoiceForLhu, Result[0]}), .out(multiplexer_1_out), .sel(jalr));
  Adder #(.width(32)) adder_1 (.a(bit_extender_1_out), .b(PC), .out(adder_1_out));  // open: cin, cout
  Adder #(.width(32)) adder_2 (.a(bit_extender_2_out), .b(PC), .out(adder_2_out));  // open: cin, cout
  Hex_Digit_Display hex_digit_display_4 (.value(LedData[15:12]));  // open: dp
  Hex_Digit_Display hex_digit_display_5 (.value(LedData[19:16]));  // open: dp
  Pull_Resistor #(.pull(0)) pull_resistor_1 (.node(IRA));
  assign IRA = or_1_out ? ~CLK : 1'bz;  // Controlled_Inverter controlled_inverter_1
  Pull_Resistor #(.pull(0)) pull_resistor_2 (.node(IRB));
  assign IRB = comparator_5_eq ? ~CLK : 1'bz;  // Controlled_Inverter controlled_inverter_2
  Pull_Resistor #(.pull(0)) pull_resistor_3 (.node(IRC));
  assign IRC = or_2_out ? ~CLK : 1'bz;  // Controlled_Inverter controlled_inverter_3
  Multiplexer #(.select(1), .width(32), .disabled("Z"), .enable("false")) multiplexer_2 (
    .in0(multiplexer_1_out), .in1(adder_1_out), .out(multiplexer_2_out), .sel(jal));
  Comparator #(.width(32), .mode("twosComplement")) comparator_6 (
    .a(R1), .b(32'h22), .eq(comparator_6_eq));  // open: gt, lt
  Hex_Digit_Display hex_digit_display_6 (.value(LedData[7:4]));  // open: dp
  Hex_Digit_Display hex_digit_display_7 (.value(LedData[11:8]));  // open: dp
  // Probe on \总周期数 
  Multiplexer #(.select(1), .width(32), .disabled("Z"), .enable("false")) multiplexer_3 (
    .in0(multiplexer_2_out), .in1(adder_2_out), .out(nextPC), .sel(or_3_out));
  not not_2 (not_2_out, comparator_6_eq);
  and and_4 (and_4_out, not_2_out, ecall);
  Hex_Digit_Display hex_digit_display_8 (.value(LedData[3:0]));  // open: dp
  Multiplexer #(.select(1), .width(32), .disabled("Z"), .enable("false")) multiplexer_4 (
    .in0(nextPC), .in1(InterrAddr), .out(multiplexer_4_out), .sel(Interr));
  Multiplexer #(.select(1), .width(32), .disabled("Z"), .enable("false")) multiplexer_5 (
    .in0(multiplexer_4_out), .in1(EPC), .out(multiplexer_5_out), .sel(uret));
  and and_5 (and_5_out, ecall, comparator_6_eq);
  not not_3 (not_3_out, Go);
  Register #(.width(32), .trigger("rising"), .Select("low")) u_PC (
    .D(multiplexer_5_out), .en(not_4_out), .Q(PC), .clk(CLK), .clr(RST));
  not not_4 (not_4_out, halt);
  Register #(.width(32), .trigger("rising"), .Select("low")) register_1 (
    .D(MDin), .en(and_5_out), .Q(LedData), .clk(CLK), .clr(RST));
  and and_6 (halt, and_4_out, not_3_out);
  or or_4 (IR1_t, IR1, IRA);
  Button Reset (.out(RST));
  Priority_Encoder #(.select(2), .disabled("Z")) priority_encoder_1 (
    .in0(1'b0), .in1(Interrupt1), .in2(Interrupt2), .in3(Interrupt3), .out(InterrNum),
    .gs(priority_encoder_1_gs));  // open: en_out, en_in
  Comparator #(.width(16), .mode("twosComplement")) comparator_7 (
    .a(\总周期数 ), .b({16{1'b0}}), .eq(comparator_7_eq));  // open: gt, lt
  or or_5 (IR2_t, IR2, IRB);
  not not_5 (not_5_out, halt);
  Counter #(.width(16), .max('hffff), .ongoal("wrap"), .trigger("rising"), .behavior("new")) counter_1 (
    .count(not_5_out), .Q(\总周期数 ), .clk(CLK), .clr(RST));  // open: load, D, carry, preset, down
  Multiplexer #(.select(2), .width(32), .disabled("Z"), .enable("false")) multiplexer_6 (
    .in1(32'h30ac), .in2(32'h3158), .in3(32'h3204), .out(InterrAddr), .sel(InterrNum));  // open: in0
  and and_7 (Interr, priority_encoder_1_gs, InterrEN, shield);
  and and_8 (and_8_out, ~Interr, ~CSRRCI);  // AND_Gate
  or or_6 (or_6_out, CSRRCI, CSRRSI, Interr, uret, comparator_7_eq);
  // RiscV_Probe riscv_probe_1: pin names not known; wires that end beside it: IR
  ROM #(.addrWidth(10), .dataWidth(32), .Select("high")) rom_1 (.addr(PC[11:2]), .data(IR));
  Adder #(.width(32)) adder_3 (.a(PC), .b(32'h4), .out(PC_4));  // open: cin, cout
  Demultiplexer #(.select(2), .width(1), .tristate("false"), .disabled("Z"), .enable("false")) demultiplexer_1 (
    .out1(demultiplexer_1_out1), .out2(demultiplexer_1_out2), .out3(demultiplexer_1_out3), .in(1'b1),
    .sel(InterrNum));  // open: out0
  Register #(.width(1), .trigger("rising"), .Select("low")) IE (
    .D(and_8_out), .en(or_6_out), .Q(InterrEN), .clk(CLK));  // open: clr
  or or_7 (IR3_t, IR3, IRC);
  or or_8 (Jump, jal, jalr);
  Pull_Resistor #(.pull(0)) pull_resistor_4 (.node(demultiplexer_1_out1));
  Pull_Resistor #(.pull(0)) pull_resistor_5 (.node(demultiplexer_1_out2));
  Pull_Resistor #(.pull(0)) pull_resistor_6 (.node(demultiplexer_1_out3));
  \单周期硬布线控制器  \u_单周期硬布线控制器_1  (
    .Funct({IR[30], IR[25], IR[14:12]}), .OP(IR[6:2]), .ALU_OP(AluOP), .MemToReg(MemToReg),
    .MemWrite(MemWrite), .ALU_SRC(AluSrcB), .RegWrite(RegWrite), .ecall(ecall), .S_type(S_type), .Jalr(jalr),
    .Beq(beq), .JAL(jal), .Bne(bne), .in_3(IR[21]), .uret(uret), .auipc(auipc), .lui(lui), .lhu(lhu),
    .blt(blt), .CSRRCI(CSRRCI), .CSRRSI(CSRRSI));
  Multiplexer #(.select(1), .width(5), .disabled("Z"), .enable("false")) multiplexer_7 (
    .in0(IR[24:20]), .in1(5'b01010), .out(multiplexer_7_out), .sel(ecall));
  Multiplexer #(.select(1), .width(32), .disabled("Z"), .enable("false")) multiplexer_8 (
    .in0({Result[31:2], ChoiceForLhu, Result[0]}), .in1(MDout), .out(multiplexer_8_out), .sel(MemToReg));
  and and_9 (uret1, uret, demultiplexer_1_out1);
  and and_10 (uret2, demultiplexer_1_out2, uret);
  and and_11 (uret3, demultiplexer_1_out3, uret);
  Multiplexer #(.select(1), .width(5), .disabled("Z"), .enable("false")) multiplexer_9 (
    .in0(IR[19:15]), .in1(5'b10001), .out(multiplexer_9_out), .sel(ecall));
  Shifter #(.width(12), .shift("ll")) shifter_1 (
    .in({IR[31], IR[7], IR[30:25], IR[11:8]}), .\dist (4'b0001), .out(imm12_B));
  Shifter #(.width(20), .shift("ll")) shifter_2 (
    .in({IR[31], IR[19:12], IR[20], IR[30:21]}), .\dist (5'b00001), .out(imm20_J));
  Multiplexer #(.select(1), .width(32), .disabled("Z"), .enable("false")) multiplexer_10 (
    .in0(multiplexer_8_out), .in1(PC_4), .out(multiplexer_10_out), .sel(Jump));
  Demultiplexer #(.select(2), .width(1), .tristate("false"), .disabled("Z"), .enable("false")) demultiplexer_2 (
    .out1(demultiplexer_2_out1), .out2(demultiplexer_2_out2), .out3(demultiplexer_2_out3), .in(Interr),
    .sel(InterrNum));  // open: out0
  or or_9 (W1, Interrupt1, d_ff_1_q);
  or or_10 (W2, Interrupt2, d_ff_2_q);
  or or_11 (W3, Interrupt3, d_ff_3_q);
  Multiplexer #(.select(1), .width(32), .disabled("Z"), .enable("false")) multiplexer_11 (
    .in0({IR[31:12], {12{1'b0}}}), .in1(adder_4_out), .out(multiplexer_11_out), .sel(auipc));
  Adder #(.width(32)) adder_4 (.a({IR[31:12], {12{1'b0}}}), .b(PC), .out(adder_4_out));  // open: cin, cout
  \中断按键参考电路  \u_中断按键参考电路_1  ();  // open: 与中断屏蔽位与, 同步清零信号
  Pull_Resistor #(.pull(0)) pull_resistor_7 (.node(demultiplexer_2_out1));
  Pull_Resistor #(.pull(0)) pull_resistor_8 (.node(demultiplexer_2_out3));
  D_Flip_Flop #(.trigger("rising"), .Pre_Clr_Positions("LEGACY"), .NegatePresetClear("false"), .enable("true"), .NewFFLayout("false")) d_ff_1 (
    .clk(IR1_t), .D(1'b1), .Q(d_ff_1_q), .reset(Interrupt1));  // open: Qn, preset, en
  D_Flip_Flop #(.trigger("rising"), .Pre_Clr_Positions("LEGACY"), .NegatePresetClear("false"), .enable("true"), .NewFFLayout("false")) d_ff_2 (
    .clk(IR2_t), .D(1'b1), .Q(d_ff_2_q), .reset(Interrupt2));  // open: Qn, preset, en
  D_Flip_Flop #(.trigger("rising"), .Pre_Clr_Positions("LEGACY"), .NegatePresetClear("false"), .enable("true"), .NewFFLayout("false")) d_ff_3 (
    .clk(IR3_t), .D(1'b1), .Q(d_ff_3_q), .reset(Interrupt3));  // open: Qn, preset, en
  Multiplexer #(.select(1), .width(32), .disabled("Z"), .enable("false")) multiplexer_12 (
    .in0(multiplexer_10_out), .in1(multiplexer_11_out), .out(RDin), .sel(or_12_out));
  or or_12 (or_12_out, auipc, lui);
  Pull_Resistor #(.pull(0)) pull_resistor_9 (.node(demultiplexer_2_out2));
  D_Flip_Flop #(.trigger("high"), .Pre_Clr_Positions("LEGACY"), .NegatePresetClear("false"), .enable("true"), .NewFFLayout("false")) d_ff_4 (.Q(d_ff_4_q));  // open: clk, D, Qn, preset, en, reset
  // Probe on 13'hc
  or or_13 (or_13_out, d_ff_1_q, Interrupt1);
  or or_14 (or_14_out, d_ff_2_q, Interrupt2);
  or or_15 (or_15_out, d_ff_3_q, Interrupt3);
  Regifile regifile_1 (
    .Din(RDin), .Clk(CLK), .R1(R1), .R2(MDin), .WE(RegWrite), .W_num(IR[11:7]), .R1_num(multiplexer_9_out),
    .R2_num(multiplexer_7_out));
  Register #(.width(32), .trigger("rising"), .Select("low")) EPC1 (
    .D(nextPC), .en(demultiplexer_2_out1), .Q(EPC1_q), .clk(CLK));  // open: clr
  Register #(.width(32), .trigger("rising"), .Select("low")) EPC2 (
    .D(nextPC), .en(demultiplexer_2_out2), .Q(EPC2_q), .clk(CLK));  // open: clr
  Register #(.width(32), .trigger("rising"), .Select("low")) EPC3 (
    .D(nextPC), .en(demultiplexer_2_out3), .Q(EPC3_q), .clk(CLK));  // open: clr
  Comparator #(.width(13), .mode("twosComplement")) comparator_8 (
    .a(CNT_num), .b(13'hc), .eq(comparator_8_eq), .lt(comparator_8_lt));  // open: gt
  Clock #(.highDuration(1), .lowDuration(1)) clock_1 (.out(clock_1_out));
  and and_12 (and_12_out, or_13_out, ~uret1);  // AND_Gate
  and and_13 (and_13_out, or_14_out, ~uret2);  // AND_Gate
  and and_14 (and_14_out, or_15_out, ~uret3);  // AND_Gate
  Multiplexer #(.select(1), .width(12), .disabled("Z"), .enable("false")) multiplexer_13 (
    .in0(IR[31:20]), .in1({IR[31:25], IR[11:7]}), .out(multiplexer_13_out), .sel(S_type));
  Multiplexer #(.select(2), .width(32), .disabled("Z"), .enable("false")) multiplexer_14 (
    .in1(EPC1_q), .in2(EPC2_q), .in3(EPC3_q), .out(EPC), .sel(InterrPreNum));  // open: in0
  Counter #(.width(13), .max('h1fff), .ongoal("stay"), .trigger("rising"), .behavior("old")) counter_2 (
    .count(comparator_8_lt), .Q(CNT_num), .clk(clock_1_out));  // open: load, D, carry, clr, preset
  D_Flip_Flop #(.trigger("rising"), .Pre_Clr_Positions("LEGACY"), .NegatePresetClear("false"), .enable("true"), .NewFFLayout("false")) u_IR1 (
    .clk(CLK), .D(and_12_out), .Q(Interrupt1));  // open: Qn, preset, en, reset
  D_Flip_Flop #(.trigger("rising"), .Pre_Clr_Positions("LEGACY"), .NegatePresetClear("false"), .enable("true"), .NewFFLayout("false")) u_IR2 (
    .clk(CLK), .D(and_13_out), .Q(Interrupt2));  // open: Qn, preset, en, reset
  D_Flip_Flop #(.trigger("rising"), .Pre_Clr_Positions("LEGACY"), .NegatePresetClear("false"), .enable("true"), .NewFFLayout("false")) u_IR3 (
    .clk(CLK), .D(and_14_out), .Q(Interrupt3));  // open: Qn, preset, en, reset
  Multiplexer #(.select(1), .width(32), .disabled("Z"), .enable("false")) multiplexer_15 (
    .in0(MDin), .in1(bit_extender_3_out), .out(multiplexer_15_out), .sel(AluSrcB));
  assign bit_extender_3_out = {{20{multiplexer_13_out[11]}}, multiplexer_13_out};  // Bit_Extender bit_extender_3
  nand nand_1 (nand_1_out, d_ff_4_q, comparator_8_eq);
  assign CLK = nand_1_out ? clock_1_out : 1'bz;  // Controlled_Buffer controlled_buffer_1
  Pull_Resistor #(.pull(1)) pull_resistor_10 (.node(CLK));
  ALU alu_1 (
    .X(R1), .Y(multiplexer_15_out), .AluOP(AluOP), .Equal(equal),
    .Result({Result[31:2], ChoiceForLhu, Result[0]}), .out_6(less));  // open: Result_2, out_4
  or or_16 (or_16_out, uret, Interr);
  Counter #(.width(2), .max('h3), .ongoal("wrap"), .trigger("rising"), .behavior("new")) counter_3 (
    .count(or_16_out), .Q(counter_3_q), .clk(CLK), .down(uret));  // open: load, D, carry, clr, preset
  Demultiplexer #(.select(2), .width(1), .tristate("false"), .disabled("Z"), .enable("false")) demultiplexer_3 (
    .out0(demultiplexer_3_out0), .out1(demultiplexer_3_out1), .out2(demultiplexer_3_out2), .in(Interr),
    .sel(counter_3_q));  // open: out3
  Pull_Resistor #(.pull(0)) pull_resistor_11 (.node(demultiplexer_3_out0));
  Pull_Resistor #(.pull(0)) pull_resistor_12 (.node(demultiplexer_3_out1));
  Pull_Resistor #(.pull(0)) pull_resistor_13 (.node(demultiplexer_3_out2));
  RAM #(.addrWidth(10), .dataWidth(32), .bus("separate"), .Select("high")) ram_1 (
    .addr(Result[11:2]), .din(MDin), .data(ram_1_data), .str(MemWrite), .clk(CLK), .ld(MemToReg), .clr(RST));  // open: sel
  Register #(.width(2), .trigger("rising"), .Select("low")) IR1_2 (
    .D(InterrNum), .en(demultiplexer_3_out0), .Q(IR1_2_q), .clk(CLK));  // open: clr
  Register #(.width(2), .trigger("rising"), .Select("low")) IR2_2 (
    .D(InterrNum), .en(demultiplexer_3_out1), .Q(IR2_2_q), .clk(CLK));  // open: clr
  Register #(.width(2), .trigger("rising"), .Select("low")) IR3_2 (
    .D(InterrNum), .en(demultiplexer_3_out2), .Q(IR3_2_q), .clk(CLK));  // open: clr
  Multiplexer #(.select(2), .width(2), .disabled("Z"), .enable("false")) multiplexer_16 (
    .in1(IR1_2_q), .in2(IR2_2_q), .in3(IR3_2_q), .out(InterrPreNum), .sel(counter_3_q));  // open: in0
  Multiplexer #(.select(1), .width(16), .disabled("Z"), .enable("false")) multiplexer_17 (
    .in0(ram_1_data[15:0]), .in1(ram_1_data[31:16]), .out(multiplexer_17_out), .sel(ChoiceForLhu));
  assign bit_extender_4_out = {{16{1'b0}}, multiplexer_17_out};  // Bit_Extender bit_extender_4
  Multiplexer #(.select(1), .width(32), .disabled("Z"), .enable("false")) multiplexer_18 (
    .in0(ram_1_data), .in1(bit_extender_4_out), .out(MDout), .sel(lhu));
  Comparator #(.width(2), .mode("unsigned")) comparator_9 (
    .a(InterrPreNum), .b(InterrNum), .lt(shield));  // open: gt, eq
  Pull_Resistor #(.pull(1)) pull_resistor_14 (.node(shield));

  // Other names for the same wires on the sheet: imm12_S[11:0] = {IR[31:25], IR[11:7]}; imm32_U[31:12] = IR[31:12];
  //   imm12_I[11:0] = IR[31:20]; R2[31:0] = MDin; Result[1] = ChoiceForLhu

  // Notes on the sheet:
  //   中断源
  //   中断等待指示
  //   总复位信号应将除ROM以外所有存储组件全部清零
  //   多级中断测试信号模拟器
  //   数码管输出
  //   数码管输出应该用寄存器锁存，否则显示数据只能一闪而过
  //   指令存储器
  //   指令字
  //   contents of rom_1 (hex, n*v repeats v):
  //   7d000113 100413 1f41993 41f9d993 433 c00913 800b13 140413 f47413 800293 100313 499993 89e9b3 1300533
  //   2200893 73 406282b3 fe0294e3 140413 f00f93 1f47433 1c41413 800293 100313 49d993 89e9b3 1300533
  //   2200893 73 406282b3 fe0294e3 1c45413 406b0b33 b0463 f95ff06f 2b3 fff2c293 1029293 fff2e293 500533
  //   2200893 73 f5dff06f 1112023 410113 a12023 410113 812023 410113 1312023 410113 1412023 410113 1512023
  //   410113 1612023 410113 40e073 100b13 300a13 100a93 1600433 441413 14469b3 1300533 2200893 73 fe0416e3
  //   415a0a33 fe0a10e3 40f073 ffc10113 12b03 ffc10113 12a83 ffc10113 12a03 ffc10113 12983 ffc10113 12403
  //   ffc10113 12503 ffc10113 12883 200073 1112023 410113 a12023 410113 812023 410113 1312023 410113
  //   1412023 410113 1512023 410113 1612023 410113 40e073 200b13 300a13 100a93 1600433 441413 14469b3
  //   1300533 2200893 73 fe0416e3 415a0a33 fe0a10e3 40f073 ffc10113 12b03 ffc10113 12a83 ffc10113 12a03
  //   ffc10113 12983 ffc10113 12403 ffc10113 12503 ffc10113 12883 200073 1112023 410113 a12023 410113
  //   812023 410113 1312023 410113 1412023 410113 1512023 410113 1612023 410113 40e073 300b13 300a13
  //   100a93 1600433 441413 14469b3 1300533 2200893 73 fe0416e3 415a0a33 fe0a10e3 40f073 ffc10113 12b03
  //   ffc10113 12a83 ffc10113 12a03 ffc10113 12983 ffc10113 12403 ffc10113 12503 ffc10113 12883 200073
  //   rs1
  //   rs2
  //   rd
  //   Beq
  //   Bne
  //   AluOP
  //   AluSrcB
  //   RegWrite
  //   MemToReg
  //   MemWrite
  //   转换为字偏移量,所以需要逻辑左移一位
  //   为方便自动评测，需要输出PC，IR，寄存器堆写如数据RDin
  //   RAM写使能MemWrite、RAM写入数据MDin等信号
  //   控制位
  //   暂停节拍，不能为0
  //   戳工具置1进入计数暂停模式，ctrl+k时钟自动运行到对应节拍暂停
  //   ctrl+k关闭时钟连续运行，将控制位置零，进入单步调试模式调试
  //   Reset 
  //   Reset 
  //   Reset 
  //   可计数暂停的时钟源
  //   数据存储器
endmodule

module \封装正确性测试  (
);

  wire IR1, IR2, IR3, MemW, RegW;
  wire [31:0] EX_PC, ID_PC, IF_PC, IR, LED, MDin, MDinr, MEM_PC, PC, RDin, RDinr, WB_PC;

  \单周期RISC_V  \u_单周期risc_v_1  (
    .IR1(IR1), .IR2(IR2), .IR3(IR3), .RegWrite(RegW), .MemWrite(MemW), .PC(PC), .IR(IR), .RDin(RDin),
    .MDin(MDin), .LedData(LED));
  \气泡流水线  \u_气泡流水线_1  (
    .RegWrite(RegW), .MemWrite(MemW), .IF_PC(IF_PC), .ID_PC(ID_PC), .EX_PC(EX_PC), .M_PC(MEM_PC),
    .WB_PC(WB_PC), .RDin(RDinr), .MDin(MDinr), .LedData(LED));
  \单周期_单级中断  \u_单周期_单级中断_1  (
    .IR1(IR1), .IR2(IR2), .IR3(IR3), .RegWrite(RegW), .MemWrite(MemW), .PC(PC), .IR(IR), .RDin(RDin),
    .MDin(MDin), .LedData(LED));
  \理想流水线  \u_理想流水线_1  (
    .RegWrite(RegW), .MemWrite(MemW), .IF_PC(IF_PC), .ID_PC(ID_PC), .EX_PC(EX_PC), .M_PC(MEM_PC),
    .WB_PC(WB_PC), .RDin(RDinr), .MDin(MDinr), .LedData(LED));
  \重定向流水线  \u_重定向流水线_1  (
    .RegWrite(RegW), .MemWrite(MemW), .IF_PC(IF_PC), .ID_PC(ID_PC), .EX_PC(EX_PC), .M_PC(MEM_PC),
    .WB_PC(WB_PC), .RDin(RDinr), .MDin(MDinr), .LedData(LED));
  \单周期_多级中断  \u_单周期_多级中断_1  (
    .IR1(IR1), .IR2(IR2), .IR3(IR3), .RegWrite(RegW), .MemWrite(MemW), .PC(PC), .IR(IR), .RDin(RDin),
    .MDin(MDin), .LedData(LED));

  // Notes on the sheet:
  //   单周期封装测试
  //   气泡流水封装测试
  //   单周期+单级中断封装测试
  //   请检查上面封装有无位宽不匹配，引脚标签是否和连接的标签相对应，否则无法在educoder平台上正确测试
  //   理想流水封装测试
  //   重定向流水封装测试
  //   单周期+多级中断封装测试
endmodule

module IF_ID (
  input  [31:0] PCin,
  input  [31:0] IRin,
  input  PridictJumpin,
  input  RST,
  input  clk,
  input  EN,
  output [31:0] PCout,
  output [31:0] IRout,
  output PridictJumpout
);

  wire multiplexer_3_out;
  wire [31:0] multiplexer_1_out, multiplexer_2_out;

  Multiplexer #(.select(1), .width(32), .disabled("Z"), .enable("false")) multiplexer_1 (
    .in0(PCin), .in1({32{1'b0}}), .out(multiplexer_1_out), .sel(RST));
  Multiplexer #(.select(1), .width(32), .disabled("Z"), .enable("false")) multiplexer_2 (
    .in0(IRin), .in1({32{1'b0}}), .out(multiplexer_2_out), .sel(RST));
  Multiplexer #(.select(1), .width(1), .disabled("Z"), .enable("false")) multiplexer_3 (
    .in0(PridictJumpin), .in1(1'b0), .out(multiplexer_3_out), .sel(RST));
  Register #(.width(32), .trigger("rising"), .Select("low")) register_1 (
    .D(multiplexer_1_out), .en(EN), .Q(PCout), .clk(clk));  // open: clr
  Register #(.width(32), .trigger("rising"), .Select("low")) register_2 (
    .D(multiplexer_2_out), .en(EN), .Q(IRout), .clk(clk));  // open: clr
  Register #(.width(1), .trigger("rising"), .Select("low")) register_3 (
    .D(multiplexer_3_out), .en(EN), .Q(PridictJumpout), .clk(clk));  // open: clr
endmodule

module ID_EX (
  input  PridictJumpin,
  input  auipcin,
  input  [31:0] PCin,
  input  Luiin,
  input  [31:0] IRin,
  input  Lhuin,
  input  Jalrin,
  input  [31:0] Imm_I_in,
  input  Jalin,
  input  [31:0] Imm_S_in,
  input  Beqin,
  input  Bltin,
  input  [31:0] Imm_B_in,
  input  Bnein,
  input  [31:0] Imm_J_in,
  input  MemToRegin,
  input  [31:0] Imm_U_in,
  input  MemWritein,
  input  [3:0] AluOpin,
  input  [31:0] R1in,
  input  AluSrcBin,
  input  [31:0] R2in,
  input  RegWritein,
  input  S_Typein,
  input  haltin,
  input  [4:0] W_in,
  input  [1:0] R1CHOICEin,
  input  [1:0] R2CHOICEin,
  input  RST,
  input  EN_H,
  input  CLK,
  output PridictJumpout,
  output auipcout,
  output [31:0] PCout,
  output Luiout,
  output [31:0] IRout,
  output Lhuout,
  output Jalrout,
  output [31:0] Imm_I_out,
  output Jalout,
  output [31:0] Imm_S_out,
  output Beqout,
  output Bltout,
  output [31:0] Imm_B_out,
  output Bneout,
  output [31:0] Imm_J_out,
  output MemToRegout,
  output [31:0] Imm_U_out,
  output MemWriteout,
  output [3:0] AluOpout,
  output [31:0] R1out,
  output AluSrcBout,
  output [31:0] R2out,
  output RegWriteout,
  output S_Tpyeout,
  output haltout,
  output [4:0] W_out,
  output [1:0] R1CHOICEout,
  output [1:0] R2CHOICEout
);

  wire multiplexer_10_out, multiplexer_11_out, multiplexer_12_out, multiplexer_13_out, multiplexer_14_out,
       multiplexer_15_out, multiplexer_16_out, multiplexer_17_out, multiplexer_18_out, multiplexer_19_out,
       multiplexer_20_out, multiplexer_22_out, multiplexer_23_out, multiplexer_24_out, multiplexer_25_out;
  wire [1:0] multiplexer_27_out, multiplexer_28_out;
  wire [3:0] multiplexer_21_out;
  wire [4:0] multiplexer_26_out;
  wire [31:0] multiplexer_1_out, multiplexer_2_out, multiplexer_3_out, multiplexer_4_out, multiplexer_5_out,
       multiplexer_6_out, multiplexer_7_out, multiplexer_8_out, multiplexer_9_out;

  Multiplexer #(.select(1), .width(32), .disabled("Z"), .enable("false")) multiplexer_1 (
    .in0(PCin), .in1({32{1'b0}}), .out(multiplexer_1_out), .sel(RST));
  Multiplexer #(.select(1), .width(32), .disabled("Z"), .enable("false")) multiplexer_2 (
    .in0(IRin), .in1({32{1'b0}}), .out(multiplexer_2_out), .sel(RST));
  Multiplexer #(.select(1), .width(32), .disabled("Z"), .enable("false")) multiplexer_3 (
    .in0(Imm_I_in), .in1({32{1'b0}}), .out(multiplexer_3_out), .sel(RST));
  Multiplexer #(.select(1), .width(32), .disabled("Z"), .enable("false")) multiplexer_4 (
    .in0(Imm_S_in), .in1({32{1'b0}}), .out(multiplexer_4_out), .sel(RST));
  Multiplexer #(.select(1), .width(32), .disabled("Z"), .enable("false")) multiplexer_5 (
    .in0(Imm_B_in), .in1({32{1'b0}}), .out(multiplexer_5_out), .sel(RST));
  Multiplexer #(.select(1), .width(32), .disabled("Z"), .enable("false")) multiplexer_6 (
    .in0(Imm_J_in), .in1({32{1'b0}}), .out(multiplexer_6_out), .sel(RST));
  Multiplexer #(.select(1), .width(32), .disabled("Z"), .enable("false")) multiplexer_7 (
    .in0(Imm_U_in), .in1({32{1'b0}}), .out(multiplexer_7_out), .sel(RST));
  Multiplexer #(.select(1), .width(32), .disabled("Z"), .enable("false")) multiplexer_8 (
    .in0(R1in), .in1({32{1'b0}}), .out(multiplexer_8_out), .sel(RST));
  Multiplexer #(.select(1), .width(32), .disabled("Z"), .enable("false")) multiplexer_9 (
    .in0(R2in), .in1({32{1'b0}}), .out(multiplexer_9_out), .sel(RST));
  Register #(.width(32), .trigger("rising"), .Select("low")) register_1 (
    .D(multiplexer_1_out), .en(EN_H), .Q(PCout), .clk(CLK));  // open: clr
  Register #(.width(32), .trigger("rising"), .Select("low")) register_2 (
    .D(multiplexer_2_out), .en(EN_H), .Q(IRout), .clk(CLK));  // open: clr
  Register #(.width(32), .trigger("rising"), .Select("low")) register_3 (
    .D(multiplexer_3_out), .en(EN_H), .Q(Imm_I_out), .clk(CLK));  // open: clr
  Register #(.width(32), .trigger("rising"), .Select("low")) register_4 (
    .D(multiplexer_4_out), .en(EN_H), .Q(Imm_S_out), .clk(CLK));  // open: clr
  Register #(.width(32), .trigger("rising"), .Select("low")) register_5 (
    .D(multiplexer_5_out), .en(EN_H), .Q(Imm_B_out), .clk(CLK));  // open: clr
  Register #(.width(32), .trigger("rising"), .Select("low")) register_6 (
    .D(multiplexer_6_out), .en(EN_H), .Q(Imm_J_out), .clk(CLK));  // open: clr
  Register #(.width(32), .trigger("rising"), .Select("low")) register_7 (
    .D(multiplexer_7_out), .en(EN_H), .Q(Imm_U_out), .clk(CLK));  // open: clr
  Register #(.width(32), .trigger("rising"), .Select("low")) register_8 (
    .D(multiplexer_8_out), .en(EN_H), .Q(R1out), .clk(CLK));  // open: clr
  Register #(.width(32), .trigger("rising"), .Select("low")) register_9 (
    .D(multiplexer_9_out), .en(EN_H), .Q(R2out), .clk(CLK));  // open: clr
  Multiplexer #(.select(1), .width(1), .disabled("Z"), .enable("false")) multiplexer_10 (
    .in0(PridictJumpin), .in1(1'b0), .out(multiplexer_10_out), .sel(RST));
  Multiplexer #(.select(1), .width(1), .disabled("Z"), .enable("false")) multiplexer_11 (
    .in0(auipcin), .in1(1'b0), .out(multiplexer_11_out), .sel(RST));
  Multiplexer #(.select(1), .width(1), .disabled("Z"), .enable("false")) multiplexer_12 (
    .in0(Luiin), .in1(1'b0), .out(multiplexer_12_out), .sel(RST));
  Multiplexer #(.select(1), .width(1), .disabled("Z"), .enable("false")) multiplexer_13 (
    .in0(Lhuin), .in1(1'b0), .out(multiplexer_13_out), .sel(RST));
  Multiplexer #(.select(1), .width(1), .disabled("Z"), .enable("false")) multiplexer_14 (
    .in0(Jalrin), .in1(1'b0), .out(multiplexer_14_out), .sel(RST));
  Multiplexer #(.select(1), .width(1), .disabled("Z"), .enable("false")) multiplexer_15 (
    .in0(Jalin), .in1(1'b0), .out(multiplexer_15_out), .sel(RST));
  Multiplexer #(.select(1), .width(1), .disabled("Z"), .enable("false")) multiplexer_16 (
    .in0(Beqin), .in1(1'b0), .out(multiplexer_16_out), .sel(RST));
  Multiplexer #(.select(1), .width(1), .disabled("Z"), .enable("false")) multiplexer_17 (
    .in0(Bltin), .in1(1'b0), .out(multiplexer_17_out), .sel(RST));
  Multiplexer #(.select(1), .width(1), .disabled("Z"), .enable("false")) multiplexer_18 (
    .in0(Bnein), .in1(1'b0), .out(multiplexer_18_out), .sel(RST));
  Multiplexer #(.select(1), .width(1), .disabled("Z"), .enable("false")) multiplexer_19 (
    .in0(MemToRegin), .in1(1'b0), .out(multiplexer_19_out), .sel(RST));
  Multiplexer #(.select(1), .width(1), .disabled("Z"), .enable("false")) multiplexer_20 (
    .in0(MemWritein), .in1(1'b0), .out(multiplexer_20_out), .sel(RST));
  Multiplexer #(.select(1), .width(4), .disabled("Z"), .enable("false")) multiplexer_21 (
    .in0(AluOpin), .in1(4'b0000), .out(multiplexer_21_out), .sel(RST));
  Multiplexer #(.select(1), .width(1), .disabled("Z"), .enable("false")) multiplexer_22 (
    .in0(AluSrcBin), .in1(1'b0), .out(multiplexer_22_out), .sel(RST));
  Multiplexer #(.select(1), .width(1), .disabled("Z"), .enable("false")) multiplexer_23 (
    .in0(RegWritein), .in1(1'b0), .out(multiplexer_23_out), .sel(RST));
  Multiplexer #(.select(1), .width(1), .disabled("Z"), .enable("false")) multiplexer_24 (
    .in0(S_Typein), .in1(1'b0), .out(multiplexer_24_out), .sel(RST));
  Multiplexer #(.select(1), .width(1), .disabled("Z"), .enable("false")) multiplexer_25 (
    .in0(haltin), .in1(1'b0), .out(multiplexer_25_out), .sel(RST));
  Multiplexer #(.select(1), .width(5), .disabled("Z"), .enable("false")) multiplexer_26 (
    .in0(W_in), .in1({5{1'b0}}), .out(multiplexer_26_out), .sel(RST));
  Multiplexer #(.select(1), .width(2), .disabled("Z"), .enable("false")) multiplexer_27 (
    .in0(R1CHOICEin), .in1(2'b00), .out(multiplexer_27_out), .sel(RST));
  Multiplexer #(.select(1), .width(2), .disabled("Z"), .enable("false")) multiplexer_28 (
    .in0(R2CHOICEin), .in1(2'b00), .out(multiplexer_28_out), .sel(RST));
  Register #(.width(1), .trigger("rising"), .Select("low")) register_10 (
    .D(multiplexer_10_out), .en(EN_H), .Q(PridictJumpout), .clk(CLK));  // open: clr
  Register #(.width(1), .trigger("rising"), .Select("low")) register_11 (
    .D(multiplexer_11_out), .en(EN_H), .Q(auipcout), .clk(CLK));  // open: clr
  Register #(.width(1), .trigger("rising"), .Select("low")) register_12 (
    .D(multiplexer_12_out), .en(EN_H), .Q(Luiout), .clk(CLK));  // open: clr
  Register #(.width(1), .trigger("rising"), .Select("low")) register_13 (
    .D(multiplexer_13_out), .en(EN_H), .Q(Lhuout), .clk(CLK));  // open: clr
  Register #(.width(1), .trigger("rising"), .Select("low")) register_14 (
    .D(multiplexer_14_out), .en(EN_H), .Q(Jalrout), .clk(CLK));  // open: clr
  Register #(.width(1), .trigger("rising"), .Select("low")) register_15 (
    .D(multiplexer_15_out), .en(EN_H), .Q(Jalout), .clk(CLK));  // open: clr
  Register #(.width(1), .trigger("rising"), .Select("low")) register_16 (
    .D(multiplexer_16_out), .en(EN_H), .Q(Beqout), .clk(CLK));  // open: clr
  Register #(.width(1), .trigger("rising"), .Select("low")) register_17 (
    .D(multiplexer_17_out), .en(EN_H), .Q(Bltout), .clk(CLK));  // open: clr
  Register #(.width(1), .trigger("rising"), .Select("low")) register_18 (
    .D(multiplexer_18_out), .en(EN_H), .Q(Bneout), .clk(CLK));  // open: clr
  Register #(.width(1), .trigger("rising"), .Select("low")) register_19 (
    .D(multiplexer_19_out), .en(EN_H), .Q(MemToRegout), .clk(CLK));  // open: clr
  Register #(.width(1), .trigger("rising"), .Select("low")) register_20 (
    .D(multiplexer_20_out), .en(EN_H), .Q(MemWriteout), .clk(CLK));  // open: clr
  Register #(.width(4), .trigger("rising"), .Select("low")) register_21 (
    .D(multiplexer_21_out), .en(EN_H), .Q(AluOpout), .clk(CLK));  // open: clr
  Register #(.width(1), .trigger("rising"), .Select("low")) register_22 (
    .D(multiplexer_22_out), .en(EN_H), .Q(AluSrcBout), .clk(CLK));  // open: clr
  Register #(.width(1), .trigger("rising"), .Select("low")) register_23 (
    .D(multiplexer_23_out), .en(EN_H), .Q(RegWriteout), .clk(CLK));  // open: clr
  Register #(.width(1), .trigger("rising"), .Select("low")) register_24 (
    .D(multiplexer_24_out), .en(EN_H), .Q(S_Tpyeout), .clk(CLK));  // open: clr
  Register #(.width(1), .trigger("rising"), .Select("low")) register_25 (
    .D(multiplexer_25_out), .en(EN_H), .Q(haltout), .clk(CLK));  // open: clr
  Register #(.width(5), .trigger("rising"), .Select("low")) register_26 (
    .D(multiplexer_26_out), .en(EN_H), .Q(W_out), .clk(CLK));  // open: clr
  Register #(.width(2), .trigger("rising"), .Select("low")) register_27 (
    .D(multiplexer_27_out), .en(EN_H), .Q(R1CHOICEout), .clk(CLK));  // open: clr
  Register #(.width(2), .trigger("rising"), .Select("low")) register_28 (
    .D(multiplexer_28_out), .en(EN_H), .Q(R2CHOICEout), .clk(CLK));  // open: clr
endmodule

module EX_MEM (
  input  Lhuin,
  input  auipcin,
  input  [31:0] Imm_U_in,
  input  Luiin,
  input  MemToRegin,
  input  [31:0] PCin,
  input  MemWritein,
  input  [31:0] IRin,
  input  Jumpin,
  input  RegWritein,
  input  [31:0] Resultin,
  input  Haltin,
  input  [31:0] MDatain,
  input  [4:0] W_in,
  input  RST,
  input  EN_H,
  input  CLK,
  output Lhuout,
  output auipcout,
  output [31:0] Imm_U_out,
  output Luiout,
  output MemToRegout,
  output [31:0] PCout,
  output MemWriteout,
  output [31:0] IRout,
  output Jumpout,
  output RegWriteout,
  output [31:0] Resultout,
  output Haltout,
  output [31:0] Mdataout,
  output [4:0] W_out
);

  wire multiplexer_6_out, multiplexer_7_out, multiplexer_8_out, multiplexer_9_out, multiplexer_10_out,
       multiplexer_11_out, multiplexer_12_out, multiplexer_13_out;
  wire [4:0] multiplexer_14_out;
  wire [31:0] multiplexer_1_out, multiplexer_2_out, multiplexer_3_out, multiplexer_4_out, multiplexer_5_out;

  Multiplexer #(.select(1), .width(32), .disabled("Z"), .enable("false")) multiplexer_1 (
    .in0(Imm_U_in), .in1({32{1'b0}}), .out(multiplexer_1_out), .sel(RST));
  Multiplexer #(.select(1), .width(32), .disabled("Z"), .enable("false")) multiplexer_2 (
    .in0(PCin), .in1({32{1'b0}}), .out(multiplexer_2_out), .sel(RST));
  Multiplexer #(.select(1), .width(32), .disabled("Z"), .enable("false")) multiplexer_3 (
    .in0(IRin), .in1({32{1'b0}}), .out(multiplexer_3_out), .sel(RST));
  Multiplexer #(.select(1), .width(32), .disabled("Z"), .enable("false")) multiplexer_4 (
    .in0(Resultin), .in1({32{1'b0}}), .out(multiplexer_4_out), .sel(RST));
  Multiplexer #(.select(1), .width(32), .disabled("Z"), .enable("false")) multiplexer_5 (
    .in0(MDatain), .in1({32{1'b0}}), .out(multiplexer_5_out), .sel(RST));
  Register #(.width(32), .trigger("rising"), .Select("low")) register_1 (
    .D(multiplexer_1_out), .en(EN_H), .Q(Imm_U_out), .clk(CLK));  // open: clr
  Register #(.width(32), .trigger("rising"), .Select("low")) register_2 (
    .D(multiplexer_2_out), .en(EN_H), .Q(PCout), .clk(CLK));  // open: clr
  Register #(.width(32), .trigger("rising"), .Select("low")) register_3 (
    .D(multiplexer_3_out), .en(EN_H), .Q(IRout), .clk(CLK));  // open: clr
  Register #(.width(32), .trigger("rising"), .Select("low")) register_4 (
    .D(multiplexer_4_out), .en(EN_H), .Q(Resultout), .clk(CLK));  // open: clr
  Register #(.width(32), .trigger("rising"), .Select("low")) register_5 (
    .D(multiplexer_5_out), .en(EN_H), .Q(Mdataout), .clk(CLK));  // open: clr
  Multiplexer #(.select(1), .width(1), .disabled("Z"), .enable("false")) multiplexer_6 (
    .in0(Lhuin), .in1(1'b0), .out(multiplexer_6_out), .sel(RST));
  Multiplexer #(.select(1), .width(1), .disabled("Z"), .enable("false")) multiplexer_7 (
    .in0(auipcin), .in1(1'b0), .out(multiplexer_7_out), .sel(RST));
  Multiplexer #(.select(1), .width(1), .disabled("Z"), .enable("false")) multiplexer_8 (
    .in0(Luiin), .in1(1'b0), .out(multiplexer_8_out), .sel(RST));
  Multiplexer #(.select(1), .width(1), .disabled("Z"), .enable("false")) multiplexer_9 (
    .in0(MemToRegin), .in1(1'b0), .out(multiplexer_9_out), .sel(RST));
  Multiplexer #(.select(1), .width(1), .disabled("Z"), .enable("false")) multiplexer_10 (
    .in0(MemWritein), .in1(1'b0), .out(multiplexer_10_out), .sel(RST));
  Multiplexer #(.select(1), .width(1), .disabled("Z"), .enable("false")) multiplexer_11 (
    .in0(Jumpin), .in1(1'b0), .out(multiplexer_11_out), .sel(RST));
  Multiplexer #(.select(1), .width(1), .disabled("Z"), .enable("false")) multiplexer_12 (
    .in0(RegWritein), .in1(1'b0), .out(multiplexer_12_out), .sel(RST));
  Multiplexer #(.select(1), .width(1), .disabled("Z"), .enable("false")) multiplexer_13 (
    .in0(Haltin), .in1(1'b0), .out(multiplexer_13_out), .sel(RST));
  Multiplexer #(.select(1), .width(5), .disabled("Z"), .enable("false")) multiplexer_14 (
    .in0(W_in), .in1({5{1'b0}}), .out(multiplexer_14_out), .sel(RST));
  Register #(.width(1), .trigger("rising"), .Select("low")) register_6 (
    .D(multiplexer_6_out), .en(EN_H), .Q(Lhuout), .clk(CLK));  // open: clr
  Register #(.width(1), .trigger("rising"), .Select("low")) register_7 (
    .D(multiplexer_7_out), .en(EN_H), .Q(auipcout), .clk(CLK));  // open: clr
  Register #(.width(1), .trigger("rising"), .Select("low")) register_8 (
    .D(multiplexer_8_out), .en(EN_H), .Q(Luiout), .clk(CLK));  // open: clr
  Register #(.width(1), .trigger("rising"), .Select("low")) register_9 (
    .D(multiplexer_9_out), .en(EN_H), .Q(MemToRegout), .clk(CLK));  // open: clr
  Register #(.width(1), .trigger("rising"), .Select("low")) register_10 (
    .D(multiplexer_10_out), .en(EN_H), .Q(MemWriteout), .clk(CLK));  // open: clr
  Register #(.width(1), .trigger("rising"), .Select("low")) register_11 (
    .D(multiplexer_11_out), .en(EN_H), .Q(Jumpout), .clk(CLK));  // open: clr
  Register #(.width(1), .trigger("rising"), .Select("low")) register_12 (
    .D(multiplexer_12_out), .en(EN_H), .Q(RegWriteout), .clk(CLK));  // open: clr
  Register #(.width(1), .trigger("rising"), .Select("low")) register_13 (
    .D(multiplexer_13_out), .en(EN_H), .Q(Haltout), .clk(CLK));  // open: clr
  Register #(.width(5), .trigger("rising"), .Select("low")) register_14 (
    .D(multiplexer_14_out), .en(EN_H), .Q(W_out), .clk(CLK));  // open: clr
endmodule

module MEM_WB (
  input  lhuin,
  input  [31:0] Imm_U_in,
  input  auipcin,
  input  Luiin,
  input  [31:0] PCin,
  input  MemToRegin,
  input  [31:0] IRin,
  input  Jumpin,
  input  RegWritein,
  input  [31:0] Resultin,
  input  Haltin,
  input  [31:0] RMDatain,
  input  [4:0] W_in,
  input  choicein,
  input  RST,
  input  EN_H,
  input  CLK,
  output lhuout,
  output [31:0] Imm_U_out,
  output auipcout,
  output Luiout,
  output [31:0] PCout,
  output MemToRegout,
  output [31:0] IRout,
  output Jumpout,
  output RegWriteout,
  output [31:0] Resultout,
  output Haltout,
  output [31:0] RMdataout,
  output [4:0] W_out,
  output choiceout
);

  wire multiplexer_6_out, multiplexer_7_out, multiplexer_8_out, multiplexer_9_out, multiplexer_10_out,
       multiplexer_11_out, multiplexer_12_out, multiplexer_14_out;
  wire [4:0] multiplexer_13_out;
  wire [31:0] multiplexer_1_out, multiplexer_2_out, multiplexer_3_out, multiplexer_4_out, multiplexer_5_out;

  Multiplexer #(.select(1), .width(32), .disabled("Z"), .enable("false")) multiplexer_1 (
    .in0(Imm_U_in), .in1({32{1'b0}}), .out(multiplexer_1_out), .sel(RST));
  Multiplexer #(.select(1), .width(32), .disabled("Z"), .enable("false")) multiplexer_2 (
    .in0(PCin), .in1({32{1'b0}}), .out(multiplexer_2_out), .sel(RST));
  Multiplexer #(.select(1), .width(32), .disabled("Z"), .enable("false")) multiplexer_3 (
    .in0(IRin), .in1({32{1'b0}}), .out(multiplexer_3_out), .sel(RST));
  Multiplexer #(.select(1), .width(32), .disabled("Z"), .enable("false")) multiplexer_4 (
    .in0(Resultin), .in1({32{1'b0}}), .out(multiplexer_4_out), .sel(RST));
  Multiplexer #(.select(1), .width(32), .disabled("Z"), .enable("false")) multiplexer_5 (
    .in0(RMDatain), .in1({32{1'b0}}), .out(multiplexer_5_out), .sel(RST));
  Register #(.width(32), .trigger("rising"), .Select("low")) register_1 (
    .D(multiplexer_1_out), .en(EN_H), .Q(Imm_U_out), .clk(CLK));  // open: clr
  Register #(.width(32), .trigger("rising"), .Select("low")) register_2 (
    .D(multiplexer_2_out), .en(EN_H), .Q(PCout), .clk(CLK));  // open: clr
  Register #(.width(32), .trigger("rising"), .Select("low")) register_3 (
    .D(multiplexer_3_out), .en(EN_H), .Q(IRout), .clk(CLK));  // open: clr
  Register #(.width(32), .trigger("rising"), .Select("low")) register_4 (
    .D(multiplexer_4_out), .en(EN_H), .Q(Resultout), .clk(CLK));  // open: clr
  Register #(.width(32), .trigger("rising"), .Select("low")) register_5 (
    .D(multiplexer_5_out), .en(EN_H), .Q(RMdataout), .clk(CLK));  // open: clr
  Multiplexer #(.select(1), .width(1), .disabled("Z"), .enable("false")) multiplexer_6 (
    .in0(lhuin), .in1(1'b0), .out(multiplexer_6_out), .sel(RST));
  Multiplexer #(.select(1), .width(1), .disabled("Z"), .enable("false")) multiplexer_7 (
    .in0(auipcin), .in1(1'b0), .out(multiplexer_7_out), .sel(RST));
  Multiplexer #(.select(1), .width(1), .disabled("Z"), .enable("false")) multiplexer_8 (
    .in0(Luiin), .in1(1'b0), .out(multiplexer_8_out), .sel(RST));
  Multiplexer #(.select(1), .width(1), .disabled("Z"), .enable("false")) multiplexer_9 (
    .in0(MemToRegin), .in1(1'b0), .out(multiplexer_9_out), .sel(RST));
  Multiplexer #(.select(1), .width(1), .disabled("Z"), .enable("false")) multiplexer_10 (
    .in0(Jumpin), .in1(1'b0), .out(multiplexer_10_out), .sel(RST));
  Multiplexer #(.select(1), .width(1), .disabled("Z"), .enable("false")) multiplexer_11 (
    .in0(RegWritein), .in1(1'b0), .out(multiplexer_11_out), .sel(RST));
  Multiplexer #(.select(1), .width(1), .disabled("Z"), .enable("false")) multiplexer_12 (
    .in0(Haltin), .in1(1'b0), .out(multiplexer_12_out), .sel(RST));
  Multiplexer #(.select(1), .width(5), .disabled("Z"), .enable("false")) multiplexer_13 (
    .in0(W_in), .in1({5{1'b0}}), .out(multiplexer_13_out), .sel(RST));
  Multiplexer #(.select(1), .width(1), .disabled("Z"), .enable("false")) multiplexer_14 (
    .in0(choicein), .in1(1'b0), .out(multiplexer_14_out), .sel(RST));
  Register #(.width(1), .trigger("rising"), .Select("low")) register_6 (
    .D(multiplexer_6_out), .en(EN_H), .Q(lhuout), .clk(CLK));  // open: clr
  Register #(.width(1), .trigger("rising"), .Select("low")) register_7 (
    .D(multiplexer_7_out), .en(EN_H), .Q(auipcout), .clk(CLK));  // open: clr
  Register #(.width(1), .trigger("rising"), .Select("low")) register_8 (
    .D(multiplexer_8_out), .en(EN_H), .Q(Luiout), .clk(CLK));  // open: clr
  Register #(.width(1), .trigger("rising"), .Select("low")) register_9 (
    .D(multiplexer_9_out), .en(EN_H), .Q(MemToRegout), .clk(CLK));  // open: clr
  Register #(.width(1), .trigger("rising"), .Select("low")) register_10 (
    .D(multiplexer_10_out), .en(EN_H), .Q(Jumpout), .clk(CLK));  // open: clr
  Register #(.width(1), .trigger("rising"), .Select("low")) register_11 (
    .D(multiplexer_11_out), .en(EN_H), .Q(RegWriteout), .clk(CLK));  // open: clr
  Register #(.width(1), .trigger("rising"), .Select("low")) register_12 (
    .D(multiplexer_12_out), .en(EN_H), .Q(Haltout), .clk(CLK));  // open: clr
  Register #(.width(5), .trigger("rising"), .Select("low")) register_13 (
    .D(multiplexer_13_out), .en(EN_H), .Q(W_out), .clk(CLK));  // open: clr
  Register #(.width(1), .trigger("rising"), .Select("low")) register_14 (
    .D(multiplexer_14_out), .en(EN_H), .Q(choiceout), .clk(CLK));  // open: clr
endmodule

// 寄存器有效信号判断自动生成
module \寄存器有效信号判断自动生成  (
  input  OP2,
  input  OP3,
  input  OP4,
  input  OP5,
  input  OP6,
  input  F12,
  input  F13,
  input  F14,
  input  F25,
  input  F30,
  output R1,
  output R2
);

  wire and_1_out, and_2_out, and_3_out, and_4_out, and_5_out, and_6_out, and_7_out, and_8_out, and_9_out,
       and_10_out, and_11_out, and_12_out, and_13_out, and_14_out, and_15_out, and_16_out, and_17_out,
       and_18_out, and_19_out, and_20_out, and_21_out, and_22_out, and_23_out, and_24_out, and_25_out,
       and_26_out, and_27_out, and_28_out, and_29_out, and_30_out, and_31_out, and_32_out, and_33_out,
       and_34_out, and_35_out, not_1_out, not_2_out, not_3_out, not_4_out, not_5_out, not_6_out, not_7_out,
       not_8_out, not_9_out, not_10_out, not_11_out, not_12_out, not_13_out, not_14_out, not_15_out,
       not_16_out, not_17_out, not_18_out, not_19_out, not_20_out, not_21_out, not_22_out, not_23_out,
       not_24_out, not_25_out, not_26_out, not_27_out, not_28_out, not_29_out, not_30_out, not_31_out,
       not_32_out, not_33_out, not_34_out, not_35_out, not_36_out, not_37_out, not_38_out, not_39_out,
       not_40_out, not_41_out, not_42_out, not_43_out, not_44_out, not_45_out, not_46_out, not_47_out,
       not_48_out, not_49_out, not_50_out, not_51_out, not_52_out, not_53_out, not_54_out, not_55_out,
       not_56_out, not_57_out, not_58_out, not_59_out, not_60_out, not_61_out, not_62_out, not_63_out,
       not_64_out, not_65_out, not_66_out, not_67_out, not_68_out, not_69_out, not_70_out, not_71_out,
       not_72_out, not_73_out, not_74_out, not_75_out, not_76_out, not_77_out, not_78_out, not_79_out,
       not_80_out, not_81_out, not_82_out, not_83_out, not_84_out, not_85_out, not_86_out, not_87_out,
       not_88_out, not_89_out, not_90_out, not_91_out, not_92_out, not_93_out, not_94_out, not_95_out,
       not_96_out, not_97_out, not_98_out, not_99_out, not_100_out, not_101_out, not_102_out, not_103_out,
       not_104_out, not_105_out, not_106_out, not_107_out, not_108_out, not_109_out, not_110_out,
       not_111_out, not_112_out, not_113_out, not_114_out, not_115_out, not_116_out, not_117_out,
       not_118_out, not_119_out, not_120_out, not_121_out, not_122_out, not_123_out, not_124_out,
       not_125_out, not_126_out, not_127_out, not_128_out, not_129_out, not_130_out, not_131_out,
       not_132_out, not_133_out, not_134_out, not_135_out, not_136_out, not_137_out, not_138_out,
       not_139_out, not_140_out, not_141_out, not_142_out, not_143_out, not_144_out, not_145_out,
       not_146_out, not_147_out, not_148_out, not_149_out, not_150_out, not_151_out, not_152_out,
       not_153_out, not_154_out, not_155_out, not_156_out, not_157_out, not_158_out, not_159_out,
       not_160_out, not_161_out, not_162_out, not_163_out, not_164_out, not_165_out, not_166_out,
       not_167_out, not_168_out, not_169_out, not_170_out, not_171_out, not_172_out, not_173_out,
       not_174_out, not_175_out, not_176_out, not_177_out, not_178_out, not_179_out, not_180_out,
       not_181_out, not_182_out, not_183_out, not_184_out, not_185_out, not_186_out, not_187_out,
       not_188_out, not_189_out, not_190_out, not_191_out, not_192_out, not_193_out, not_194_out,
       not_195_out, not_196_out, not_197_out, not_198_out, not_199_out, not_200_out, not_201_out,
       not_202_out, not_203_out, not_204_out, not_205_out, not_206_out, not_207_out, not_208_out,
       not_209_out, not_210_out, not_211_out;

  not not_1 (not_1_out, F30);
  not not_2 (not_2_out, F25);
  not not_3 (not_3_out, F14);
  not not_4 (not_4_out, F13);
  not not_5 (not_5_out, F12);
  not not_6 (not_6_out, OP6);
  not not_7 (not_7_out, OP3);
  not not_8 (not_8_out, OP2);
  not not_9 (not_9_out, F25);
  not not_10 (not_10_out, F14);
  not not_11 (not_11_out, F13);
  not not_12 (not_12_out, F12);
  not not_13 (not_13_out, OP6);
  not not_14 (not_14_out, OP3);
  not not_15 (not_15_out, OP2);
  not not_16 (not_16_out, F30);
  not not_17 (not_17_out, F25);
  not not_18 (not_18_out, OP6);
  not not_19 (not_19_out, OP3);
  not not_20 (not_20_out, OP2);
  not not_21 (not_21_out, F30);
  not not_22 (not_22_out, F25);
  not not_23 (not_23_out, F12);
  not not_24 (not_24_out, OP6);
  not not_25 (not_25_out, OP3);
  not not_26 (not_26_out, OP2);
  not not_27 (not_27_out, F30);
  not not_28 (not_28_out, F25);
  not not_29 (not_29_out, F14);
  not not_30 (not_30_out, F12);
  not not_31 (not_31_out, OP6);
  not not_32 (not_32_out, OP3);
  not not_33 (not_33_out, OP2);
  not not_34 (not_34_out, F30);
  not not_35 (not_35_out, F25);
  not not_36 (not_36_out, F14);
  not not_37 (not_37_out, OP6);
  not not_38 (not_38_out, OP3);
  not not_39 (not_39_out, OP2);
  not not_40 (not_40_out, F14);
  not not_41 (not_41_out, F13);
  not not_42 (not_42_out, F12);
  not not_43 (not_43_out, OP6);
  not not_44 (not_44_out, OP5);
  not not_45 (not_45_out, OP3);
  not not_46 (not_46_out, OP2);
  not not_47 (not_47_out, OP6);
  not not_48 (not_48_out, OP5);
  not not_49 (not_49_out, OP3);
  not not_50 (not_50_out, OP2);
  not not_51 (not_51_out, F12);
  not not_52 (not_52_out, OP6);
  not not_53 (not_53_out, OP5);
  not not_54 (not_54_out, OP3);
  not not_55 (not_55_out, OP2);
  not not_56 (not_56_out, F13);
  not not_57 (not_57_out, F12);
  not not_58 (not_58_out, OP6);
  not not_59 (not_59_out, OP5);
  not not_60 (not_60_out, OP3);
  not not_61 (not_61_out, OP2);
  not not_62 (not_62_out, F14);
  not not_63 (not_63_out, F12);
  not not_64 (not_64_out, OP6);
  not not_65 (not_65_out, OP5);
  not not_66 (not_66_out, OP3);
  not not_67 (not_67_out, OP2);
  not not_68 (not_68_out, F30);
  not not_69 (not_69_out, F25);
  not not_70 (not_70_out, F14);
  not not_71 (not_71_out, F13);
  not not_72 (not_72_out, OP6);
  not not_73 (not_73_out, OP5);
  not not_74 (not_74_out, OP3);
  not not_75 (not_75_out, OP2);
  not not_76 (not_76_out, F30);
  not not_77 (not_77_out, F25);
  not not_78 (not_78_out, F13);
  not not_79 (not_79_out, OP6);
  not not_80 (not_80_out, OP5);
  not not_81 (not_81_out, OP3);
  not not_82 (not_82_out, OP2);
  not not_83 (not_83_out, F25);
  not not_84 (not_84_out, F13);
  not not_85 (not_85_out, OP6);
  not not_86 (not_86_out, OP5);
  not not_87 (not_87_out, OP3);
  not not_88 (not_88_out, OP2);
  not not_89 (not_89_out, F14);
  not not_90 (not_90_out, F12);
  not not_91 (not_91_out, OP6);
  not not_92 (not_92_out, OP5);
  not not_93 (not_93_out, OP4);
  not not_94 (not_94_out, OP3);
  not not_95 (not_95_out, OP2);
  not not_96 (not_96_out, F14);
  not not_97 (not_97_out, F12);
  not not_98 (not_98_out, OP6);
  not not_99 (not_99_out, OP4);
  not not_100 (not_100_out, OP3);
  not not_101 (not_101_out, OP2);
  not not_102 (not_102_out, F30);
  not not_103 (not_103_out, F25);
  not not_104 (not_104_out, F14);
  not not_105 (not_105_out, F13);
  not not_106 (not_106_out, F12);
  not not_107 (not_107_out, OP3);
  not not_108 (not_108_out, OP2);
  not not_109 (not_109_out, F14);
  not not_110 (not_110_out, F13);
  not not_111 (not_111_out, F12);
  not not_112 (not_112_out, OP4);
  not not_113 (not_113_out, OP3);
  not not_114 (not_114_out, OP2);
  not not_115 (not_115_out, F14);
  not not_116 (not_116_out, F13);
  not not_117 (not_117_out, OP4);
  not not_118 (not_118_out, OP3);
  not not_119 (not_119_out, OP2);
  not not_120 (not_120_out, F14);
  not not_121 (not_121_out, F13);
  not not_122 (not_122_out, F12);
  not not_123 (not_123_out, OP4);
  not not_124 (not_124_out, OP3);
  not not_125 (not_125_out, F30);
  not not_126 (not_126_out, F25);
  not not_127 (not_127_out, F13);
  not not_128 (not_128_out, OP6);
  not not_129 (not_129_out, OP3);
  not not_130 (not_130_out, OP2);
  not not_131 (not_131_out, F13);
  not not_132 (not_132_out, OP6);
  not not_133 (not_133_out, OP5);
  not not_134 (not_134_out, OP4);
  not not_135 (not_135_out, OP3);
  not not_136 (not_136_out, OP2);
  not not_137 (not_137_out, OP4);
  not not_138 (not_138_out, OP3);
  not not_139 (not_139_out, OP2);
  not not_140 (not_140_out, F30);
  not not_141 (not_141_out, F25);
  not not_142 (not_142_out, F14);
  not not_143 (not_143_out, F13);
  not not_144 (not_144_out, F12);
  not not_145 (not_145_out, OP6);
  not not_146 (not_146_out, OP3);
  not not_147 (not_147_out, OP2);
  not not_148 (not_148_out, F25);
  not not_149 (not_149_out, F14);
  not not_150 (not_150_out, F13);
  not not_151 (not_151_out, F12);
  not not_152 (not_152_out, OP6);
  not not_153 (not_153_out, OP3);
  not not_154 (not_154_out, OP2);
  not not_155 (not_155_out, F30);
  not not_156 (not_156_out, F25);
  not not_157 (not_157_out, OP6);
  not not_158 (not_158_out, OP3);
  not not_159 (not_159_out, OP2);
  not not_160 (not_160_out, F30);
  not not_161 (not_161_out, F25);
  not not_162 (not_162_out, F12);
  not not_163 (not_163_out, OP6);
  not not_164 (not_164_out, OP3);
  not not_165 (not_165_out, OP2);
  not not_166 (not_166_out, F30);
  not not_167 (not_167_out, F25);
  not not_168 (not_168_out, F14);
  not not_169 (not_169_out, F12);
  not not_170 (not_170_out, OP6);
  not not_171 (not_171_out, OP3);
  not not_172 (not_172_out, OP2);
  not not_173 (not_173_out, F30);
  not not_174 (not_174_out, F25);
  not not_175 (not_175_out, F14);
  not not_176 (not_176_out, OP6);
  not not_177 (not_177_out, OP3);
  not not_178 (not_178_out, OP2);
  not not_179 (not_179_out, F14);
  not not_180 (not_180_out, F12);
  not not_181 (not_181_out, OP6);
  not not_182 (not_182_out, OP4);
  not not_183 (not_183_out, OP3);
  not not_184 (not_184_out, OP2);
  not not_185 (not_185_out, F30);
  not not_186 (not_186_out, F25);
  not not_187 (not_187_out, F14);
  not not_188 (not_188_out, F13);
  not not_189 (not_189_out, F12);
  not not_190 (not_190_out, OP3);
  not not_191 (not_191_out, OP2);
  not not_192 (not_192_out, F14);
  not not_193 (not_193_out, F13);
  not not_194 (not_194_out, F12);
  not not_195 (not_195_out, OP4);
  not not_196 (not_196_out, OP3);
  not not_197 (not_197_out, OP2);
  not not_198 (not_198_out, F14);
  not not_199 (not_199_out, F13);
  not not_200 (not_200_out, OP4);
  not not_201 (not_201_out, OP3);
  not not_202 (not_202_out, OP2);
  not not_203 (not_203_out, F30);
  not not_204 (not_204_out, F25);
  not not_205 (not_205_out, F13);
  not not_206 (not_206_out, OP6);
  not not_207 (not_207_out, OP3);
  not not_208 (not_208_out, OP2);
  not not_209 (not_209_out, OP4);
  not not_210 (not_210_out, OP3);
  not not_211 (not_211_out, OP2);
  and and_1 (and_1_out, not_1_out, not_2_out, not_3_out, not_4_out, not_5_out, not_6_out, OP5, OP4, not_7_out, not_8_out);
  and and_2 (and_2_out, F30, not_9_out, not_10_out, not_11_out, not_12_out, not_13_out, OP5, OP4, not_14_out, not_15_out);
  and and_3 (and_3_out, not_16_out, not_17_out, F14, F13, F12, not_18_out, OP5, OP4, not_19_out, not_20_out);
  and and_4 (and_4_out, not_21_out, not_22_out, F14, F13, not_23_out, not_24_out, OP5, OP4, not_25_out, not_26_out);
  and and_5 (and_5_out, not_27_out, not_28_out, not_29_out, F13, not_30_out, not_31_out, OP5, OP4, not_32_out, not_33_out);
  and and_6 (and_6_out, not_34_out, not_35_out, not_36_out, F13, F12, not_37_out, OP5, OP4, not_38_out, not_39_out);
  and and_7 (and_7_out, not_40_out, not_41_out, not_42_out, not_43_out, not_44_out, OP4, not_45_out, not_46_out);
  and and_8 (and_8_out, F14, F13, F12, not_47_out, not_48_out, OP4, not_49_out, not_50_out);
  and and_9 (and_9_out, F14, F13, not_51_out, not_52_out, not_53_out, OP4, not_54_out, not_55_out);
  and and_10 (and_10_out, F14, not_56_out, not_57_out, not_58_out, not_59_out, OP4, not_60_out, not_61_out);
  and and_11 (and_11_out, not_62_out, F13, not_63_out, not_64_out, not_65_out, OP4, not_66_out, not_67_out);
  and and_12 (and_12_out, not_68_out, not_69_out, not_70_out, not_71_out, F12, not_72_out, not_73_out, OP4, not_74_out, not_75_out);
  and and_13 (and_13_out, not_76_out, not_77_out, F14, not_78_out, F12, not_79_out, not_80_out, OP4, not_81_out, not_82_out);
  and and_14 (and_14_out, F30, not_83_out, F14, not_84_out, F12, not_85_out, not_86_out, OP4, not_87_out, not_88_out);
  and and_15 (and_15_out, not_89_out, F13, not_90_out, not_91_out, not_92_out, not_93_out, not_94_out, not_95_out);
  and and_16 (and_16_out, not_96_out, F13, not_97_out, not_98_out, OP5, not_99_out, not_100_out, not_101_out);
  and and_17 (and_17_out, not_102_out, not_103_out, not_104_out, not_105_out, not_106_out, OP6, OP5, OP4, not_107_out, not_108_out);
  and and_18 (and_18_out, not_109_out, not_110_out, not_111_out, OP6, OP5, not_112_out, not_113_out, not_114_out);
  and and_19 (and_19_out, not_115_out, not_116_out, F12, OP6, OP5, not_117_out, not_118_out, not_119_out);
  and and_20 (and_20_out, not_120_out, not_121_out, not_122_out, OP6, OP5, not_123_out, not_124_out, OP2);
  and and_21 (and_21_out, not_125_out, not_126_out, F14, not_127_out, F12, not_128_out, OP5, OP4, not_129_out, not_130_out);
  and and_22 (and_22_out, F14, not_131_out, F12, not_132_out, not_133_out, not_134_out, not_135_out, not_136_out);
  and and_23 (and_23_out, F14, F13, F12, OP6, OP5, not_137_out, not_138_out, not_139_out);
  and and_24 (and_24_out, not_140_out, not_141_out, not_142_out, not_143_out, not_144_out, not_145_out, OP5, OP4, not_146_out, not_147_out);
  and and_25 (and_25_out, F30, not_148_out, not_149_out, not_150_out, not_151_out, not_152_out, OP5, OP4, not_153_out, not_154_out);
  and and_26 (and_26_out, not_155_out, not_156_out, F14, F13, F12, not_157_out, OP5, OP4, not_158_out, not_159_out);
  and and_27 (and_27_out, not_160_out, not_161_out, F14, F13, not_162_out, not_163_out, OP5, OP4, not_164_out, not_165_out);
  and and_28 (and_28_out, not_166_out, not_167_out, not_168_out, F13, not_169_out, not_170_out, OP5, OP4, not_171_out, not_172_out);
  and and_29 (and_29_out, not_173_out, not_174_out, not_175_out, F13, F12, not_176_out, OP5, OP4, not_177_out, not_178_out);
  and and_30 (and_30_out, not_179_out, F13, not_180_out, not_181_out, OP5, not_182_out, not_183_out, not_184_out);
  and and_31 (and_31_out, not_185_out, not_186_out, not_187_out, not_188_out, not_189_out, OP6, OP5, OP4, not_190_out, not_191_out);
  and and_32 (and_32_out, not_192_out, not_193_out, not_194_out, OP6, OP5, not_195_out, not_196_out, not_197_out);
  and and_33 (and_33_out, not_198_out, not_199_out, F12, OP6, OP5, not_200_out, not_201_out, not_202_out);
  and and_34 (and_34_out, not_203_out, not_204_out, F14, not_205_out, F12, not_206_out, OP5, OP4, not_207_out, not_208_out);
  and and_35 (and_35_out, F14, F13, F12, OP6, OP5, not_209_out, not_210_out, not_211_out);
  or or_1 (R2, and_24_out, and_25_out, and_26_out, and_27_out, and_28_out, and_29_out, and_30_out, and_31_out, and_32_out, and_33_out, and_34_out, and_35_out);
  or or_2 (R1, and_1_out, and_2_out, and_3_out, and_4_out, and_5_out, and_6_out, and_7_out, and_8_out, and_9_out, and_10_out, and_11_out, and_12_out, and_13_out, and_14_out, and_15_out, and_16_out, and_17_out, and_18_out, and_19_out, and_20_out, and_21_out, and_22_out, and_23_out);
endmodule

// 数据相关-气泡流水线
module \数据相关_气泡流水线  (
  input  [4:0] ID_R1_num,
  input  [4:0] EX_W_num,
  input  EX_RegWrite,
  input  [4:0] ID_R2_num,
  input  [4:0] MEM_W_num,
  input  MEM_RegWrite,
  input  [4:0] ID_OP,
  input  [4:0] ID_Funct,
  output \数据相关 
);

  wire and_1_out, and_2_out, and_3_out, and_4_out, and_5_out, and_6_out, comparator_1_eq, comparator_2_eq,
       comparator_3_eq, comparator_4_eq, comparator_5_eq, comparator_6_eq, comparator_7_eq, comparator_8_eq,
       or_1_out, or_2_out, \寄存器有效信号判断自动生成_1_r1 , \寄存器有效信号判断自动生成_1_r2 ;

  \寄存器有效信号判断自动生成  \u_寄存器有效信号判断自动生成_1  (
    .OP2(ID_OP[0]), .OP3(ID_OP[1]), .OP4(ID_OP[2]), .OP5(ID_OP[3]), .OP6(ID_OP[4]), .F12(ID_Funct[0]),
    .F13(ID_Funct[1]), .F14(ID_Funct[2]), .F25(ID_Funct[3]), .F30(ID_Funct[4]), .R1(\寄存器有效信号判断自动生成_1_r1 ),
    .R2(\寄存器有效信号判断自动生成_1_r2 ));
  Comparator #(.width(5), .mode("twosComplement")) comparator_1 (
    .a(MEM_W_num), .b(ID_R1_num), .eq(comparator_1_eq));  // open: gt, lt
  Comparator #(.width(5), .mode("twosComplement")) comparator_2 (
    .a(MEM_W_num), .b({5{1'b0}}), .eq(comparator_2_eq));  // open: gt, lt
  Comparator #(.width(5), .mode("twosComplement")) comparator_3 (
    .a(EX_W_num), .b({5{1'b0}}), .eq(comparator_3_eq));  // open: gt, lt
  Comparator #(.width(5), .mode("twosComplement")) comparator_4 (
    .a(EX_W_num), .b(ID_R1_num), .eq(comparator_4_eq));  // open: gt, lt
  Comparator #(.width(5), .mode("twosComplement")) comparator_5 (
    .a(MEM_W_num), .b(ID_R2_num), .eq(comparator_5_eq));  // open: gt, lt
  Comparator #(.width(5), .mode("twosComplement")) comparator_6 (
    .a(MEM_W_num), .b({5{1'b0}}), .eq(comparator_6_eq));  // open: gt, lt
  Comparator #(.width(5), .mode("twosComplement")) comparator_7 (
    .a(EX_W_num), .b({5{1'b0}}), .eq(comparator_7_eq));  // open: gt, lt
  Comparator #(.width(5), .mode("twosComplement")) comparator_8 (
    .a(EX_W_num), .b(ID_R2_num), .eq(comparator_8_eq));  // open: gt, lt
  and and_1 (and_1_out, MEM_RegWrite, comparator_1_eq, ~comparator_2_eq);  // AND_Gate
  and and_2 (and_2_out, ~comparator_3_eq, comparator_4_eq, EX_RegWrite);  // AND_Gate
  and and_3 (and_3_out, MEM_RegWrite, comparator_5_eq, ~comparator_6_eq);  // AND_Gate
  and and_4 (and_4_out, ~comparator_7_eq, comparator_8_eq, EX_RegWrite);  // AND_Gate
  or or_1 (or_1_out, and_1_out, and_2_out);
  or or_2 (or_2_out, and_3_out, and_4_out);
  and and_5 (and_5_out, or_1_out, \寄存器有效信号判断自动生成_1_r1 );
  and and_6 (and_6_out, \寄存器有效信号判断自动生成_1_r2 , or_2_out);
  or or_3 (\数据相关 , and_5_out, and_6_out);

  // Other names for the same wires on the sheet: ID_Funct_num[4:0] = ID_Funct; ID_OP_num[4:0] = ID_OP
endmodule

// 数据相关-重定向流水线
module \数据相关_重定向流水线  (
  input  [4:0] ID_R1_num,
  input  [4:0] EX_W_num,
  input  EX_RegWrite,
  input  [4:0] ID_R2_num,
  input  [4:0] MEM_W_num,
  input  MEM_RegWrite,
  input  [4:0] ID_OP,
  input  [4:0] EX_OP,
  input  [4:0] ID_Funct,
  output [1:0] R1C,
  output [1:0] R2C,
  output \数据相关 ,
  output Load_Use
);

  wire and_5_out, and_6_out, and_7_out, and_8_out, and_9_out, and_10_out, and_11_out, and_12_out,
       comparator_1_eq, comparator_2_eq, comparator_3_eq, comparator_4_eq, comparator_5_eq, comparator_6_eq,
       comparator_7_eq, comparator_8_eq, comparator_9_eq, comparator_10_eq, comparator_11_eq, \EX_R1冲突 ,
       \EX_R2冲突 , \MEM_R1冲突 , \MEM_R2冲突 , or_1_out, or_2_out, or_4_out, or_5_out, \R1使用 , \R2使用 ;

  \寄存器有效信号判断自动生成  \u_寄存器有效信号判断自动生成_1  (
    .OP2(ID_OP[0]), .OP3(ID_OP[1]), .OP4(ID_OP[2]), .OP5(ID_OP[3]), .OP6(ID_OP[4]), .F12(ID_Funct[0]),
    .F13(ID_Funct[1]), .F14(ID_Funct[2]), .F25(ID_Funct[3]), .F30(ID_Funct[4]), .R1(\R1使用 ), .R2(\R2使用 ));
  Comparator #(.width(5), .mode("twosComplement")) comparator_1 (
    .a(MEM_W_num), .b(ID_R1_num), .eq(comparator_1_eq));  // open: gt, lt
  Comparator #(.width(5), .mode("twosComplement")) comparator_2 (
    .a(MEM_W_num), .b({5{1'b0}}), .eq(comparator_2_eq));  // open: gt, lt
  Comparator #(.width(5), .mode("twosComplement")) comparator_3 (
    .a(EX_W_num), .b({5{1'b0}}), .eq(comparator_3_eq));  // open: gt, lt
  Comparator #(.width(5), .mode("twosComplement")) comparator_4 (
    .a(EX_W_num), .b(ID_R1_num), .eq(comparator_4_eq));  // open: gt, lt
  Comparator #(.width(5), .mode("twosComplement")) comparator_5 (
    .a(MEM_W_num), .b(ID_R2_num), .eq(comparator_5_eq));  // open: gt, lt
  Comparator #(.width(5), .mode("twosComplement")) comparator_6 (
    .a(MEM_W_num), .b({5{1'b0}}), .eq(comparator_6_eq));  // open: gt, lt
  Comparator #(.width(5), .mode("twosComplement")) comparator_7 (
    .a(EX_W_num), .b({5{1'b0}}), .eq(comparator_7_eq));  // open: gt, lt
  Comparator #(.width(5), .mode("twosComplement")) comparator_8 (
    .a(EX_W_num), .b(ID_R2_num), .eq(comparator_8_eq));  // open: gt, lt
  and and_1 (\MEM_R1冲突 , MEM_RegWrite, comparator_1_eq, ~comparator_2_eq);  // AND_Gate
  and and_2 (\EX_R1冲突 , ~comparator_3_eq, comparator_4_eq, EX_RegWrite);  // AND_Gate
  and and_3 (\MEM_R2冲突 , MEM_RegWrite, comparator_5_eq, ~comparator_6_eq);  // AND_Gate
  and and_4 (\EX_R2冲突 , ~comparator_7_eq, comparator_8_eq, EX_RegWrite);  // AND_Gate
  or or_1 (or_1_out, \MEM_R1冲突 , \EX_R1冲突 );
  or or_2 (or_2_out, \MEM_R2冲突 , \EX_R2冲突 );
  and and_5 (and_5_out, or_1_out, \R1使用 );
  and and_6 (and_6_out, \R2使用 , or_2_out);
  or or_3 (\数据相关 , and_5_out, and_6_out);
  and and_7 (and_7_out, \R1使用 , \MEM_R1冲突 );
  and and_8 (and_8_out, \R1使用 , \EX_R1冲突 );
  and and_9 (and_9_out, \R2使用 , \MEM_R2冲突 );
  and and_10 (and_10_out, \R2使用 , \EX_R2冲突 );
  and and_11 (and_11_out, \R1使用 , \EX_R1冲突 );
  and and_12 (and_12_out, \EX_R2冲突 , \R2使用 );
  Comparator #(.width(5), .mode("twosComplement")) comparator_9 (
    .a(EX_OP), .b({5{1'b0}}), .eq(comparator_9_eq));  // open: gt, lt
  Comparator #(.width(5), .mode("twosComplement")) comparator_10 (
    .a(EX_OP), .b(5'b00101), .eq(comparator_10_eq));  // open: gt, lt
  Comparator #(.width(5), .mode("twosComplement")) comparator_11 (
    .a(EX_OP), .b(5'b01101), .eq(comparator_11_eq));  // open: gt, lt
  Priority_Encoder #(.select(2), .disabled("Z")) priority_encoder_1 (
    .in0(1'b1), .in1(and_7_out), .in2(and_8_out), .out(R1C));  // open: in3, gs, en_out, en_in
  Priority_Encoder #(.select(2), .disabled("Z")) priority_encoder_2 (
    .in0(1'b1), .in1(and_9_out), .in2(and_10_out), .out(R2C));  // open: in3, gs, en_out, en_in
  or or_4 (or_4_out, and_11_out, and_12_out);
  or or_5 (or_5_out, comparator_9_eq, comparator_10_eq, comparator_11_eq);
  and and_13 (Load_Use, or_4_out, or_5_out);

  // Other names for the same wires on the sheet: EX_Opcode[4:0] = EX_OP; ID_Funct_num[4:0] = ID_Funct;
  //   ID_OP_num[4:0] = ID_OP

  // Notes on the sheet:
  //   lw、lhu
  //   auipc
  //   lui
endmodule
module \流水线中断  (
  output RegWrite,
  output MemWrite,
  output [31:0] IF_PC,
  output [31:0] ID_PC,
  output [31:0] EX_PC,
  output [31:0] M_PC,
  output [31:0] WB_PC,
  output [31:0] RDin,
  output [31:0] MDin,
  output [31:0] LedData
);

  wire and_1_out, and_2_out, and_3_out, and_4_out, and_5_out, and_7_out, and_8_out, and_9_out, and_10_out,
       and_11_out, and_15_out, auipc, beq, blt, bne, branch, branchOn, Choicein, CLK, clock_1_out,
       comparator_1_eq, comparator_1_lt, comparator_2_eq, comparator_3_eq, comparator_4_eq, comparator_5_eq,
       d_ff_1_q, d_ff_2_q, d_ff_3_q, d_ff_4_q, demultiplexer_1_out1, demultiplexer_1_out2,
       demultiplexer_1_out3, en, equal, EX_ecall, EX_MEM_auipcout, EX_MEM_haltout, EX_MEM_jumpout,
       EX_MEM_lhuout, EX_MEM_luiout, EX_MEM_memtoregout, EX_RegWrite, Go, halt, ID_ecall, ID_EX_alusrcbout,
       ID_EX_auipcout, ID_EX_lhuout, ID_EX_luiout, ID_EX_memtoregout, ID_EX_memwriteout, ID_EX_s_tpyeout,
       IE_q, Interr, InterrEN, Interrupt1, Interrupt2, Interrupt3, IR1, IR2, IR3, jal, jalr, Jump, less,
       lhuout, LoadUse, lui, MEM_RegWrite, MEM_WB_choiceout, MEM_WB_haltout, MemToReg, nand_1_out, not_1_out,
       not_2_out, not_3_out, not_4_out, not_5_out, not_6_out, not_7_out, not_8_out, not_9_out, not_10_out,
       not_11_out, not_12_out, or_2_out, or_3_out, or_5_out, or_7_out, or_8_out, or_9_out, or_10_out,
       or_12_out, or_13_out, RST, uret, uret1, uret2, uret3, W1, W2, W3, \单周期硬布线控制器_1_alu_src ,
       \单周期硬布线控制器_1_auipc , \单周期硬布线控制器_1_beq , \单周期硬布线控制器_1_blt , \单周期硬布线控制器_1_bne , \单周期硬布线控制器_1_jal ,
       \单周期硬布线控制器_1_jalr , \单周期硬布线控制器_1_lhu , \单周期硬布线控制器_1_lui , \单周期硬布线控制器_1_memtoreg ,
       \单周期硬布线控制器_1_memwrite , \单周期硬布线控制器_1_regwrite , \单周期硬布线控制器_1_s_type , \数据相关 ;
  wire [1:0] EX_R1C, EX_R2C, ID_R1C, ID_R2C, priority_encoder_1_out, retReg_q;
  wire [3:0] ID_EX_aluopout, \单周期硬布线控制器_1_alu_op ;
  wire [4:0] EX_W_num, ID_funct, ID_R1_num, ID_R2_num, MEM_W_num, W_num;
  wire [11:0] shifter_1_out;
  wire [12:0] CNT_num;
  wire [15:0] adder_4_out, \LoadUse次数 , multiplexer_13_out, shifter_3_out, \总周期数 , \插入气泡数 , \无条件分支数 ,
       \条件分支成功数 ;
  wire [19:0] shifter_2_out;
  wire [31:0] adder_1_out, adder_2_out, adder_3_out, adder_6_out, adder_7_out, bit_extender_1_out,
       bit_extender_2_out, bit_extender_3_out, bit_extender_4_out, bit_extender_5_out, EPC, EX_IR,
       EX_MEM_imm_u_out, EX_R1, EX_R2, ID_EX_imm_i_out, ID_EX_imm_s_out, ID_EX_imm_u_out, ID_IR, IF_IR,
       imm32_B, imm32_J, InterrAddr, jaddress, MDout, MEM_IR, MEM_Result, MEM_WB_rmdataout,
       multiplexer_1_out, multiplexer_2_out, multiplexer_4_out, multiplexer_5_out, multiplexer_9_out,
       multiplexer_10_out, multiplexer_15_out, multiplexer_16_out, multiplexer_17_out, nextPC, R1, R1out, R2,
       R2out, ram_1_data, Result, WB_imm32_U, WB_IR;

  Button \u_总复位  (.out(RST));
  Button _1 (.out(IR1));
  Button _2 (.out(IR2));
  Button _3 (.out(IR3));
  // Probe on \总周期数 
  // Probe on \总周期数 
  Button \u_继续运行  (.out(Go));
  LED #(.active("true")) led_1 (.in(W1));
  LED #(.active("true")) led_2 (.in(W2));
  LED #(.active("true")) led_3 (.in(W3));
  Hex_Digit_Display hex_digit_display_1 (.value(LedData[31:28]));  // open: dp
  // Probe on IF_PC[19:0]
  // RiscV_Probe riscv_probe_1: pin names not known; wires that end beside it: IF_IR
  Hex_Digit_Display hex_digit_display_2 (.value(LedData[23:20]));  // open: dp
  Hex_Digit_Display hex_digit_display_3 (.value(LedData[27:24]));  // open: dp
  // Probe on ID_PC[19:0]
  // RiscV_Probe riscv_probe_2: pin names not known; wires that end beside it: {ID_IR[31], ID_funct[4], ID_IR[29:26], ID_funct[3], ID_IR[24:15], ID_funct[2:0], ID_IR[11:0]}
  Multiplexer #(.select(1), .width(32), .disabled("Z"), .enable("false")) multiplexer_1 (
    .in0(adder_3_out), .in1(jaddress), .out(multiplexer_1_out), .sel(jalr));
  Adder #(.width(32)) adder_1 (.a(imm32_J), .b(EX_PC), .out(adder_1_out));  // open: cin, cout
  Adder #(.width(32)) adder_2 (.a(imm32_B), .b(EX_PC), .out(adder_2_out));  // open: cin, cout
  Hex_Digit_Display hex_digit_display_4 (.value(LedData[19:16]));  // open: dp
  Hex_Digit_Display hex_digit_display_5 (.value(LedData[15:12]));  // open: dp
  Multiplexer #(.select(1), .width(32), .disabled("Z"), .enable("false")) multiplexer_2 (
    .in0(multiplexer_1_out), .in1(adder_1_out), .out(multiplexer_2_out), .sel(jal));
  Hex_Digit_Display hex_digit_display_6 (.value(LedData[7:4]));  // open: dp
  Hex_Digit_Display hex_digit_display_7 (.value(LedData[11:8]));  // open: dp
  // Probe on EX_PC[19:0]
  // RiscV_Probe riscv_probe_3: pin names not known; wires that end beside it: EX_IR
  Multiplexer #(.select(1), .width(32), .disabled("Z"), .enable("false")) multiplexer_3 (
    .in0(multiplexer_2_out), .in1(adder_2_out), .out(nextPC), .sel(branch));
  Hex_Digit_Display hex_digit_display_8 (.value(LedData[3:0]));  // open: dp
  Multiplexer #(.select(1), .width(32), .disabled("Z"), .enable("false")) multiplexer_4 (
    .in0(nextPC), .in1(InterrAddr), .out(multiplexer_4_out), .sel(InterrEN));
  \数据相关_重定向流水线  \u_数据相关_重定向流水线_1  (
    .ID_R1_num(ID_R1_num), .EX_W_num(EX_W_num), .EX_RegWrite(EX_RegWrite), .ID_R2_num(ID_R2_num),
    .MEM_W_num(MEM_W_num), .MEM_RegWrite(MEM_RegWrite), .ID_OP(ID_IR[6:2]), .EX_OP(EX_IR[6:2]),
    .ID_Funct(ID_funct), .R1C(ID_R1C), .R2C(ID_R2C), .\数据相关 (\数据相关 ), .Load_Use(LoadUse));
  or or_1 (W1, Interrupt1, d_ff_1_q);
  // Probe on \总周期数 
  // Probe on M_PC[19:0]
  // RiscV_Probe riscv_probe_4: pin names not known; wires that end beside it: MEM_IR
  Multiplexer #(.select(1), .width(32), .disabled("Z"), .enable("false")) multiplexer_5 (
    .in0(multiplexer_4_out), .in1(EPC), .out(multiplexer_5_out), .sel(uret));
  D_Flip_Flop #(.trigger("rising"), .Pre_Clr_Positions("LEGACY"), .NegatePresetClear("false"), .enable("true"), .NewFFLayout("false")) d_ff_1 (
    .clk(IR1), .D(1'b1), .Q(d_ff_1_q), .reset(Interrupt1));  // open: Qn, preset, en
  // Probe on \总周期数 
  // Probe on \无条件分支数 
  // Probe on \条件分支成功数 
  // Probe on \插入气泡数 
  // Probe on \LoadUse次数 
  Register #(.width(32), .trigger("rising"), .Select("low")) PC (
    .D(multiplexer_5_out), .en(and_1_out), .Q(IF_PC), .clk(CLK), .clr(RST));
  and and_1 (and_1_out, not_1_out, not_2_out);
  not not_1 (not_1_out, LoadUse);
  not not_2 (not_2_out, halt);
  or or_2 (or_2_out, d_ff_1_q, Interrupt1);
  and and_2 (and_2_out, or_2_out, ~uret1);  // AND_Gate
  // Probe on IF_PC[11:0]
  // Probe on WB_PC[19:0]
  // RiscV_Probe riscv_probe_5: pin names not known; wires that end beside it: WB_IR, 13'h117
  D_Flip_Flop #(.trigger("rising"), .Pre_Clr_Positions("LEGACY"), .NegatePresetClear("false"), .enable("true"), .NewFFLayout("false")) u_IR1 (
    .clk(CLK), .D(and_2_out), .Q(Interrupt1), .en(branchOn));  // open: Qn, preset, reset
  // Probe on ID_PC[11:0]
  // Probe on EX_PC[11:0]
  // Probe on M_PC[11:0]
  D_Flip_Flop #(.trigger("high"), .Pre_Clr_Positions("LEGACY"), .NegatePresetClear("false"), .enable("true"), .NewFFLayout("false")) d_ff_2 (.Q(d_ff_2_q));  // open: clk, D, Qn, preset, en, reset
  // Probe on 13'h117
  ROM #(.addrWidth(10), .dataWidth(32), .Select("high")) rom_1 (.addr(IF_PC[11:2]), .data(IF_IR));
  Adder #(.width(32)) adder_3 (.a(IF_PC), .b(32'h4), .out(adder_3_out));  // open: cin, cout
  or or_3 (or_3_out, RST, branch, jal, jalr, InterrEN);
  // Probe on WB_PC[11:0]
  Comparator #(.width(13), .mode("twosComplement")) comparator_1 (
    .a(CNT_num), .b(13'h117), .eq(comparator_1_eq), .lt(comparator_1_lt));  // open: gt
  Clock #(.highDuration(1), .lowDuration(1)) clock_1 (.out(clock_1_out));
  IF_ID IF_ID (
    .PCin(IF_PC), .IRin(IF_IR), .PCout(ID_PC),
    .IRout({ID_IR[31], ID_funct[4], ID_IR[29:26], ID_funct[3], ID_IR[24:15], ID_funct[2:0], ID_IR[11:0]}),
    .RST(or_3_out), .clk(CLK), .EN(and_3_out));  // open: PridictJumpin, PridictJumpout
  and and_3 (and_3_out, en, not_3_out);
  not not_3 (not_3_out, LoadUse);
  or or_4 (W2, Interrupt2, d_ff_3_q);
  nand nand_1 (nand_1_out, d_ff_2_q, comparator_1_eq);
  Counter #(.width(13), .max('h1fff), .ongoal("stay"), .trigger("rising"), .behavior("old")) counter_1 (
    .count(comparator_1_lt), .Q(CNT_num), .clk(clock_1_out));  // open: load, D, carry, clr, preset
  // RiscV_Probe riscv_probe_6: pin names not known; wires that end beside it: {ID_IR[31], ID_funct[4], ID_IR[29:26], ID_funct[3], ID_IR[24:15], ID_funct[2:0], ID_IR[11:0]}
  D_Flip_Flop #(.trigger("rising"), .Pre_Clr_Positions("LEGACY"), .NegatePresetClear("false"), .enable("true"), .NewFFLayout("false")) d_ff_3 (
    .clk(IR2), .D(1'b1), .Q(d_ff_3_q), .reset(Interrupt2));  // open: Qn, preset, en
  assign CLK = nand_1_out ? clock_1_out : 1'bz;  // Controlled_Buffer controlled_buffer_1
  or or_5 (or_5_out, d_ff_3_q, Interrupt2);
  Pull_Resistor #(.pull(1)) pull_resistor_1 (.node(CLK));
  assign bit_extender_1_out = {{20{ID_IR[31]}}, {ID_IR[31], ID_funct[4], ID_IR[29:26], ID_funct[3], ID_IR[24:20]}};  // Bit_Extender bit_extender_1
  assign bit_extender_2_out = {{20{ID_IR[31]}}, {ID_IR[31], ID_funct[4], ID_IR[29:26], ID_funct[3], ID_IR[11:7]}};  // Bit_Extender bit_extender_2
  and and_4 (and_4_out, or_5_out, ~uret2);  // AND_Gate
  \单周期硬布线控制器  \u_单周期硬布线控制器_1  (
    .Funct(ID_funct), .OP(ID_IR[6:2]), .ALU_OP(\单周期硬布线控制器_1_alu_op ), .MemToReg(\单周期硬布线控制器_1_memtoreg ),
    .MemWrite(\单周期硬布线控制器_1_memwrite ), .ALU_SRC(\单周期硬布线控制器_1_alu_src ), .RegWrite(\单周期硬布线控制器_1_regwrite ),
    .ecall(ID_ecall), .S_type(\单周期硬布线控制器_1_s_type ), .Jalr(\单周期硬布线控制器_1_jalr ), .Beq(\单周期硬布线控制器_1_beq ),
    .JAL(\单周期硬布线控制器_1_jal ), .Bne(\单周期硬布线控制器_1_bne ), .in_3(ID_IR[21]), .uret(uret),
    .auipc(\单周期硬布线控制器_1_auipc ), .lui(\单周期硬布线控制器_1_lui ), .lhu(\单周期硬布线控制器_1_lhu ), .blt(\单周期硬布线控制器_1_blt ));  // open: CSRRCI, CSRRSI
  Multiplexer #(.select(1), .width(5), .disabled("Z"), .enable("false")) multiplexer_6 (
    .in0(ID_IR[19:15]), .in1(5'b10001), .out(ID_R1_num), .sel(ID_ecall));
  Multiplexer #(.select(1), .width(5), .disabled("Z"), .enable("false")) multiplexer_7 (
    .in0(ID_IR[24:20]), .in1(5'b01010), .out(ID_R2_num), .sel(ID_ecall));
  assign bit_extender_3_out = {{20{shifter_1_out[11]}}, shifter_1_out};  // Bit_Extender bit_extender_3
  Shifter #(.width(12), .shift("ll")) shifter_1 (
    .in({ID_IR[31], ID_IR[7], ID_funct[4], ID_IR[29:26], ID_funct[3], ID_IR[11:8]}), .\dist (4'b0001),
    .out(shifter_1_out));
  Shifter #(.width(20), .shift("ll")) shifter_2 (
    .in({ID_IR[31], ID_IR[19:15], ID_funct[2:0], ID_IR[20], ID_funct[4], ID_IR[29:26], ID_funct[3], ID_IR[24:21]}),
    .\dist (5'b00001), .out(shifter_2_out));
  assign bit_extender_4_out = {{12{shifter_2_out[19]}}, shifter_2_out};  // Bit_Extender bit_extender_4
  D_Flip_Flop #(.trigger("rising"), .Pre_Clr_Positions("LEGACY"), .NegatePresetClear("false"), .enable("true"), .NewFFLayout("false")) u_IR2 (
    .clk(CLK), .D(and_4_out), .Q(Interrupt2), .en(branchOn));  // open: Qn, preset, reset
  not not_4 (not_4_out, CLK);
  or or_6 (W3, Interrupt3, d_ff_4_q);
  Regifile regifile_1 (
    .Din(RDin), .Clk(not_4_out), .R1(R1), .R2(R2), .WE(RegWrite), .W_num(W_num), .R1_num(ID_R1_num),
    .R2_num(ID_R2_num));
  D_Flip_Flop #(.trigger("rising"), .Pre_Clr_Positions("LEGACY"), .NegatePresetClear("false"), .enable("true"), .NewFFLayout("false")) d_ff_4 (
    .clk(IR3), .D(1'b1), .Q(d_ff_4_q), .reset(Interrupt3));  // open: Qn, preset, en
  or or_7 (or_7_out, d_ff_4_q, Interrupt3);
  and and_5 (and_5_out, or_7_out, ~uret3);  // AND_Gate
  or or_8 (or_8_out, LoadUse, or_3_out);
  D_Flip_Flop #(.trigger("rising"), .Pre_Clr_Positions("LEGACY"), .NegatePresetClear("false"), .enable("true"), .NewFFLayout("false")) u_IR3 (
    .clk(CLK), .D(and_5_out), .Q(Interrupt3), .en(branchOn));  // open: Qn, preset, reset
  ID_EX ID_EX (
    .PCin(ID_PC), .Lhuin(\单周期硬布线控制器_1_lhu ), .Jalrin(\单周期硬布线控制器_1_jalr ),
    .IRin({ID_IR[31], ID_funct[4], ID_IR[29:26], ID_funct[3], ID_IR[24:15], ID_funct[2:0], ID_IR[11:0]}),
    .Jalin(\单周期硬布线控制器_1_jal ), .Beqin(\单周期硬布线控制器_1_beq ), .Imm_I_in(bit_extender_1_out),
    .Bltin(\单周期硬布线控制器_1_blt ), .Imm_S_in(bit_extender_2_out), .Bnein(\单周期硬布线控制器_1_bne ),
    .Imm_B_in(bit_extender_3_out), .MemToRegin(\单周期硬布线控制器_1_memtoreg ), .MemWritein(\单周期硬布线控制器_1_memwrite ),
    .Imm_J_in(bit_extender_4_out), .AluOpin(\单周期硬布线控制器_1_alu_op ),
    .Imm_U_in({ID_IR[31], ID_funct[4], ID_IR[29:26], ID_funct[3], ID_IR[24:15], ID_funct[2:0], {12{1'b0}}}),
    .AluSrcBin(\单周期硬布线控制器_1_alu_src ), .R1in(R1), .RegWritein(\单周期硬布线控制器_1_regwrite ), .R2in(R2),
    .S_Typein(\单周期硬布线控制器_1_s_type ), .haltin(ID_ecall), .W_in(ID_IR[11:7]), .PCout(EX_PC),
    .Lhuout(ID_EX_lhuout), .Jalrout(jalr), .IRout(EX_IR), .Jalout(jal), .Beqout(beq),
    .Imm_I_out(ID_EX_imm_i_out), .Bltout(blt), .Imm_S_out(ID_EX_imm_s_out), .Bneout(bne),
    .Imm_B_out(imm32_B), .MemToRegout(ID_EX_memtoregout), .MemWriteout(ID_EX_memwriteout),
    .Imm_J_out(imm32_J), .AluOpout(ID_EX_aluopout), .Imm_U_out(ID_EX_imm_u_out),
    .AluSrcBout(ID_EX_alusrcbout), .R1out(R1out), .RegWriteout(EX_RegWrite), .R2out(R2out),
    .S_Tpyeout(ID_EX_s_tpyeout), .haltout(EX_ecall), .W_out(EX_W_num), .RST(or_8_out), .EN_H(en), .CLK(CLK),
    .Luiin(\单周期硬布线控制器_1_lui ), .Luiout(ID_EX_luiout), .auipcin(\单周期硬布线控制器_1_auipc ),
    .auipcout(ID_EX_auipcout), .R1CHOICEin(ID_R1C), .R1CHOICEout(EX_R1C), .R2CHOICEin(ID_R2C),
    .R2CHOICEout(EX_R2C));  // open: PridictJumpin, PridictJumpout
  or or_9 (or_9_out, jal, jalr);
  Multiplexer #(.select(2), .width(32), .disabled("Z"), .enable("false")) multiplexer_8 (
    .in0(R2out), .in1(RDin), .in2({MEM_Result[31:2], Choicein, MEM_Result[0]}), .out(EX_R2), .sel(EX_R2C));  // open: in3
  Multiplexer #(.select(1), .width(32), .disabled("Z"), .enable("false")) multiplexer_9 (
    .in0(ID_EX_imm_i_out), .in1(ID_EX_imm_s_out), .out(multiplexer_9_out), .sel(ID_EX_s_tpyeout));
  Counter #(.width(16), .max('hffff), .ongoal("wrap"), .trigger("rising"), .behavior("new")) counter_2 (
    .count(branch), .Q(\条件分支成功数 ), .clk(CLK), .clr(RST));  // open: load, D, carry, preset, down
  Comparator #(.width(5), .mode("twosComplement")) comparator_2 (
    .a(IF_PC[6:2]), .b(5'b11000), .eq(comparator_2_eq));  // open: gt, lt
  not not_5 (not_5_out, comparator_2_eq);
  Comparator #(.width(5), .mode("twosComplement")) comparator_3 (
    .a(IF_PC[6:2]), .b(5'b11011), .eq(comparator_3_eq));  // open: gt, lt
  not not_6 (not_6_out, comparator_3_eq);
  Comparator #(.width(5), .mode("twosComplement")) comparator_4 (
    .a(IF_PC[6:2]), .b(5'b11001), .eq(comparator_4_eq));  // open: gt, lt
  not not_7 (not_7_out, comparator_4_eq);
  Multiplexer #(.select(1), .width(32), .disabled("Z"), .enable("false")) multiplexer_10 (
    .in0(EX_R2), .in1(multiplexer_9_out), .out(multiplexer_10_out), .sel(ID_EX_alusrcbout));
  Comparator #(.width(32), .mode("twosComplement")) comparator_5 (
    .a(EX_R1), .b(32'h22), .eq(comparator_5_eq));  // open: gt, lt
  not not_8 (not_8_out, comparator_5_eq);
  and and_6 (branchOn, not_5_out, not_6_out, not_7_out);
  Multiplexer #(.select(2), .width(32), .disabled("Z"), .enable("false")) multiplexer_11 (
    .in0(R1out), .in1(RDin), .in2({MEM_Result[31:2], Choicein, MEM_Result[0]}), .out(EX_R1), .sel(EX_R1C));  // open: in3
  ALU alu_1 (
    .X(EX_R1), .Y(multiplexer_10_out), .AluOP(ID_EX_aluopout), .Equal(equal), .Result(jaddress), .out_6(less));  // open: Result_2, out_4
  and and_7 (and_7_out, EX_ecall, comparator_5_eq);
  and and_8 (and_8_out, not_8_out, EX_ecall);
  and and_9 (and_9_out, blt, less);
  and and_10 (and_10_out, beq, equal);
  not not_9 (not_9_out, equal);
  and and_11 (and_11_out, not_9_out, bne);
  Register #(.width(32), .trigger("rising"), .Select("low")) register_1 (
    .D(EX_R2), .en(and_7_out), .Q(LedData), .clk(CLK), .clr(RST));
  or or_10 (or_10_out, jal, jalr);
  Counter #(.width(16), .max('hffff), .ongoal("wrap"), .trigger("rising"), .behavior("new")) counter_3 (
    .count(or_10_out), .Q(\无条件分支数 ), .clk(CLK), .clr(RST));  // open: load, D, carry, preset, down
  Priority_Encoder #(.select(2), .disabled("Z")) priority_encoder_1 (
    .in0(1'b0), .in1(Interrupt1), .in2(Interrupt2), .in3(Interrupt3), .out(priority_encoder_1_out),
    .gs(Interr));  // open: en_out, en_in
  or or_11 (branch, and_9_out, and_10_out, and_11_out);
  Multiplexer #(.select(2), .width(32), .disabled("Z"), .enable("false")) multiplexer_12 (
    .in1(32'h30ac), .in2(32'h3150), .in3(32'h31f4), .out(InterrAddr), .sel(priority_encoder_1_out));  // open: in0
  not not_10 (not_10_out, halt);
  Register #(.width(2), .trigger("rising"), .Select("low")) retReg (
    .D(priority_encoder_1_out), .en(InterrEN), .Q(retReg_q), .clk(CLK));  // open: clr
  EX_MEM EX_MEM (
    .MemToRegin(ID_EX_memtoregout), .PCin(EX_PC), .MemWritein(ID_EX_memwriteout), .IRin(EX_IR),
    .Jumpin(or_9_out), .RegWritein(EX_RegWrite), .Resultin(jaddress), .Haltin(and_8_out), .MDatain(EX_R2),
    .W_in(EX_W_num), .MemToRegout(EX_MEM_memtoregout), .PCout(M_PC), .MemWriteout(MemWrite), .IRout(MEM_IR),
    .Jumpout(EX_MEM_jumpout), .RegWriteout(MEM_RegWrite),
    .Resultout({MEM_Result[31:2], Choicein, MEM_Result[0]}), .Haltout(EX_MEM_haltout), .Mdataout(MDin),
    .W_out(MEM_W_num), .RST(RST), .EN_H(en), .CLK(CLK), .auipcin(ID_EX_auipcout), .auipcout(EX_MEM_auipcout),
    .Luiin(ID_EX_luiout), .Luiout(EX_MEM_luiout), .Lhuin(ID_EX_lhuout), .Lhuout(EX_MEM_lhuout),
    .Imm_U_in(ID_EX_imm_u_out), .Imm_U_out(EX_MEM_imm_u_out));
  Counter #(.width(16), .max('hffff), .ongoal("wrap"), .trigger("rising"), .behavior("new")) counter_4 (
    .count(not_10_out), .Q(\总周期数 ), .clk(CLK), .clr(RST));  // open: load, D, carry, preset, down
  Demultiplexer #(.select(2), .width(1), .tristate("false"), .disabled("Z"), .enable("false")) demultiplexer_1 (
    .out1(demultiplexer_1_out1), .out2(demultiplexer_1_out2), .out3(demultiplexer_1_out3), .in(1'b1),
    .sel(retReg_q));  // open: out0
  and and_12 (uret1, uret, demultiplexer_1_out1);
  and and_13 (uret2, demultiplexer_1_out2, uret);
  and and_14 (uret3, demultiplexer_1_out3, uret);
  not not_11 (not_11_out, halt);
  and and_15 (and_15_out, not_11_out, LoadUse);
  Adder #(.width(16)) adder_4 (.a(\条件分支成功数 ), .b(\无条件分支数 ), .out(adder_4_out));  // open: cin, cout
  RAM #(.addrWidth(10), .dataWidth(32), .bus("separate"), .Select("high")) ram_1 (
    .addr(MEM_Result[11:2]), .din(MDin), .data(ram_1_data), .str(MemWrite), .clk(CLK),
    .ld(EX_MEM_memtoregout), .clr(RST));  // open: sel
  Shifter #(.width(16), .shift("ll")) shifter_3 (.in(adder_4_out), .\dist (4'b0001), .out(shifter_3_out));
  Counter #(.width(16), .max('hffff), .ongoal("wrap"), .trigger("rising"), .behavior("new")) counter_5 (
    .count(and_15_out), .Q(\LoadUse次数 ), .clk(CLK), .clr(RST));  // open: load, D, carry, preset, down
  or or_12 (or_12_out, InterrEN, uret);
  MEM_WB MEM_WB (
    .PCin(M_PC), .MemToRegin(EX_MEM_memtoregout), .IRin(MEM_IR), .Jumpin(EX_MEM_jumpout),
    .RegWritein(MEM_RegWrite), .Resultin({MEM_Result[31:2], Choicein, MEM_Result[0]}),
    .Haltin(EX_MEM_haltout), .RMDatain(ram_1_data), .W_in(MEM_W_num), .PCout(WB_PC), .MemToRegout(MemToReg),
    .IRout(WB_IR), .Jumpout(Jump), .RegWriteout(RegWrite), .Resultout(Result), .Haltout(MEM_WB_haltout),
    .RMdataout(MEM_WB_rmdataout), .W_out(W_num), .RST(RST), .EN_H(en), .CLK(CLK), .auipcin(EX_MEM_auipcout),
    .auipcout(auipc), .Luiin(EX_MEM_luiout), .Luiout(lui), .Imm_U_in(EX_MEM_imm_u_out),
    .Imm_U_out(WB_imm32_U), .lhuin(EX_MEM_lhuout), .lhuout(lhuout), .choicein(Choicein),
    .choiceout(MEM_WB_choiceout));
  Adder #(.width(16)) adder_5 (.a(shifter_3_out), .b(\LoadUse次数 ), .out(\插入气泡数 ));  // open: cin, cout
  not not_12 (not_12_out, IE_q);
  Register #(.width(1), .trigger("rising"), .Select("low")) IE (
    .D(InterrEN), .en(or_12_out), .Q(IE_q), .clk(CLK));  // open: clr
  Register #(.width(32), .trigger("rising"), .Select("low")) u_EPC (
    .D(nextPC), .en(InterrEN), .Q(EPC), .clk(CLK));  // open: clr
  and and_16 (InterrEN, not_12_out, Interr);
  assign bit_extender_5_out = {{16{1'b0}}, multiplexer_13_out};  // Bit_Extender bit_extender_5
  Multiplexer #(.select(1), .width(16), .disabled("Z"), .enable("false")) multiplexer_13 (
    .in0(MEM_WB_rmdataout[15:0]), .in1(MEM_WB_rmdataout[31:16]), .out(multiplexer_13_out),
    .sel(MEM_WB_choiceout));
  Multiplexer #(.select(1), .width(32), .disabled("Z"), .enable("false")) multiplexer_14 (
    .in0(MEM_WB_rmdataout), .in1(bit_extender_5_out), .out(MDout), .sel(lhuout));
  and and_17 (halt, MEM_WB_haltout, ~Go);  // AND_Gate
  not not_13 (en, halt);
  Multiplexer #(.select(1), .width(32), .disabled("Z"), .enable("false")) multiplexer_15 (
    .in0(Result), .in1(MDout), .out(multiplexer_15_out), .sel(MemToReg));
  Adder #(.width(32)) adder_6 (.a(WB_PC), .b(32'h4), .out(adder_6_out));  // open: cin, cout
  Multiplexer #(.select(1), .width(32), .disabled("Z"), .enable("false")) multiplexer_16 (
    .in0(multiplexer_15_out), .in1(adder_6_out), .out(multiplexer_16_out), .sel(Jump));
  Multiplexer #(.select(1), .width(32), .disabled("Z"), .enable("false")) multiplexer_17 (
    .in0(WB_imm32_U), .in1(adder_7_out), .out(multiplexer_17_out), .sel(auipc));
  Adder #(.width(32)) adder_7 (.a(WB_imm32_U), .b(WB_PC), .out(adder_7_out));  // open: cin, cout
  Multiplexer #(.select(1), .width(32), .disabled("Z"), .enable("false")) multiplexer_18 (
    .in0(multiplexer_16_out), .in1(multiplexer_17_out), .out(RDin), .sel(or_13_out));
  or or_13 (or_13_out, auipc, lui);

  // Other names for the same wires on the sheet: ID_IR (some bits) = ID_funct; ID_OP[4:0] = ID_IR[6:2];
  //   MEM_PC[31:0] = M_PC; MEM_Result[1] = Choicein; WriteBackData[31:0] = RDin

  // Notes on the sheet:
  //   中断源
  //   时空图监测，可删除
  //   中断等待指示
  //   数码管输出
  //   Reset 
  //   控制位
  //   指令存储器
  //   流水调试日志用
  //   暂停节拍，不能为0
  //   contents of rom_1 (hex, n*v repeats v):
  //   7d000113 100413 1f41993 41f9d993 433 c00913 800b13 140413 f47413 800293 100313 499993 89e9b3 1300533
  //   2200893 73 406282b3 fe0294e3 140413 f00f93 1f47433 1c41413 800293 100313 49d993 89e9b3 1300533
  //   2200893 73 406282b3 fe0294e3 1c45413 406b0b33 b0463 f95ff06f 2b3 fff2c293 1029293 fff2e293 500533
  //   2200893 73 f5dff06f 1112023 410113 a12023 410113 812023 410113 1312023 410113 1412023 410113 1512023
  //   410113 1612023 410113 100b13 300a13 100a93 1600433 441413 14469b3 1300533 2200893 73 fe0416e3
  //   415a0a33 fe0a10e3 ffc10113 12b03 ffc10113 12a83 ffc10113 12a03 ffc10113 12983 ffc10113 12403
  //   ffc10113 12503 ffc10113 12883 200073 1112023 410113 a12023 410113 812023 410113 1312023 410113
  //   1412023 410113 1512023 410113 1612023 410113 200b13 300a13 100a93 1600433 441413 14469b3 1300533
  //   2200893 73 fe0416e3 415a0a33 fe0a10e3 ffc10113 12b03 ffc10113 12a83 ffc10113 12a03 ffc10113 12983
  //   ffc10113 12403 ffc10113 12503 ffc10113 12883 200073 1112023 410113 a12023 410113 812023 410113
  //   1312023 410113 1412023 410113 1512023 410113 1612023 410113 300b13 300a13 100a93 1600433 441413
  //   14469b3 1300533 2200893 73 fe0416e3 415a0a33 fe0a10e3 ffc10113 12b03 ffc10113 12a83 ffc10113 12a03
  //   ffc10113 12983 ffc10113 12403 ffc10113 12503 ffc10113 12883 200073
  //   戳工具置1进入计数暂停模式，ctrl+k时钟自动运行到对应节拍暂停
  //   ctrl+k关闭时钟连续运行，将控制位置零，进入单步调试模式调试
  //   指令字ID.IR
  //   可计数暂停的时钟源
  //   rs1
  //   rs2
  //   rd
  //   Reset 
  //   Beq
  //   Bne
  //   MemToReg
  //   MemWrite
  //   AluOP
  //   AluSrcB
  //   RegWrite
  //   转换为字偏移量,所以需要逻辑左移一位
  //   为方便自动评测，需要输出流水线各段保存的PC值，注意是PC不是PC+4，另外ID段寄存器写入信息，Mem段内存写入信息也要输出
  //   Reset 
  //   数据存储器
endmodule

module \分支预测  (
  output RegWrite,
  output MemWrite,
  output [31:0] IF_PC,
  output [31:0] ID_PC,
  output [31:0] EX_PC,
  output [31:0] M_PC,
  output [31:0] WB_PC,
  output [31:0] RDin,
  output [31:0] MDin,
  output [31:0] LedData
);

  wire and_1_out, and_2_out, and_3_out, and_4_out, and_5_out, and_6_out, and_7_out, and_8_out, and_9_out,
       auipc, beq, blt, bne, branch, branchTaken, Choicein, CLK, clock_1_out, comparator_1_eq,
       comparator_1_lt, comparator_2_eq, comparator_3_eq, d_ff_1_q, en, equal, EX_ecall, EX_MEM_auipcout,
       EX_MEM_haltout, EX_MEM_jumpout, EX_MEM_lhuout, EX_MEM_luiout, EX_MEM_memtoregout, EX_PredictErr,
       EX_PredictJump, EX_RegWrite, Go, halt, ID_ecall, ID_EX_alusrcbout, ID_EX_auipcout, ID_EX_lhuout,
       ID_EX_luiout, ID_EX_memtoregout, ID_EX_memwriteout, ID_EX_s_tpyeout, IF_ID_pridictjumpout, IR1, IR2,
       IR3, jal, jalr, Jump, less, lhuout, LoadUse, lui, MEM_RegWrite, MEM_WB_choiceout, MEM_WB_haltout,
       MemToReg, nand_1_out, not_1_out, not_2_out, not_4_out, not_5_out, not_6_out, not_7_out, not_8_out,
       not_9_out, or_1_out, or_2_out, or_3_out, or_4_out, or_5_out, or_6_out, or_7_out, or_8_out, or_11_out,
       PredictJump, RST, W1, W2, W3, \单周期硬布线控制器_1_alu_src , \单周期硬布线控制器_1_auipc , \单周期硬布线控制器_1_beq ,
       \单周期硬布线控制器_1_blt , \单周期硬布线控制器_1_bne , \单周期硬布线控制器_1_jal , \单周期硬布线控制器_1_jalr , \单周期硬布线控制器_1_lhu ,
       \单周期硬布线控制器_1_lui , \单周期硬布线控制器_1_memtoreg , \单周期硬布线控制器_1_memwrite , \单周期硬布线控制器_1_regwrite ,
       \单周期硬布线控制器_1_s_type , \数据相关 ;
  wire [1:0] EX_R1C, EX_R2C, ID_R1C, ID_R2C;
  wire [3:0] ID_EX_aluopout, \单周期硬布线控制器_1_alu_op ;
  wire [4:0] EX_W_num, ID_funct, ID_R1_num, ID_R2_num, MEM_W_num, W_num;
  wire [11:0] shifter_1_out;
  wire [12:0] CNT_num;
  wire [15:0] adder_5_out, \LoadUse次数 , multiplexer_13_out, shifter_3_out, \分支成功数 , \总周期数 , \插入气泡数 ,
       \无条件分支数 , \条件分支成功数 ;
  wire [19:0] shifter_2_out;
  wire [31:0] adder_1_out, adder_2_out, adder_3_out, adder_7_out, adder_8_out, bit_extender_1_out,
       bit_extender_2_out, bit_extender_3_out, bit_extender_4_out, bit_extender_5_out, branchAddr, EX_IR,
       EX_MEM_imm_u_out, EX_R1, EX_R2, ID_EX_imm_i_out, ID_EX_imm_s_out, ID_EX_imm_u_out, ID_IR, IF_IR,
       IF_PC_4, imm32_B, imm32_J, jaddress, JumpAddr, MDout, MEM_IR, MEM_Result, MEM_WB_rmdataout,
       multiplexer_1_out, multiplexer_3_out, multiplexer_4_out, multiplexer_5_out, multiplexer_6_out,
       multiplexer_10_out, multiplexer_11_out, multiplexer_15_out, multiplexer_16_out, multiplexer_17_out,
       R1, R1out, R2, R2out, ram_1_data, Result, WB_imm32_U, WB_IR;

  Button \u_总复位  (.out(RST));
  Button _1 (.out(IR1));
  Button _2 (.out(IR2));
  Button _3 (.out(IR3));
  // Probe on \总周期数 
  // Probe on \总周期数 
  Button \u_继续运行  (.out(Go));
  LED #(.active("true")) led_1 (.in(W1));
  LED #(.active("true")) led_2 (.in(W2));
  LED #(.active("true")) led_3 (.in(W3));
  Hex_Digit_Display hex_digit_display_1 (.value(LedData[31:28]));  // open: dp
  // Probe on IF_PC[19:0]
  // RiscV_Probe riscv_probe_1: pin names not known; wires that end beside it: IF_IR
  Hex_Digit_Display hex_digit_display_2 (.value(LedData[23:20]));  // open: dp
  Hex_Digit_Display hex_digit_display_3 (.value(LedData[27:24]));  // open: dp
  // Probe on ID_PC[19:0]
  // RiscV_Probe riscv_probe_2: pin names not known; wires that end beside it: {ID_IR[31], ID_funct[4], ID_IR[29:26], ID_funct[3], ID_IR[24:15], ID_funct[2:0], ID_IR[11:0]}
  Hex_Digit_Display hex_digit_display_4 (.value(LedData[19:16]));  // open: dp
  Hex_Digit_Display hex_digit_display_5 (.value(LedData[15:12]));  // open: dp
  Adder #(.width(32)) adder_1 (.a(EX_PC), .b(32'h4), .out(adder_1_out));  // open: cin, cout
  Adder #(.width(32)) adder_2 (.a(imm32_J), .b(EX_PC), .out(adder_2_out));  // open: cin, cout
  Adder #(.width(32)) adder_3 (.a(imm32_B), .b(EX_PC), .out(adder_3_out));  // open: cin, cout
  Hex_Digit_Display hex_digit_display_6 (.value(LedData[11:8]));  // open: dp
  Hex_Digit_Display hex_digit_display_7 (.value(LedData[7:4]));  // open: dp
  // Probe on EX_PC[19:0]
  // RiscV_Probe riscv_probe_3: pin names not known; wires that end beside it: EX_IR
  Multiplexer #(.select(1), .width(32), .disabled("Z"), .enable("false")) multiplexer_1 (
    .in0(IF_PC_4), .in1(adder_2_out), .out(multiplexer_1_out), .sel(jal));
  Hex_Digit_Display hex_digit_display_8 (.value(LedData[3:0]));  // open: dp
  or or_1 (or_1_out, branchTaken, jal);
  Multiplexer #(.select(1), .width(32), .disabled("Z"), .enable("false")) multiplexer_2 (
    .in0(multiplexer_1_out), .in1(adder_3_out), .out(branchAddr), .sel(branch));
  // Probe on \总周期数 
  // Probe on M_PC[19:0]
  // RiscV_Probe riscv_probe_4: pin names not known; wires that end beside it: MEM_IR
  or or_2 (or_2_out, branch, jal);
  Multiplexer #(.select(1), .width(32), .disabled("Z"), .enable("false")) multiplexer_3 (
    .in0(IF_PC_4), .in1(JumpAddr), .out(multiplexer_3_out), .sel(PredictJump));
  // Probe on \总周期数 
  // Probe on \无条件分支数 
  // Probe on \条件分支成功数 
  // Probe on \插入气泡数 
  // Probe on \LoadUse次数 
  or or_3 (or_3_out, branch, jal);
  and and_1 (and_1_out, or_3_out, ~EX_PredictErr);  // AND_Gate
  BTB2 BTB (
    .Clk(CLK), .EX_Branch(or_2_out), .PC(IF_PC), .EX_PC(EX_PC), .EX_BranchAddr(branchAddr),
    .EX_Branched(or_1_out), .JumpAddr(JumpAddr), .PredictJump(PredictJump));
  Multiplexer #(.select(1), .width(32), .disabled("Z"), .enable("false")) multiplexer_4 (
    .in0(adder_1_out), .in1(branchAddr), .out(multiplexer_4_out), .sel(or_1_out));
  // Probe on IF_PC[11:0]
  // Probe on WB_PC[19:0]
  // RiscV_Probe riscv_probe_5: pin names not known; wires that end beside it: WB_IR
  Counter #(.width(16), .max('hffff), .ongoal("wrap"), .trigger("rising"), .behavior("new")) counter_1 (
    .count(and_1_out), .Q(\分支成功数 ), .clk(CLK), .clr(RST));  // open: load, D, carry, preset, down
  Multiplexer #(.select(1), .width(32), .disabled("Z"), .enable("false")) multiplexer_5 (
    .in0(multiplexer_3_out), .in1(multiplexer_4_out), .out(multiplexer_5_out), .sel(EX_PredictErr));
  // Probe on ID_PC[11:0]
  // Probe on EX_PC[11:0]
  // Probe on \分支成功数 
  Multiplexer #(.select(1), .width(32), .disabled("Z"), .enable("false")) multiplexer_6 (
    .in0(multiplexer_5_out), .in1(jaddress), .out(multiplexer_6_out), .sel(jalr));
  and and_2 (and_2_out, not_1_out, not_2_out);
  not not_1 (not_1_out, LoadUse);
  not not_2 (not_2_out, halt);
  // Probe on M_PC[11:0]
  D_Flip_Flop #(.trigger("high"), .Pre_Clr_Positions("LEGACY"), .NegatePresetClear("false"), .enable("true"), .NewFFLayout("false")) d_ff_1 (.Q(d_ff_1_q));  // open: clk, D, Qn, preset, en, reset
  // Probe on 13'h97
  Register #(.width(32), .trigger("rising"), .Select("low")) PC (
    .D(multiplexer_6_out), .en(and_2_out), .Q(IF_PC), .clk(CLK), .clr(RST));
  // Probe on WB_PC[11:0]
  Comparator #(.width(13), .mode("twosComplement")) comparator_1 (
    .a(CNT_num), .b(13'h97), .eq(comparator_1_eq), .lt(comparator_1_lt));  // open: gt
  Clock #(.highDuration(1), .lowDuration(1)) clock_1 (.out(clock_1_out));
  or or_4 (or_4_out, branchTaken, jal, jalr);
  Comparator #(.width(1), .mode("twosComplement")) comparator_2 (
    .a(or_4_out), .b(EX_PredictJump), .eq(comparator_2_eq));  // open: gt, lt
  nand nand_1 (nand_1_out, d_ff_1_q, comparator_1_eq);
  Counter #(.width(13), .max('h1fff), .ongoal("stay"), .trigger("rising"), .behavior("old")) counter_2 (
    .count(comparator_1_lt), .Q(CNT_num), .clk(clock_1_out));  // open: load, D, carry, clr, preset
  Adder #(.width(32)) adder_4 (.a(IF_PC), .b(32'h4), .out(IF_PC_4));  // open: cin, cout
  not not_3 (EX_PredictErr, comparator_2_eq);
  assign CLK = nand_1_out ? clock_1_out : 1'bz;  // Controlled_Buffer controlled_buffer_1
  ROM #(.addrWidth(10), .dataWidth(32), .Select("high")) rom_1 (.addr(IF_PC[11:2]), .data(IF_IR));
  or or_5 (or_5_out, RST, EX_PredictErr);
  Pull_Resistor #(.pull(1)) pull_resistor_1 (.node(CLK));
  IF_ID IF_ID (
    .PCin(IF_PC), .IRin(IF_IR), .PCout(ID_PC),
    .IRout({ID_IR[31], ID_funct[4], ID_IR[29:26], ID_funct[3], ID_IR[24:15], ID_funct[2:0], ID_IR[11:0]}),
    .RST(or_5_out), .clk(CLK), .EN(and_3_out), .PridictJumpin(PredictJump),
    .PridictJumpout(IF_ID_pridictjumpout));
  and and_3 (and_3_out, en, not_4_out);
  not not_4 (not_4_out, LoadUse);
  // RiscV_Probe riscv_probe_6: pin names not known; wires that end beside it: {ID_IR[31], ID_funct[4], ID_IR[29:26], ID_funct[3], ID_IR[24:15], ID_funct[2:0], ID_IR[11:0]}
  assign bit_extender_1_out = {{20{ID_IR[31]}}, {ID_IR[31], ID_funct[4], ID_IR[29:26], ID_funct[3], ID_IR[24:20]}};  // Bit_Extender bit_extender_1
  assign bit_extender_2_out = {{20{ID_IR[31]}}, {ID_IR[31], ID_funct[4], ID_IR[29:26], ID_funct[3], ID_IR[11:7]}};  // Bit_Extender bit_extender_2
  \单周期硬布线控制器  \u_单周期硬布线控制器_1  (
    .Funct(ID_funct), .OP(ID_IR[6:2]), .ALU_OP(\单周期硬布线控制器_1_alu_op ), .MemToReg(\单周期硬布线控制器_1_memtoreg ),
    .MemWrite(\单周期硬布线控制器_1_memwrite ), .ALU_SRC(\单周期硬布线控制器_1_alu_src ), .RegWrite(\单周期硬布线控制器_1_regwrite ),
    .ecall(ID_ecall), .S_type(\单周期硬布线控制器_1_s_type ), .Jalr(\单周期硬布线控制器_1_jalr ), .Beq(\单周期硬布线控制器_1_beq ),
    .JAL(\单周期硬布线控制器_1_jal ), .Bne(\单周期硬布线控制器_1_bne ), .in_3(ID_IR[21]), .auipc(\单周期硬布线控制器_1_auipc ),
    .lui(\单周期硬布线控制器_1_lui ), .lhu(\单周期硬布线控制器_1_lhu ), .blt(\单周期硬布线控制器_1_blt ));  // open: uret, CSRRCI, CSRRSI
  Multiplexer #(.select(1), .width(5), .disabled("Z"), .enable("false")) multiplexer_7 (
    .in0(ID_IR[19:15]), .in1(5'b10001), .out(ID_R1_num), .sel(ID_ecall));
  Multiplexer #(.select(1), .width(5), .disabled("Z"), .enable("false")) multiplexer_8 (
    .in0(ID_IR[24:20]), .in1(5'b01010), .out(ID_R2_num), .sel(ID_ecall));
  Shifter #(.width(12), .shift("ll")) shifter_1 (
    .in({ID_IR[31], ID_IR[7], ID_funct[4], ID_IR[29:26], ID_funct[3], ID_IR[11:8]}), .\dist (4'b0001),
    .out(shifter_1_out));
  assign bit_extender_3_out = {{20{shifter_1_out[11]}}, shifter_1_out};  // Bit_Extender bit_extender_3
  assign bit_extender_4_out = {{12{shifter_2_out[19]}}, shifter_2_out};  // Bit_Extender bit_extender_4
  Shifter #(.width(20), .shift("ll")) shifter_2 (
    .in({ID_IR[31], ID_IR[19:15], ID_funct[2:0], ID_IR[20], ID_funct[4], ID_IR[29:26], ID_funct[3], ID_IR[24:21]}),
    .\dist (5'b00001), .out(shifter_2_out));
  not not_5 (not_5_out, CLK);
  Regifile regifile_1 (
    .Din(RDin), .Clk(not_5_out), .R1(R1), .R2(R2), .WE(RegWrite), .W_num(W_num), .R1_num(ID_R1_num),
    .R2_num(ID_R2_num));
  \数据相关_重定向流水线  \u_数据相关_重定向流水线_1  (
    .ID_R1_num(ID_R1_num), .EX_W_num(EX_W_num), .EX_RegWrite(EX_RegWrite), .ID_R2_num(ID_R2_num),
    .MEM_W_num(MEM_W_num), .MEM_RegWrite(MEM_RegWrite), .ID_OP(ID_IR[6:2]), .EX_OP(EX_IR[6:2]),
    .ID_Funct(ID_funct), .R1C(ID_R1C), .R2C(ID_R2C), .\数据相关 (\数据相关 ), .Load_Use(LoadUse));
  or or_6 (or_6_out, LoadUse, or_5_out);
  ID_EX ID_EX (
    .PCin(ID_PC), .Lhuin(\单周期硬布线控制器_1_lhu ), .Jalrin(\单周期硬布线控制器_1_jalr ),
    .IRin({ID_IR[31], ID_funct[4], ID_IR[29:26], ID_funct[3], ID_IR[24:15], ID_funct[2:0], ID_IR[11:0]}),
    .Jalin(\单周期硬布线控制器_1_jal ), .Beqin(\单周期硬布线控制器_1_beq ), .Imm_I_in(bit_extender_1_out),
    .Bltin(\单周期硬布线控制器_1_blt ), .Imm_S_in(bit_extender_2_out), .Bnein(\单周期硬布线控制器_1_bne ),
    .Imm_B_in(bit_extender_3_out), .MemToRegin(\单周期硬布线控制器_1_memtoreg ), .MemWritein(\单周期硬布线控制器_1_memwrite ),
    .Imm_J_in(bit_extender_4_out), .AluOpin(\单周期硬布线控制器_1_alu_op ),
    .Imm_U_in({ID_IR[31], ID_funct[4], ID_IR[29:26], ID_funct[3], ID_IR[24:15], ID_funct[2:0], {12{1'b0}}}),
    .AluSrcBin(\单周期硬布线控制器_1_alu_src ), .R1in(R1), .RegWritein(\单周期硬布线控制器_1_regwrite ), .R2in(R2),
    .S_Typein(\单周期硬布线控制器_1_s_type ), .haltin(ID_ecall), .W_in(ID_IR[11:7]), .PCout(EX_PC),
    .Lhuout(ID_EX_lhuout), .Jalrout(jalr), .IRout(EX_IR), .Jalout(jal), .Beqout(beq),
    .Imm_I_out(ID_EX_imm_i_out), .Bltout(blt), .Imm_S_out(ID_EX_imm_s_out), .Bneout(bne),
    .Imm_B_out(imm32_B), .MemToRegout(ID_EX_memtoregout), .MemWriteout(ID_EX_memwriteout),
    .Imm_J_out(imm32_J), .AluOpout(ID_EX_aluopout), .Imm_U_out(ID_EX_imm_u_out),
    .AluSrcBout(ID_EX_alusrcbout), .R1out(R1out), .RegWriteout(EX_RegWrite), .R2out(R2out),
    .S_Tpyeout(ID_EX_s_tpyeout), .haltout(EX_ecall), .W_out(EX_W_num), .RST(or_6_out), .EN_H(en), .CLK(CLK),
    .Luiin(\单周期硬布线控制器_1_lui ), .Luiout(ID_EX_luiout), .auipcin(\单周期硬布线控制器_1_auipc ),
    .auipcout(ID_EX_auipcout), .R1CHOICEin(ID_R1C), .R1CHOICEout(EX_R1C), .R2CHOICEin(ID_R2C),
    .R2CHOICEout(EX_R2C), .PridictJumpin(IF_ID_pridictjumpout), .PridictJumpout(EX_PredictJump));
  or or_7 (or_7_out, jal, jalr);
  Multiplexer #(.select(2), .width(32), .disabled("Z"), .enable("false")) multiplexer_9 (
    .in0(R2out), .in1(RDin), .in2({MEM_Result[31:2], Choicein, MEM_Result[0]}), .out(EX_R2), .sel(EX_R2C));  // open: in3
  Multiplexer #(.select(1), .width(32), .disabled("Z"), .enable("false")) multiplexer_10 (
    .in0(ID_EX_imm_i_out), .in1(ID_EX_imm_s_out), .out(multiplexer_10_out), .sel(ID_EX_s_tpyeout));
  Multiplexer #(.select(1), .width(32), .disabled("Z"), .enable("false")) multiplexer_11 (
    .in0(EX_R2), .in1(multiplexer_10_out), .out(multiplexer_11_out), .sel(ID_EX_alusrcbout));
  Counter #(.width(16), .max('hffff), .ongoal("wrap"), .trigger("rising"), .behavior("new")) counter_3 (
    .count(branch), .Q(\条件分支成功数 ), .clk(CLK), .clr(RST));  // open: load, D, carry, preset, down
  Comparator #(.width(32), .mode("twosComplement")) comparator_3 (
    .a(EX_R1), .b(32'h22), .eq(comparator_3_eq));  // open: gt, lt
  not not_6 (not_6_out, comparator_3_eq);
  Multiplexer #(.select(2), .width(32), .disabled("Z"), .enable("false")) multiplexer_12 (
    .in0(R1out), .in1(RDin), .in2({MEM_Result[31:2], Choicein, MEM_Result[0]}), .out(EX_R1), .sel(EX_R1C));  // open: in3
  ALU alu_1 (
    .X(EX_R1), .Y(multiplexer_11_out), .AluOP(ID_EX_aluopout), .Equal(equal), .Result(jaddress), .out_6(less));  // open: Result_2, out_4
  and and_4 (and_4_out, EX_ecall, comparator_3_eq);
  and and_5 (and_5_out, not_6_out, EX_ecall);
  or or_8 (or_8_out, jal, jalr);
  and and_6 (and_6_out, blt, less);
  and and_7 (and_7_out, beq, equal);
  not not_7 (not_7_out, equal);
  and and_8 (and_8_out, not_7_out, bne);
  Register #(.width(32), .trigger("rising"), .Select("low")) register_1 (
    .D(EX_R2), .en(and_4_out), .Q(LedData), .clk(CLK), .clr(RST));
  Counter #(.width(16), .max('hffff), .ongoal("wrap"), .trigger("rising"), .behavior("new")) counter_4 (
    .count(or_8_out), .Q(\无条件分支数 ), .clk(CLK), .clr(RST));  // open: load, D, carry, preset, down
  or or_9 (branch, blt, beq, bne);
  or or_10 (branchTaken, and_6_out, and_7_out, and_8_out);
  not not_8 (not_8_out, halt);
  Counter #(.width(16), .max('hffff), .ongoal("wrap"), .trigger("rising"), .behavior("new")) counter_5 (
    .count(not_8_out), .Q(\总周期数 ), .clk(CLK), .clr(RST));  // open: load, D, carry, preset, down
  EX_MEM EX_MEM (
    .MemToRegin(ID_EX_memtoregout), .PCin(EX_PC), .MemWritein(ID_EX_memwriteout), .IRin(EX_IR),
    .Jumpin(or_7_out), .RegWritein(EX_RegWrite), .Resultin(jaddress), .Haltin(and_5_out), .MDatain(EX_R2),
    .W_in(EX_W_num), .MemToRegout(EX_MEM_memtoregout), .PCout(M_PC), .MemWriteout(MemWrite), .IRout(MEM_IR),
    .Jumpout(EX_MEM_jumpout), .RegWriteout(MEM_RegWrite),
    .Resultout({MEM_Result[31:2], Choicein, MEM_Result[0]}), .Haltout(EX_MEM_haltout), .Mdataout(MDin),
    .W_out(MEM_W_num), .RST(RST), .EN_H(en), .CLK(CLK), .auipcin(ID_EX_auipcout), .auipcout(EX_MEM_auipcout),
    .Luiin(ID_EX_luiout), .Luiout(EX_MEM_luiout), .Lhuin(ID_EX_lhuout), .Lhuout(EX_MEM_lhuout),
    .Imm_U_in(ID_EX_imm_u_out), .Imm_U_out(EX_MEM_imm_u_out));
  Adder #(.width(16)) adder_5 (.a(\条件分支成功数 ), .b(\无条件分支数 ), .out(adder_5_out));  // open: cin, cout
  not not_9 (not_9_out, halt);
  and and_9 (and_9_out, not_9_out, LoadUse);
  RAM #(.addrWidth(10), .dataWidth(32), .bus("separate"), .Select("high")) ram_1 (
    .addr(MEM_Result[11:2]), .din(MDin), .data(ram_1_data), .str(MemWrite), .clk(CLK),
    .ld(EX_MEM_memtoregout), .clr(RST));  // open: sel
  Shifter #(.width(16), .shift("ll")) shifter_3 (.in(adder_5_out), .\dist (4'b0001), .out(shifter_3_out));
  Counter #(.width(16), .max('hffff), .ongoal("wrap"), .trigger("rising"), .behavior("new")) counter_6 (
    .count(and_9_out), .Q(\LoadUse次数 ), .clk(CLK), .clr(RST));  // open: load, D, carry, preset, down
  Adder #(.width(16)) adder_6 (.a(shifter_3_out), .b(\LoadUse次数 ), .out(\插入气泡数 ));  // open: cin, cout
  MEM_WB MEM_WB (
    .PCin(M_PC), .MemToRegin(EX_MEM_memtoregout), .IRin(MEM_IR), .Jumpin(EX_MEM_jumpout),
    .RegWritein(MEM_RegWrite), .Resultin({MEM_Result[31:2], Choicein, MEM_Result[0]}),
    .Haltin(EX_MEM_haltout), .RMDatain(ram_1_data), .W_in(MEM_W_num), .PCout(WB_PC), .MemToRegout(MemToReg),
    .IRout(WB_IR), .Jumpout(Jump), .RegWriteout(RegWrite), .Resultout(Result), .Haltout(MEM_WB_haltout),
    .RMdataout(MEM_WB_rmdataout), .W_out(W_num), .RST(RST), .EN_H(en), .CLK(CLK), .auipcin(EX_MEM_auipcout),
    .auipcout(auipc), .Luiin(EX_MEM_luiout), .Luiout(lui), .Imm_U_in(EX_MEM_imm_u_out),
    .Imm_U_out(WB_imm32_U), .lhuin(EX_MEM_lhuout), .lhuout(lhuout), .choicein(Choicein),
    .choiceout(MEM_WB_choiceout));
  Multiplexer #(.select(1), .width(16), .disabled("Z"), .enable("false")) multiplexer_13 (
    .in0(MEM_WB_rmdataout[15:0]), .in1(MEM_WB_rmdataout[31:16]), .out(multiplexer_13_out),
    .sel(MEM_WB_choiceout));
  assign bit_extender_5_out = {{16{1'b0}}, multiplexer_13_out};  // Bit_Extender bit_extender_5
  Multiplexer #(.select(1), .width(32), .disabled("Z"), .enable("false")) multiplexer_14 (
    .in0(MEM_WB_rmdataout), .in1(bit_extender_5_out), .out(MDout), .sel(lhuout));
  and and_10 (halt, MEM_WB_haltout, ~Go);  // AND_Gate
  not not_10 (en, halt);
  Multiplexer #(.select(1), .width(32), .disabled("Z"), .enable("false")) multiplexer_15 (
    .in0(Result), .in1(MDout), .out(multiplexer_15_out), .sel(MemToReg));
  Adder #(.width(32)) adder_7 (.a(WB_PC), .b(32'h4), .out(adder_7_out));  // open: cin, cout
  Multiplexer #(.select(1), .width(32), .disabled("Z"), .enable("false")) multiplexer_16 (
    .in0(multiplexer_15_out), .in1(adder_7_out), .out(multiplexer_16_out), .sel(Jump));
  Adder #(.width(32)) adder_8 (.a(WB_imm32_U), .b(WB_PC), .out(adder_8_out));  // open: cin, cout
  Multiplexer #(.select(1), .width(32), .disabled("Z"), .enable("false")) multiplexer_17 (
    .in0(WB_imm32_U), .in1(adder_8_out), .out(multiplexer_17_out), .sel(auipc));
  or or_11 (or_11_out, auipc, lui);
  Multiplexer #(.select(1), .width(32), .disabled("Z"), .enable("false")) multiplexer_18 (
    .in0(multiplexer_16_out), .in1(multiplexer_17_out), .out(RDin), .sel(or_11_out));

  // Other names for the same wires on the sheet: ID_IR (some bits) = ID_funct; ID_OP[4:0] = ID_IR[6:2];
  //   MEM_PC[31:0] = M_PC; MEM_Result[1] = Choicein; WriteBackData[31:0] = RDin

  // Notes on the sheet:
  //   中断源
  //   时空图监测，可删除
  //   中断等待指示
  //   数码管输出
  //   控制位
  //   流水调试日志用
  //   暂停节拍，不能为0
  //   戳工具置1进入计数暂停模式，ctrl+k时钟自动运行到对应节拍暂停
  //   ctrl+k关闭时钟连续运行，将控制位置零，进入单步调试模式调试
  //   指令存储器
  //   可计数暂停的时钟源
  //   contents of rom_1 (hex, n*v repeats v):
  //   100493 100006f 100493 200913 300993 100006f 100493 200913 300993 100006f 100493 200913 300993
  //   100006f 100493 200913 300993 29c000ef 100413 100493 1f49493 900533 2200893 73 24d493 48463 fedff06f
  //   900533 2200893 73 100493 249493 900533 2200893 73 48463 fedff06f 100493 1f49493 900533 2200893 73
  //   4034d493 900533 2200893 73 4044d493 900533 2200893 73 4044d493 900533 2200893 73 4044d493 900533
  //   2200893 73 4044d493 900533 2200893 73 4044d493 900533 2200893 73 4044d493 900533 2200893 73 4044d493
  //   900533 2200893 73 100413 1f41993 41f9d993 433 c00913 300b13 140413 f47413 800293 100313 499993
  //   89e9b3 1300533 2200893 73 406282b3 fe0294e3 140413 f00f93 1f47433 1c41413 800293 100313 49d993
  //   89e9b3 1300533 2200893 73 406282b3 fe0294e3 1c45413 406b0b33 b0463 f95ff06f 2b3 fff2c293 829293
  //   ff2e293 500533 2200893 73 fff00413 493 84a023 140413 448493 84a023 140413 448493 84a023 140413
  //   448493 84a023 140413 448493 84a023 140413 448493 84a023 140413 448493 84a023 140413 448493 84a023
  //   140413 448493 84a023 140413 448493 84a023 140413 448493 84a023 140413 448493 84a023 140413 448493
  //   84a023 140413 448493 84a023 140413 448493 84a023 140413 448493 84a023 140413 448493 140413 433
  //   3c00493 42983 4aa03 149a2b3 28663 134a023 1442023 ffc48493 fe9412e3 800533 2200893 73 440413 3c00493
  //   fc9416e3 a00893 73 413 140413 800533 2200893 73 240413 800533 2200893 73 340413 800533 2200893 73
  //   440413 800533 2200893 73 540413 800533 2200893 73 640413 800533 2200893 73 740413 800533 2200893 73
  //   840413 800533 2200893 2200893 73 8067
  //   指令字ID.IR
  //   rs1
  //   rs2
  //   rd
  //   为方便自动评测，需要输出流水线各段保存的PC值，注意是PC不是PC+4，另外ID段寄存器写入信息，Mem段内存写入信息也要输出
  //   Beq
  //   Bne
  //   MemToReg
  //   MemWrite
  //   AluOP
  //   AluSrcB
  //   RegWrite
  //   转换为字偏移量,所以需要逻辑左移一位
  //   数据存储器
endmodule

// BTB
module BTB (
  input  CLK,
  input  EX_Branch,
  input  [31:0] EX_PC,
  input  [31:0] EX_BranchAddr,
  input  [31:0] PC,
  input  EX_BranchTaken,
  output PredictJump,
  output [31:0] JumpAddr,
  output IF_Hit,
  output EX_Hit
);

  wire and_1_out, comparator_1_eq, comparator_2_eq, comparator_3_eq, comparator_4_eq, comparator_5_eq,
       comparator_6_eq, comparator_7_eq, comparator_8_eq, comparator_9_eq, comparator_10_eq,
       comparator_11_eq, comparator_12_eq, comparator_13_eq, comparator_14_eq, comparator_15_eq,
       comparator_16_eq, EX_Miss, EX_Write0, EX_Write1, EX_Write2, EX_Write3, EX_Write4, EX_Write5,
       EX_Write6, EX_Write7, L0, L1, L2, L3, L4, L5, L6, L7, Miss, not_1_out, not_2_out, not_3_out,
       not_4_out, not_5_out, not_6_out, not_7_out, not_8_out, priority_encoder_1_en_out, V0, V1, V2, V3, V4,
       V5, V6, V7, Write0, Write1, Write2, Write3, Write4, Write5, Write6, Write7;
  wire [0:0] controlled_buffer_9_out, controlled_buffer_10_out, controlled_buffer_11_out,
       controlled_buffer_12_out, controlled_buffer_13_out, controlled_buffer_14_out,
       controlled_buffer_15_out, controlled_buffer_16_out;
  wire [1:0] adder_1_out, JumpState, multiplexer_2_out, multiplexer_3_out, multiplexer_4_out,
       multiplexer_5_out, multiplexer_6_out, \分支预测历史位_2_q , \分支预测历史位_3_q , \分支预测历史位_4_q , \分支预测历史位_5_q ,
       \分支预测历史位_6_q , \分支预测历史位_7_q , \分支预测历史位_8_q , \分支预测历史位_q ;
  wire [2:0] \max2_归并比较_1_max_num , \max2_归并比较_2_p6 , \max2_归并比较_3_p6 , \max2_归并比较_4_p6 ,
       \max2_归并比较_5_max_num , \max2_归并比较_6_max_num , \max2_归并比较_7_max_num , multiplexer_1_out,
       priority_encoder_1_out;
  wire [15:0] C2, C3, C4, C5, C6, C7;
  wire [31:0] C0, C1, \max2_归并比较_1_max , \max2_归并比较_2_p5 , \max2_归并比较_3_p5 , \max2_归并比较_4_p5 ,
       \max2_归并比较_5_max , \max2_归并比较_6_max , Tag0, Tag1, Tag2, Tag3, Tag4, Tag5, Tag6, Tag7, \分支目标地址_2_q ,
       \分支目标地址_3_q , \分支目标地址_4_q , \分支目标地址_5_q , \分支目标地址_6_q , \分支目标地址_7_q , \分支目标地址_8_q , \分支目标地址_q ;

  Register #(.width(1), .trigger("rising"), .Select("low")) Valid (
    .D(1'b1), .en(Write0), .Q(V0), .clk(CLK));  // open: clr
  Register #(.width(1), .trigger("rising"), .Select("low")) Valid_2 (
    .D(1'b1), .en(Write1), .Q(V1), .clk(CLK));  // open: clr
  Register #(.width(1), .trigger("rising"), .Select("low")) Valid_3 (
    .D(1'b1), .en(Write2), .Q(V2), .clk(CLK));  // open: clr
  Register #(.width(1), .trigger("rising"), .Select("low")) Valid_4 (
    .D(1'b1), .en(Write3), .Q(V3), .clk(CLK));  // open: clr
  Register #(.width(1), .trigger("rising"), .Select("low")) Valid_5 (
    .D(1'b1), .en(Write4), .Q(V4), .clk(CLK));  // open: clr
  Register #(.width(1), .trigger("rising"), .Select("low")) Valid_6 (
    .D(1'b1), .en(Write5), .Q(V5), .clk(CLK));  // open: clr
  Register #(.width(1), .trigger("rising"), .Select("low")) Valid_7 (
    .D(1'b1), .en(Write6), .Q(V6), .clk(CLK));  // open: clr
  Register #(.width(1), .trigger("rising"), .Select("low")) Valid_8 (
    .D(1'b1), .en(Write7), .Q(V7), .clk(CLK));  // open: clr
  \Max2_归并比较  \max2_归并比较_1  (
    .Y(C0), .X(C1), .Y_num(3'b000), .X_num(3'b001), .MAX(\max2_归并比较_1_max ), .MAX_num(\max2_归并比较_1_max_num ));
  // Max2_归并比较 max2_归并比较_2: pin names not known; wires that end beside it: C2, 3'b010, C3, 3'b011, \max2_归并比较_2_p5 , \max2_归并比较_2_p6 
  // Max2_归并比较 max2_归并比较_3: pin names not known; wires that end beside it: C4, 3'b100, C5, 3'b101, \max2_归并比较_3_p5 , \max2_归并比较_3_p6 
  // Max2_归并比较 max2_归并比较_4: pin names not known; wires that end beside it: C6, 3'b110, C7, 3'b111, \max2_归并比较_4_p5 , \max2_归并比较_4_p6 
  Register #(.width(32), .trigger("rising"), .Select("low")) \u_分支指令地址  (
    .D(EX_PC), .en(Write0), .Q(Tag0), .clk(CLK));  // open: clr
  Register #(.width(32), .trigger("rising"), .Select("low")) \u_分支指令地址_2  (
    .D(EX_PC), .en(Write1), .Q(Tag1), .clk(CLK));  // open: clr
  Register #(.width(32), .trigger("rising"), .Select("low")) \u_分支指令地址_3  (
    .D(EX_PC), .en(Write2), .Q(Tag2), .clk(CLK));  // open: clr
  Register #(.width(32), .trigger("rising"), .Select("low")) \u_分支指令地址_4  (
    .D(EX_PC), .en(Write3), .Q(Tag3), .clk(CLK));  // open: clr
  Register #(.width(32), .trigger("rising"), .Select("low")) \u_分支指令地址_5  (
    .D(EX_PC), .en(Write4), .Q(Tag4), .clk(CLK));  // open: clr
  Register #(.width(32), .trigger("rising"), .Select("low")) \u_分支指令地址_6  (
    .D(EX_PC), .en(Write5), .Q(Tag5), .clk(CLK));  // open: clr
  Register #(.width(32), .trigger("rising"), .Select("low")) \u_分支指令地址_7  (
    .D(EX_PC), .en(Write6), .Q(Tag6), .clk(CLK));  // open: clr
  Register #(.width(32), .trigger("rising"), .Select("low")) \u_分支指令地址_8  (
    .D(EX_PC), .en(Write7), .Q(Tag7), .clk(CLK));  // open: clr
  not not_1 (not_1_out, V0);
  not not_2 (not_2_out, V1);
  not not_3 (not_3_out, V2);
  not not_4 (not_4_out, V3);
  not not_5 (not_5_out, V4);
  not not_6 (not_6_out, V5);
  not not_7 (not_7_out, V6);
  not not_8 (not_8_out, V7);
  \Max2_归并比较  \max2_归并比较_5  (
    .Y(\max2_归并比较_1_max ), .X(\max2_归并比较_2_p5 ), .Y_num(\max2_归并比较_1_max_num ), .X_num(\max2_归并比较_2_p6 ),
    .MAX(\max2_归并比较_5_max ), .MAX_num(\max2_归并比较_5_max_num ));
  \Max2_归并比较  \max2_归并比较_6  (
    .Y(\max2_归并比较_3_p5 ), .X(\max2_归并比较_4_p5 ), .Y_num(\max2_归并比较_3_p6 ), .X_num(\max2_归并比较_4_p6 ),
    .MAX(\max2_归并比较_6_max ), .MAX_num(\max2_归并比较_6_max_num ));
  Priority_Encoder #(.select(3), .disabled("Z")) priority_encoder_1 (
    .in0(not_1_out), .in1(not_2_out), .in2(not_3_out), .in3(not_4_out), .in4(not_5_out), .in5(not_6_out),
    .in6(not_7_out), .in7(not_8_out), .out(priority_encoder_1_out), .en_out(priority_encoder_1_en_out));  // open: gs, en_in
  \Max2_归并比较  \max2_归并比较_7  (
    .Y(\max2_归并比较_5_max ), .X(\max2_归并比较_6_max ), .Y_num(\max2_归并比较_5_max_num ),
    .X_num(\max2_归并比较_6_max_num ), .MAX_num(\max2_归并比较_7_max_num ));  // open: MAX
  Multiplexer #(.select(1), .width(3), .disabled("Z"), .enable("false")) multiplexer_1 (
    .in0(priority_encoder_1_out), .in1(\max2_归并比较_7_max_num ), .out(multiplexer_1_out),
    .sel(priority_encoder_1_en_out));
  assign JumpAddr = L0 ? \分支目标地址_q  : 32'bz;  // Controlled_Buffer controlled_buffer_1
  Register #(.width(32), .trigger("rising"), .Select("low")) \u_分支目标地址  (
    .D(EX_BranchAddr), .en(Write0), .Q(\分支目标地址_q ), .clk(CLK));  // open: clr
  Register #(.width(32), .trigger("rising"), .Select("low")) \u_分支目标地址_2  (
    .D(EX_BranchAddr), .en(Write1), .Q(\分支目标地址_2_q ), .clk(CLK));  // open: clr
  assign JumpAddr = L1 ? \分支目标地址_2_q  : 32'bz;  // Controlled_Buffer controlled_buffer_2
  assign JumpAddr = L2 ? \分支目标地址_3_q  : 32'bz;  // Controlled_Buffer controlled_buffer_3
  Register #(.width(32), .trigger("rising"), .Select("low")) \u_分支目标地址_3  (
    .D(EX_BranchAddr), .en(Write2), .Q(\分支目标地址_3_q ), .clk(CLK));  // open: clr
  Register #(.width(32), .trigger("rising"), .Select("low")) \u_分支目标地址_4  (
    .D(EX_BranchAddr), .en(Write3), .Q(\分支目标地址_4_q ), .clk(CLK));  // open: clr
  assign JumpAddr = L3 ? \分支目标地址_4_q  : 32'bz;  // Controlled_Buffer controlled_buffer_4
  Register #(.width(32), .trigger("rising"), .Select("low")) \u_分支目标地址_5  (
    .D(EX_BranchAddr), .en(Write4), .Q(\分支目标地址_5_q ), .clk(CLK));  // open: clr
  assign JumpAddr = L4 ? \分支目标地址_5_q  : 32'bz;  // Controlled_Buffer controlled_buffer_5
  Register #(.width(32), .trigger("rising"), .Select("low")) \u_分支目标地址_6  (
    .D(EX_BranchAddr), .en(Write5), .Q(\分支目标地址_6_q ), .clk(CLK));  // open: clr
  assign JumpAddr = L5 ? \分支目标地址_6_q  : 32'bz;  // Controlled_Buffer controlled_buffer_6
  assign JumpAddr = L6 ? \分支目标地址_7_q  : 32'bz;  // Controlled_Buffer controlled_buffer_7
  Register #(.width(32), .trigger("rising"), .Select("low")) \u_分支目标地址_7  (
    .D(EX_BranchAddr), .en(Write6), .Q(\分支目标地址_7_q ), .clk(CLK));  // open: clr
  Register #(.width(32), .trigger("rising"), .Select("low")) \u_分支目标地址_8  (
    .D(EX_BranchAddr), .en(Write7), .Q(\分支目标地址_8_q ), .clk(CLK));  // open: clr
  assign JumpAddr = L7 ? \分支目标地址_8_q  : 32'bz;  // Controlled_Buffer controlled_buffer_8
  and and_1 (and_1_out, EX_Branch, EX_Miss);
  Demultiplexer #(.select(3), .width(1), .tristate("false"), .disabled("Z"), .enable("false")) demultiplexer_1 (
    .out0(Write0), .out1(Write1), .out2(Write2), .out3(Write3), .out4(Write4), .out5(Write5), .out6(Write6),
    .out7(Write7), .in(and_1_out), .sel(multiplexer_1_out));
  Register #(.width(2), .trigger("rising"), .Select("low")) \u_分支预测历史位  (
    .D(JumpState), .en(Write0), .Q(\分支预测历史位_q ), .clk(CLK));  // open: clr
  assign {PredictJump, controlled_buffer_9_out[0]} = L0 ? \分支预测历史位_q  : 2'bz;  // Controlled_Buffer controlled_buffer_9
  assign {PredictJump, controlled_buffer_10_out[0]} = L1 ? \分支预测历史位_2_q  : 2'bz;  // Controlled_Buffer controlled_buffer_10
  Register #(.width(2), .trigger("rising"), .Select("low")) \u_分支预测历史位_2  (
    .D(JumpState), .en(Write1), .Q(\分支预测历史位_2_q ), .clk(CLK));  // open: clr
  assign {PredictJump, controlled_buffer_11_out[0]} = L2 ? \分支预测历史位_3_q  : 2'bz;  // Controlled_Buffer controlled_buffer_11
  Register #(.width(2), .trigger("rising"), .Select("low")) \u_分支预测历史位_3  (
    .D(JumpState), .en(Write2), .Q(\分支预测历史位_3_q ), .clk(CLK));  // open: clr
  assign {PredictJump, controlled_buffer_12_out[0]} = L3 ? \分支预测历史位_4_q  : 2'bz;  // Controlled_Buffer controlled_buffer_12
  Register #(.width(2), .trigger("rising"), .Select("low")) \u_分支预测历史位_4  (
    .D(JumpState), .en(Write3), .Q(\分支预测历史位_4_q ), .clk(CLK));  // open: clr
  Register #(.width(2), .trigger("rising"), .Select("low")) \u_分支预测历史位_5  (
    .D(JumpState), .en(Write4), .Q(\分支预测历史位_5_q ), .clk(CLK));  // open: clr
  assign {PredictJump, controlled_buffer_13_out[0]} = L4 ? \分支预测历史位_5_q  : 2'bz;  // Controlled_Buffer controlled_buffer_13
  Register #(.width(2), .trigger("rising"), .Select("low")) \u_分支预测历史位_6  (
    .D(JumpState), .en(Write5), .Q(\分支预测历史位_6_q ), .clk(CLK));  // open: clr
  assign {PredictJump, controlled_buffer_14_out[0]} = L5 ? \分支预测历史位_6_q  : 2'bz;  // Controlled_Buffer controlled_buffer_14
  Register #(.width(2), .trigger("rising"), .Select("low")) \u_分支预测历史位_7  (
    .D(JumpState), .en(Write6), .Q(\分支预测历史位_7_q ), .clk(CLK));  // open: clr
  assign {PredictJump, controlled_buffer_15_out[0]} = L6 ? \分支预测历史位_7_q  : 2'bz;  // Controlled_Buffer controlled_buffer_15
  assign {PredictJump, controlled_buffer_16_out[0]} = L7 ? \分支预测历史位_8_q  : 2'bz;  // Controlled_Buffer controlled_buffer_16
  Register #(.width(2), .trigger("rising"), .Select("low")) \u_分支预测历史位_8  (
    .D(JumpState), .en(Write7), .Q(\分支预测历史位_8_q ), .clk(CLK));  // open: clr
  Pull_Resistor #(.pull(0)) pull_resistor_1 (.node(PredictJump));
  Counter #(.width(16), .max('hffff), .ongoal("wrap"), .trigger("rising"), .behavior("new")) \u_淘汰置换记数器  (
    .Q(C0[15:0]), .clk(CLK), .clr(L0));  // open: load, D, count, carry, preset, down
  Counter #(.width(16), .max('hffff), .ongoal("wrap"), .trigger("rising"), .behavior("new")) \u_淘汰置换记数器_2  (
    .Q(C1[15:0]), .clk(CLK), .clr(L1));  // open: load, D, count, carry, preset, down
  Counter #(.width(16), .max('hffff), .ongoal("wrap"), .trigger("rising"), .behavior("new")) \u_淘汰置换记数器_3  (
    .Q(C2), .clk(CLK), .clr(L2));  // open: load, D, count, carry, preset, down
  Counter #(.width(16), .max('hffff), .ongoal("wrap"), .trigger("rising"), .behavior("new")) \u_淘汰置换记数器_4  (
    .Q(C3), .clk(CLK), .clr(L3));  // open: load, D, count, carry, preset, down
  Counter #(.width(16), .max('hffff), .ongoal("wrap"), .trigger("rising"), .behavior("new")) \u_淘汰置换记数器_5  (
    .Q(C4), .clk(CLK), .clr(L4));  // open: load, D, count, carry, preset, down
  Counter #(.width(16), .max('hffff), .ongoal("wrap"), .trigger("rising"), .behavior("new")) \u_淘汰置换记数器_6  (
    .Q(C5), .clk(CLK), .clr(L5));  // open: load, D, count, carry, preset, down
  Counter #(.width(16), .max('hffff), .ongoal("wrap"), .trigger("rising"), .behavior("new")) \u_淘汰置换记数器_7  (
    .Q(C6), .clk(CLK), .clr(L6));  // open: load, D, count, carry, preset, down
  Counter #(.width(16), .max('hffff), .ongoal("wrap"), .trigger("rising"), .behavior("new")) \u_淘汰置换记数器_8  (
    .Q(C7), .clk(CLK), .clr(L7));  // open: load, D, count, carry, preset, down
  Multiplexer #(.select(1), .width(2), .disabled("Z"), .enable("false")) multiplexer_2 (
    .in0(2'b00), .in1(2'b01), .out(multiplexer_2_out), .sel(EX_BranchTaken));
  Multiplexer #(.select(1), .width(2), .disabled("Z"), .enable("false")) multiplexer_3 (
    .in0(2'b11), .in1(2'b01), .out(multiplexer_3_out), .sel(EX_BranchTaken));
  Multiplexer #(.select(1), .width(2), .disabled("Z"), .enable("false")) multiplexer_4 (
    .in0(2'b01), .in1(2'b00), .out(multiplexer_4_out), .sel(EX_BranchTaken));
  Multiplexer #(.select(1), .width(2), .disabled("Z"), .enable("false")) multiplexer_5 (
    .in0(2'b01), .in1(2'b11), .out(multiplexer_5_out), .sel(EX_BranchTaken));
  Multiplexer #(.select(2), .width(2), .disabled("Z"), .enable("false")) multiplexer_6 (
    .in0(multiplexer_2_out), .in1(multiplexer_3_out), .in2(multiplexer_4_out), .in3(multiplexer_5_out),
    .out(multiplexer_6_out), .sel(JumpState));
  Adder #(.width(2)) adder_1 (.a(multiplexer_6_out), .b(JumpState), .out(adder_1_out));  // open: cin, cout
  Register #(.width(2), .trigger("rising"), .Select("low")) \u_双位预测状态_2位  (
    .D(adder_1_out), .en(EX_Branch), .Q(JumpState), .clk(CLK));  // open: clr
  Comparator #(.width(32), .mode("unsigned")) comparator_1 (.a(PC), .b(Tag0), .eq(comparator_1_eq));  // open: gt, lt
  Comparator #(.width(32), .mode("unsigned")) comparator_2 (.a(PC), .b(Tag1), .eq(comparator_2_eq));  // open: gt, lt
  Comparator #(.width(32), .mode("unsigned")) comparator_3 (.a(PC), .b(Tag2), .eq(comparator_3_eq));  // open: gt, lt
  Comparator #(.width(32), .mode("unsigned")) comparator_4 (.a(PC), .b(Tag3), .eq(comparator_4_eq));  // open: gt, lt
  Comparator #(.width(32), .mode("unsigned")) comparator_5 (.a(PC), .b(Tag4), .eq(comparator_5_eq));  // open: gt, lt
  Comparator #(.width(32), .mode("unsigned")) comparator_6 (.a(PC), .b(Tag5), .eq(comparator_6_eq));  // open: gt, lt
  Comparator #(.width(32), .mode("unsigned")) comparator_7 (.a(PC), .b(Tag6), .eq(comparator_7_eq));  // open: gt, lt
  Comparator #(.width(32), .mode("unsigned")) comparator_8 (.a(PC), .b(Tag7), .eq(comparator_8_eq));  // open: gt, lt
  Comparator #(.width(32), .mode("unsigned")) comparator_9 (.a(EX_PC), .b(Tag0), .eq(comparator_9_eq));  // open: gt, lt
  Comparator #(.width(32), .mode("unsigned")) comparator_10 (
    .a(EX_PC), .b(Tag1), .eq(comparator_10_eq));  // open: gt, lt
  Comparator #(.width(32), .mode("unsigned")) comparator_11 (
    .a(EX_PC), .b(Tag2), .eq(comparator_11_eq));  // open: gt, lt
  Comparator #(.width(32), .mode("unsigned")) comparator_12 (
    .a(EX_PC), .b(Tag3), .eq(comparator_12_eq));  // open: gt, lt
  Comparator #(.width(32), .mode("unsigned")) comparator_13 (
    .a(EX_PC), .b(Tag4), .eq(comparator_13_eq));  // open: gt, lt
  Comparator #(.width(32), .mode("unsigned")) comparator_14 (
    .a(EX_PC), .b(Tag5), .eq(comparator_14_eq));  // open: gt, lt
  Comparator #(.width(32), .mode("unsigned")) comparator_15 (
    .a(EX_PC), .b(Tag6), .eq(comparator_15_eq));  // open: gt, lt
  Comparator #(.width(32), .mode("unsigned")) comparator_16 (
    .a(EX_PC), .b(Tag7), .eq(comparator_16_eq));  // open: gt, lt
  and and_2 (L0, comparator_1_eq, V0);
  and and_3 (L1, comparator_2_eq, V1);
  and and_4 (L2, comparator_3_eq, V2);
  and and_5 (L3, comparator_4_eq, V3);
  and and_6 (L4, comparator_5_eq, V4);
  and and_7 (L5, comparator_6_eq, V5);
  and and_8 (L6, comparator_7_eq, V6);
  and and_9 (L7, comparator_8_eq, V7);
  and and_10 (EX_Write0, comparator_9_eq, V0);
  and and_11 (EX_Write1, comparator_10_eq, V1);
  and and_12 (EX_Write2, comparator_11_eq, V2);
  and and_13 (EX_Write3, comparator_12_eq, V3);
  and and_14 (EX_Write4, comparator_13_eq, V4);
  and and_15 (EX_Write5, comparator_14_eq, V5);
  and and_16 (EX_Write6, comparator_15_eq, V6);
  and and_17 (EX_Write7, comparator_16_eq, V7);
  or or_1 (IF_Hit, L0, L1, L2, L3, L4, L5, L6, L7);
  or or_2 (EX_Hit, EX_Write0, EX_Write1, EX_Write2, EX_Write3, EX_Write4, EX_Write5, EX_Write6, EX_Write7);
  not not_9 (Miss, IF_Hit);
  not not_10 (EX_Miss, EX_Hit);
  // Pins of 16 and 32 bits meet at C0
  // Pins of 16 and 32 bits meet at C1

  // Other names for the same wires on the sheet: Hit = IF_Hit

  // Notes on the sheet:
  //   Cache
  //   找出置换标记最大的行Cache替换
  //   双位预测状态转换图
endmodule

module \Max2_归并比较  (
  input  [31:0] Y,
  input  [31:0] X,
  input  [2:0] Y_num,
  input  [2:0] X_num,
  output [31:0] MAX,
  output [2:0] MAX_num
);

  wire comparator_1_eq, comparator_1_gt, or_1_out;

  Multiplexer #(.select(1), .width(32), .disabled("Z"), .enable("true")) multiplexer_1 (
    .in0(Y), .in1(X), .out(MAX), .sel(or_1_out), .en(1'b1));
  Comparator #(.width(32), .mode("unsigned")) comparator_1 (
    .a(X), .b(Y), .gt(comparator_1_gt), .eq(comparator_1_eq));  // open: lt
  or or_1 (or_1_out, comparator_1_gt, comparator_1_eq);
  Multiplexer #(.select(1), .width(3), .disabled("Z"), .enable("false")) multiplexer_2 (
    .in0(Y_num), .in1(X_num), .out(MAX_num), .sel(or_1_out));

  // Notes on the sheet:
  //   输出两个输入中的较大值，并输出较大值的2位编号
endmodule

// BTB
module BTB2 (
  input  Clk,
  input  EX_Branch,
  input  [31:0] PC,
  input  [31:0] EX_PC,
  input  [31:0] EX_BranchAddr,
  input  EX_Branched,
  output [31:0] JumpAddr,
  output PredictJump
);

  wire A0, A1, A2, A3, A4, A5, A6, A7, and_1_out, comparator_1_eq, comparator_2_eq, comparator_3_eq,
       comparator_4_eq, comparator_5_eq, comparator_6_eq, comparator_7_eq, comparator_8_eq, comparator_9_eq,
       comparator_10_eq, comparator_11_eq, comparator_12_eq, comparator_13_eq, comparator_14_eq,
       comparator_15_eq, comparator_16_eq, decoder_1_out0, decoder_1_out1, decoder_1_out2, decoder_1_out3,
       decoder_1_out4, decoder_1_out5, decoder_1_out6, decoder_1_out7, decoder_2_out0, decoder_2_out1,
       decoder_2_out2, decoder_2_out3, decoder_2_out4, decoder_2_out5, decoder_2_out6, decoder_2_out7,
       EX_Hit, EX_Miss, IF_Hit, IF_Miss, L0, L1, L2, L3, L4, L5, L6, L7, M0, M1, M2, M3, M4, M5, M6, M7,
       not_1_out, not_2_out, not_3_out, not_4_out, not_5_out, not_6_out, not_7_out, not_8_out, or_1_out,
       or_2_out, or_3_out, or_4_out, or_5_out, or_6_out, or_7_out, or_8_out, or_9_out, or_10_out, or_11_out,
       or_12_out, or_13_out, or_14_out, or_17_out, or_18_out, priority_encoder_1_gs, V0, V1, V2, V3, V4, V5,
       V6, V7, WriteL0, WriteL1, WriteL2, WriteL3, WriteL4, WriteL5, WriteL6, WriteL7;
  wire [0:0] controlled_buffer_1_out, controlled_buffer_2_out, controlled_buffer_3_out,
       controlled_buffer_4_out, controlled_buffer_5_out, controlled_buffer_6_out, controlled_buffer_7_out,
       controlled_buffer_8_out;
  wire [1:0] Predict0, Predict1, Predict2, Predict3, Predict4, Predict5, Predict6, Predict7;
  wire [2:0] \max2_归并比较_1_max_num , \max2_归并比较_2_max_num , \max2_归并比较_3_max_num , \max2_归并比较_4_max_num ,
       \max2_归并比较_5_max_num , \max2_归并比较_6_max_num , \max2_归并比较_7_max_num , priority_encoder_1_out;
  wire [31:0] C0, C1, C2, C3, C4, C5, C6, C7, \max2_归并比较_1_max , \max2_归并比较_2_max , \max2_归并比较_3_max ,
       \max2_归并比较_4_max , \max2_归并比较_5_max , \max2_归并比较_6_max , Tag0, Tag1, Tag2, Tag3, Tag4, Tag5, Tag6,
       Tag7, \分支目标地址_2_q , \分支目标地址_3_q , \分支目标地址_4_q , \分支目标地址_5_q , \分支目标地址_6_q , \分支目标地址_7_q ,
       \分支目标地址_8_q , \分支目标地址_q ;

  Pull_Resistor #(.pull(0)) pull_resistor_1 (.node(PredictJump));
  assign {PredictJump, controlled_buffer_1_out[0]} = L0 ? Predict0 : 2'bz;  // Controlled_Buffer controlled_buffer_1
  assign {PredictJump, controlled_buffer_2_out[0]} = L1 ? Predict1 : 2'bz;  // Controlled_Buffer controlled_buffer_2
  assign {PredictJump, controlled_buffer_3_out[0]} = L2 ? Predict2 : 2'bz;  // Controlled_Buffer controlled_buffer_3
  assign {PredictJump, controlled_buffer_4_out[0]} = L3 ? Predict3 : 2'bz;  // Controlled_Buffer controlled_buffer_4
  assign {PredictJump, controlled_buffer_5_out[0]} = L4 ? Predict4 : 2'bz;  // Controlled_Buffer controlled_buffer_5
  assign {PredictJump, controlled_buffer_6_out[0]} = L5 ? Predict5 : 2'bz;  // Controlled_Buffer controlled_buffer_6
  assign {PredictJump, controlled_buffer_7_out[0]} = L6 ? Predict6 : 2'bz;  // Controlled_Buffer controlled_buffer_7
  assign {PredictJump, controlled_buffer_8_out[0]} = L7 ? Predict7 : 2'bz;  // Controlled_Buffer controlled_buffer_8
  Register #(.width(1), .trigger("rising"), .Select("low")) VALID (
    .D(1'b1), .en(WriteL0), .Q(V0), .clk(Clk));  // open: clr
  Register #(.width(1), .trigger("rising"), .Select("low")) VALID_2 (
    .D(1'b1), .en(WriteL1), .Q(V1), .clk(Clk));  // open: clr
  Register #(.width(1), .trigger("rising"), .Select("low")) VALID_3 (
    .D(1'b1), .en(WriteL2), .Q(V2), .clk(Clk));  // open: clr
  Register #(.width(1), .trigger("rising"), .Select("low")) VALID_4 (
    .D(1'b1), .en(WriteL3), .Q(V3), .clk(Clk));  // open: clr
  Register #(.width(1), .trigger("rising"), .Select("low")) VALID_5 (
    .D(1'b1), .en(WriteL4), .Q(V4), .clk(Clk));  // open: clr
  Register #(.width(1), .trigger("rising"), .Select("low")) VALID_6 (
    .D(1'b1), .en(WriteL5), .Q(V5), .clk(Clk));  // open: clr
  Register #(.width(1), .trigger("rising"), .Select("low")) VALID_7 (
    .D(1'b1), .en(WriteL6), .Q(V6), .clk(Clk));  // open: clr
  Register #(.width(1), .trigger("rising"), .Select("low")) VALID_8 (
    .D(1'b1), .en(WriteL7), .Q(V7), .clk(Clk));  // open: clr
  not not_1 (not_1_out, V0);
  not not_2 (not_2_out, V1);
  not not_3 (not_3_out, V2);
  not not_4 (not_4_out, V3);
  not not_5 (not_5_out, V4);
  not not_6 (not_6_out, V5);
  not not_7 (not_7_out, V6);
  not not_8 (not_8_out, V7);
  \Max2_归并比较  \max2_归并比较_1  (
    .Y(C0), .X(C1), .Y_num(3'b000), .X_num(3'b001), .MAX(\max2_归并比较_1_max ), .MAX_num(\max2_归并比较_1_max_num ));
  \Max2_归并比较  \max2_归并比较_2  (
    .Y(C2), .X(C3), .Y_num(3'b010), .X_num(3'b011), .MAX(\max2_归并比较_2_max ), .MAX_num(\max2_归并比较_2_max_num ));
  \Max2_归并比较  \max2_归并比较_3  (
    .Y(C4), .X(C5), .Y_num(3'b100), .X_num(3'b101), .MAX(\max2_归并比较_3_max ), .MAX_num(\max2_归并比较_3_max_num ));
  \Max2_归并比较  \max2_归并比较_4  (
    .Y(C6), .X(C7), .Y_num(3'b110), .X_num(3'b111), .MAX(\max2_归并比较_4_max ), .MAX_num(\max2_归并比较_4_max_num ));
  and and_1 (and_1_out, V0, V1, V2, V3, V4, V5, V6, V7);
  Register #(.width(32), .trigger("rising"), .Select("low")) \u_分支指令地址  (
    .D(EX_PC), .en(WriteL0), .Q(Tag0), .clk(Clk));  // open: clr
  Register #(.width(32), .trigger("rising"), .Select("low")) \u_分支指令地址_2  (
    .D(EX_PC), .en(WriteL1), .Q(Tag1), .clk(Clk));  // open: clr
  Register #(.width(32), .trigger("rising"), .Select("low")) \u_分支指令地址_3  (
    .D(EX_PC), .en(WriteL2), .Q(Tag2), .clk(Clk));  // open: clr
  Register #(.width(32), .trigger("rising"), .Select("low")) \u_分支指令地址_4  (
    .D(EX_PC), .en(WriteL3), .Q(Tag3), .clk(Clk));  // open: clr
  Register #(.width(32), .trigger("rising"), .Select("low")) \u_分支指令地址_5  (
    .D(EX_PC), .en(WriteL4), .Q(Tag4), .clk(Clk));  // open: clr
  Register #(.width(32), .trigger("rising"), .Select("low")) \u_分支指令地址_6  (
    .D(EX_PC), .en(WriteL5), .Q(Tag5), .clk(Clk));  // open: clr
  Register #(.width(32), .trigger("rising"), .Select("low")) \u_分支指令地址_7  (
    .D(EX_PC), .en(WriteL6), .Q(Tag6), .clk(Clk));  // open: clr
  Register #(.width(32), .trigger("rising"), .Select("low")) \u_分支指令地址_8  (
    .D(EX_PC), .en(WriteL7), .Q(Tag7), .clk(Clk));  // open: clr
  Priority_Encoder #(.select(3), .disabled("Z")) priority_encoder_1 (
    .in0(not_1_out), .in1(not_2_out), .in2(not_3_out), .in3(not_4_out), .in4(not_5_out), .in5(not_6_out),
    .in6(not_7_out), .in7(not_8_out), .out(priority_encoder_1_out), .gs(priority_encoder_1_gs));  // open: en_out, en_in
  \Max2_归并比较  \max2_归并比较_5  (
    .Y(\max2_归并比较_1_max ), .X(\max2_归并比较_2_max ), .Y_num(\max2_归并比较_1_max_num ),
    .X_num(\max2_归并比较_2_max_num ), .MAX(\max2_归并比较_5_max ), .MAX_num(\max2_归并比较_5_max_num ));
  \Max2_归并比较  \max2_归并比较_6  (
    .Y(\max2_归并比较_3_max ), .X(\max2_归并比较_4_max ), .Y_num(\max2_归并比较_3_max_num ),
    .X_num(\max2_归并比较_4_max_num ), .MAX(\max2_归并比较_6_max ), .MAX_num(\max2_归并比较_6_max_num ));
  or or_1 (or_1_out, L1, L2, L3, L4, L5, L6, L7, WriteL1, WriteL2, WriteL3, WriteL4, WriteL5, WriteL6, WriteL7);
  or or_2 (or_2_out, L0, L1, L2, L3, L5, L6, L7, WriteL0, WriteL1, WriteL2, WriteL3, WriteL5, WriteL6, WriteL7);
  Decoder #(.select(3), .tristate("false"), .disabled(0), .enable("true")) decoder_1 (
    .out0(decoder_1_out0), .out1(decoder_1_out1), .out2(decoder_1_out2), .out3(decoder_1_out3),
    .out4(decoder_1_out4), .out5(decoder_1_out5), .out6(decoder_1_out6), .out7(decoder_1_out7),
    .sel(priority_encoder_1_out), .en(priority_encoder_1_gs));
  Decoder #(.select(3), .tristate("false"), .disabled(0), .enable("true")) decoder_2 (
    .out0(decoder_2_out0), .out1(decoder_2_out1), .out2(decoder_2_out2), .out3(decoder_2_out3),
    .out4(decoder_2_out4), .out5(decoder_2_out5), .out6(decoder_2_out6), .out7(decoder_2_out7),
    .sel(\max2_归并比较_7_max_num ), .en(and_1_out));
  \Max2_归并比较  \max2_归并比较_7  (
    .Y(\max2_归并比较_5_max ), .X(\max2_归并比较_6_max ), .Y_num(\max2_归并比较_5_max_num ),
    .X_num(\max2_归并比较_6_max_num ), .MAX_num(\max2_归并比较_7_max_num ));  // open: MAX
  and and_2 (A0, or_1_out, V0);
  and and_3 (A4, or_2_out, V4);
  Counter #(.width(32), .max('hffffffff), .ongoal("wrap"), .trigger("rising"), .behavior("old")) \u_置换标记  (
    .count(A0), .Q(C0), .clk(Clk), .clr(L0));  // open: load, D, carry, preset
  Counter #(.width(32), .max('hffffffff), .ongoal("wrap"), .trigger("rising"), .behavior("old")) \u_置换标记_2  (
    .count(A1), .Q(C1), .clk(Clk), .clr(L1));  // open: load, D, carry, preset
  Counter #(.width(32), .max('hffffffff), .ongoal("wrap"), .trigger("rising"), .behavior("old")) \u_置换标记_3  (
    .count(A2), .Q(C2), .clk(Clk), .clr(L2));  // open: load, D, carry, preset
  Counter #(.width(32), .max('hffffffff), .ongoal("wrap"), .trigger("rising"), .behavior("old")) \u_置换标记_4  (
    .count(A3), .Q(C3), .clk(Clk), .clr(L3));  // open: load, D, carry, preset
  Counter #(.width(32), .max('hffffffff), .ongoal("wrap"), .trigger("rising"), .behavior("old")) \u_置换标记_5  (
    .count(A4), .Q(C4), .clk(Clk), .clr(L4));  // open: load, D, carry, preset
  Counter #(.width(32), .max('hffffffff), .ongoal("wrap"), .trigger("rising"), .behavior("old")) \u_置换标记_6  (
    .count(A5), .Q(C5), .clk(Clk), .clr(L5));  // open: load, D, carry, preset
  Counter #(.width(32), .max('hffffffff), .ongoal("wrap"), .trigger("rising"), .behavior("old")) \u_置换标记_7  (
    .count(A6), .Q(C6), .clk(Clk), .clr(L6));  // open: load, D, carry, preset
  Counter #(.width(32), .max('hffffffff), .ongoal("wrap"), .trigger("rising"), .behavior("old")) \u_置换标记_8  (
    .count(A7), .Q(C7), .clk(Clk), .clr(L7));  // open: load, D, carry, preset
  \分支预测状态机  \u_分支预测状态机_1  (.Branched(EX_Branched), .predict(Predict1), .En(M1), .clk(Clk));
  \分支预测状态机  \u_分支预测状态机_2  (.Branched(EX_Branched), .predict(Predict5), .En(M5), .clk(Clk));
  Register #(.width(32), .trigger("rising"), .Select("low")) \u_分支目标地址  (
    .D(EX_BranchAddr), .en(WriteL0), .Q(\分支目标地址_q ), .clk(Clk));  // open: clr
  Register #(.width(32), .trigger("rising"), .Select("low")) \u_分支目标地址_2  (
    .D(EX_BranchAddr), .en(WriteL1), .Q(\分支目标地址_2_q ), .clk(Clk));  // open: clr
  Register #(.width(32), .trigger("rising"), .Select("low")) \u_分支目标地址_3  (
    .D(EX_BranchAddr), .en(WriteL2), .Q(\分支目标地址_3_q ), .clk(Clk));  // open: clr
  Register #(.width(32), .trigger("rising"), .Select("low")) \u_分支目标地址_4  (
    .D(EX_BranchAddr), .en(WriteL3), .Q(\分支目标地址_4_q ), .clk(Clk));  // open: clr
  Register #(.width(32), .trigger("rising"), .Select("low")) \u_分支目标地址_5  (
    .D(EX_BranchAddr), .en(WriteL4), .Q(\分支目标地址_5_q ), .clk(Clk));  // open: clr
  Register #(.width(32), .trigger("rising"), .Select("low")) \u_分支目标地址_6  (
    .D(EX_BranchAddr), .en(WriteL5), .Q(\分支目标地址_6_q ), .clk(Clk));  // open: clr
  Register #(.width(32), .trigger("rising"), .Select("low")) \u_分支目标地址_7  (
    .D(EX_BranchAddr), .en(WriteL6), .Q(\分支目标地址_7_q ), .clk(Clk));  // open: clr
  Register #(.width(32), .trigger("rising"), .Select("low")) \u_分支目标地址_8  (
    .D(EX_BranchAddr), .en(WriteL7), .Q(\分支目标地址_8_q ), .clk(Clk));  // open: clr
  or or_3 (or_3_out, decoder_1_out0, decoder_2_out0);
  or or_4 (or_4_out, decoder_1_out1, decoder_2_out1);
  or or_5 (or_5_out, decoder_1_out2, decoder_2_out2);
  or or_6 (or_6_out, decoder_1_out3, decoder_2_out3);
  or or_7 (or_7_out, decoder_1_out4, decoder_2_out4);
  or or_8 (or_8_out, decoder_1_out5, decoder_2_out5);
  or or_9 (or_9_out, decoder_1_out6, decoder_2_out6);
  or or_10 (or_10_out, decoder_1_out7, decoder_2_out7);
  or or_11 (or_11_out, L0, L2, L3, L4, L5, L6, L7, WriteL0, WriteL2, WriteL3, WriteL4, WriteL5, WriteL6, WriteL7);
  or or_12 (or_12_out, L0, L1, L2, L3, L4, L6, L7, WriteL0, WriteL1, WriteL2, WriteL3, WriteL4, WriteL6, WriteL7);
  \分支预测状态机  \u_分支预测状态机_3  (.Branched(EX_Branched), .predict(Predict2), .En(M2), .clk(Clk));
  \分支预测状态机  \u_分支预测状态机_4  (.Branched(EX_Branched), .predict(Predict6), .En(M6), .clk(Clk));
  assign JumpAddr = L0 ? \分支目标地址_q  : 32'bz;  // Controlled_Buffer controlled_buffer_9
  assign JumpAddr = L1 ? \分支目标地址_2_q  : 32'bz;  // Controlled_Buffer controlled_buffer_10
  assign JumpAddr = L2 ? \分支目标地址_3_q  : 32'bz;  // Controlled_Buffer controlled_buffer_11
  assign JumpAddr = L3 ? \分支目标地址_4_q  : 32'bz;  // Controlled_Buffer controlled_buffer_12
  assign JumpAddr = L4 ? \分支目标地址_5_q  : 32'bz;  // Controlled_Buffer controlled_buffer_13
  assign JumpAddr = L5 ? \分支目标地址_6_q  : 32'bz;  // Controlled_Buffer controlled_buffer_14
  assign JumpAddr = L6 ? \分支目标地址_7_q  : 32'bz;  // Controlled_Buffer controlled_buffer_15
  assign JumpAddr = L7 ? \分支目标地址_8_q  : 32'bz;  // Controlled_Buffer controlled_buffer_16
  and and_4 (WriteL0, or_3_out, EX_Miss, EX_Branch);
  and and_5 (WriteL1, or_4_out, EX_Miss, EX_Branch);
  and and_6 (WriteL2, or_5_out, EX_Miss, EX_Branch);
  and and_7 (WriteL3, or_6_out, EX_Miss, EX_Branch);
  and and_8 (WriteL4, or_7_out, EX_Miss, EX_Branch);
  and and_9 (WriteL5, or_8_out, EX_Miss, EX_Branch);
  and and_10 (WriteL6, or_9_out, EX_Miss, EX_Branch);
  and and_11 (WriteL7, or_10_out, EX_Miss, EX_Branch);
  and and_12 (A1, or_11_out, V1);
  and and_13 (A5, or_12_out, V5);
  Comparator #(.width(32), .mode("twosComplement")) comparator_1 (
    .a(PC), .b(Tag0), .eq(comparator_1_eq));  // open: gt, lt
  Comparator #(.width(32), .mode("twosComplement")) comparator_2 (
    .a(PC), .b(Tag1), .eq(comparator_2_eq));  // open: gt, lt
  Comparator #(.width(32), .mode("twosComplement")) comparator_3 (
    .a(PC), .b(Tag2), .eq(comparator_3_eq));  // open: gt, lt
  Comparator #(.width(32), .mode("twosComplement")) comparator_4 (
    .a(PC), .b(Tag3), .eq(comparator_4_eq));  // open: gt, lt
  Comparator #(.width(32), .mode("twosComplement")) comparator_5 (
    .a(PC), .b(Tag4), .eq(comparator_5_eq));  // open: gt, lt
  Comparator #(.width(32), .mode("twosComplement")) comparator_6 (
    .a(PC), .b(Tag5), .eq(comparator_6_eq));  // open: gt, lt
  Comparator #(.width(32), .mode("twosComplement")) comparator_7 (
    .a(PC), .b(Tag6), .eq(comparator_7_eq));  // open: gt, lt
  Comparator #(.width(32), .mode("twosComplement")) comparator_8 (
    .a(PC), .b(Tag7), .eq(comparator_8_eq));  // open: gt, lt
  Comparator #(.width(32), .mode("twosComplement")) comparator_9 (
    .a(EX_PC), .b(Tag0), .eq(comparator_9_eq));  // open: gt, lt
  Comparator #(.width(32), .mode("twosComplement")) comparator_10 (
    .a(EX_PC), .b(Tag1), .eq(comparator_10_eq));  // open: gt, lt
  Comparator #(.width(32), .mode("twosComplement")) comparator_11 (
    .a(EX_PC), .b(Tag2), .eq(comparator_11_eq));  // open: gt, lt
  Comparator #(.width(32), .mode("twosComplement")) comparator_12 (
    .a(EX_PC), .b(Tag3), .eq(comparator_12_eq));  // open: gt, lt
  Comparator #(.width(32), .mode("twosComplement")) comparator_13 (
    .a(EX_PC), .b(Tag4), .eq(comparator_13_eq));  // open: gt, lt
  Comparator #(.width(32), .mode("twosComplement")) comparator_14 (
    .a(EX_PC), .b(Tag5), .eq(comparator_14_eq));  // open: gt, lt
  Comparator #(.width(32), .mode("twosComplement")) comparator_15 (
    .a(EX_PC), .b(Tag6), .eq(comparator_15_eq));  // open: gt, lt
  Comparator #(.width(32), .mode("twosComplement")) comparator_16 (
    .a(EX_PC), .b(Tag7), .eq(comparator_16_eq));  // open: gt, lt
  or or_13 (or_13_out, L0, L1, L3, L4, L5, L6, L7, WriteL0, WriteL1, WriteL3, WriteL4, WriteL5, WriteL6, WriteL7);
  or or_14 (or_14_out, L0, L1, L2, L3, L4, L5, L7, WriteL0, WriteL1, WriteL2, WriteL3, WriteL4, WriteL5, WriteL7);
  \分支预测状态机  \u_分支预测状态机_5  (.Branched(EX_Branched), .predict(Predict3), .En(M3), .clk(Clk));
  \分支预测状态机  \u_分支预测状态机_6  (.Branched(EX_Branched), .predict(Predict7), .En(M7), .clk(Clk));
  and and_14 (L0, comparator_1_eq, V0);
  and and_15 (L1, comparator_2_eq, V1);
  and and_16 (L2, comparator_3_eq, V2);
  and and_17 (L3, comparator_4_eq, V3);
  and and_18 (L4, comparator_5_eq, V4);
  and and_19 (L5, comparator_6_eq, V5);
  and and_20 (L6, comparator_7_eq, V6);
  and and_21 (L7, comparator_8_eq, V7);
  and and_22 (M0, comparator_9_eq, V0);
  and and_23 (M1, comparator_10_eq, V1);
  and and_24 (M2, comparator_11_eq, V2);
  and and_25 (M3, comparator_12_eq, V3);
  and and_26 (M4, comparator_13_eq, V4);
  and and_27 (M5, comparator_14_eq, V5);
  and and_28 (M6, comparator_15_eq, V6);
  and and_29 (M7, comparator_16_eq, V7);
  and and_30 (A2, or_13_out, V2);
  and and_31 (A6, or_14_out, V6);
  or or_15 (IF_Hit, L0, L1, L2, L3, L4, L5, L6, L7);
  or or_16 (EX_Hit, M0, M1, M2, M3, M4, M5, M6, M7);
  \分支预测状态机  \u_分支预测状态机_7  (.Branched(EX_Branched), .predict(Predict4), .En(M4), .clk(Clk));
  \分支预测状态机  \u_分支预测状态机_8  (.Branched(EX_Branched), .predict(Predict0), .En(M0), .clk(Clk));
  not not_9 (IF_Miss, IF_Hit);
  not not_10 (EX_Miss, EX_Hit);
  or or_17 (or_17_out, L0, L1, L2, L4, L5, L6, L7, WriteL0, WriteL1, WriteL2, WriteL4, WriteL5, WriteL6, WriteL7);
  or or_18 (or_18_out, L0, L1, L2, L3, L4, L5, L6, WriteL0, WriteL1, WriteL2, WriteL3, WriteL4, WriteL5, WriteL6);
  and and_32 (A3, or_17_out, V3);
  and and_33 (A7, or_18_out, V7);

  // Other names for the same wires on the sheet: Tag[31:0] = EX_PC

  // Notes on the sheet:
  //   Cache槽
  //   查找逻辑
endmodule

module \分支预测状态机  (
  input  Branched,
  input  En,
  input  clk,
  output [1:0] predict
);

  wire [1:0] adder_1_out, multiplexer_1_out, multiplexer_2_out, multiplexer_3_out, multiplexer_4_out,
       multiplexer_5_out;

  Multiplexer #(.select(1), .width(2), .disabled("Z"), .enable("false")) multiplexer_1 (
    .in0(2'b00), .in1(2'b01), .out(multiplexer_1_out), .sel(Branched));
  Multiplexer #(.select(1), .width(2), .disabled("Z"), .enable("false")) multiplexer_2 (
    .in0(2'b11), .in1(2'b01), .out(multiplexer_2_out), .sel(Branched));
  Multiplexer #(.select(1), .width(2), .disabled("Z"), .enable("false")) multiplexer_3 (
    .in0(2'b01), .in1(2'b00), .out(multiplexer_3_out), .sel(Branched));
  Multiplexer #(.select(1), .width(2), .disabled("Z"), .enable("false")) multiplexer_4 (
    .in0(2'b01), .in1(2'b11), .out(multiplexer_4_out), .sel(Branched));
  Multiplexer #(.select(2), .width(2), .disabled("Z"), .enable("false")) multiplexer_5 (
    .in0(multiplexer_1_out), .in1(multiplexer_2_out), .in2(multiplexer_3_out), .in3(multiplexer_4_out),
    .out(multiplexer_5_out), .sel(predict));
  Adder #(.width(2)) adder_1 (.a(predict), .b(multiplexer_5_out), .out(adder_1_out));  // open: cin, cout
  Register #(.width(2), .trigger("rising"), .Select("low")) \u_分支预测历史位  (
    .D(adder_1_out), .en(En), .Q(predict), .clk(clk));  // open: clr

  // Other names for the same wires on the sheet: EX_Branched = Branched; M7 = En; Predict7[1:0] = predict
endmodule
